// Logisim project ACM1401_U201414697_朱谷才_alu.circ as structural Verilog: 8 circuits, main circuit ALU
module ALU (
  input  [31:0] X,
  input  [31:0] Y,
  input  [3:0] AluOP,
  output Signed_Overflow,
  output UnSigned_Overflow,
  output Equal,
  output [31:0] Result,
  output [31:0] Result_2
);

  wire A_S, and_3_out, and_4_out, CofADD, comparator_1_lt, comparator_2_lt, decoder_1_out5, or_3_out, Sub,
       xor_3_out;
  wire [31:0] ADD, AND, ARS, DIV, LLS, LPD, LRS, multiplexer_1_out, NOR, OR, REM, SCOM, UCOM, UPD, XOR, Yin;

  // Probe on X
  // Probe on X
  Shifter #(.width(32)) shifter_1 (.in(X), .\dist (Y[4:0]), .out(LLS));
  Shifter #(.width(32), .shift("ar")) shifter_2 (.in(X), .\dist (Y[4:0]), .out(ARS));
  Shifter #(.width(32), .shift("lr")) shifter_3 (.in(X), .\dist (Y[4:0]), .out(LRS));
  // Probe on Y
  // Probe on Y
  Multiplexer #(.width(32)) multiplexer_1 (
    .in0({32{1'b0}}), .in1({32{1'b1}}), .out(multiplexer_1_out), .sel(Sub), .en(1'b1));
  assign Yin = Y ^ multiplexer_1_out;  // XOR_Gate xor_1, 32 bits wide
  Multiplier #(.width(32)) multiplier_1 (.a(X), .b(Y), .out(LPD), .cin({32{1'b0}}), .cout(UPD));
  Divider #(.width(32)) divider_1 (.a(X), .b(Y), .out(DIV), .upper({32{1'b0}}), .rem(REM));
  assign AND = X & Y;  // AND_Gate and_1, 32 bits wide
  assign OR = X | Y;  // OR_Gate or_1, 32 bits wide
  assign XOR = X ^ Y;  // XOR_Gate xor_2, 32 bits wide
  assign NOR = ~(X | Y);  // NOR_Gate nor_1, 32 bits wide
  Comparator #(.width(32)) comparator_1 (.a(X), .b(Y), .lt(comparator_1_lt));  // open: gt, eq
  Comparator #(.width(32), .mode("unsigned")) comparator_2 (
    .a(X), .b(Y), .eq(Equal), .lt(comparator_2_lt));  // open: gt
  // Probe on AluOP
  _32BitParalAdder u_32bitparaladder_1 (.in_2(X), .in_3(Yin), .out(ADD), .in_1(Sub), .out_2(CofADD));
  assign SCOM = {{31{1'b0}}, comparator_1_lt};  // Bit_Extender bit_extender_1
  // Probe on Result
  // Probe on Result
  assign UCOM = {{31{1'b0}}, comparator_2_lt};  // Bit_Extender bit_extender_2
  xor xor_3 (xor_3_out, CofADD, Sub);
  and and_2 (UnSigned_Overflow, xor_3_out, A_S);
  // Probe on Result_2
  or or_2 (A_S, Sub, decoder_1_out5);
  Multiplexer #(.select(4), .width(32)) multiplexer_2 (
    .in0(LLS), .in1(ARS), .in2(LRS), .in3(LPD), .in4(DIV), .in5(ADD), .in6(ADD), .in7(AND), .in8(OR),
    .in9(XOR), .in10(NOR), .in11(SCOM), .in12(UCOM), .in13({32{1'b0}}), .in14({32{1'b0}}), .in15({32{1'b0}}),
    .out(Result), .sel(AluOP), .en(1'b1));
  Decoder #(.select(4)) decoder_1 (
    .out5(decoder_1_out5), .out6(Sub), .sel(AluOP), .en(1'b1));  // open: out0, out1, out2, out3, out4, out7, out8, out9, out10, out11, out12, out13, out14, out15
  Multiplexer #(.select(4), .width(32)) multiplexer_3 (
    .in0({32{1'b0}}), .in1({32{1'b0}}), .in2({32{1'b0}}), .in3(UPD), .in4(REM), .in5({32{1'b0}}),
    .in6({32{1'b0}}), .in7({32{1'b0}}), .in8({32{1'b0}}), .in9({32{1'b0}}), .in10({32{1'b0}}),
    .in11({32{1'b0}}), .in12({32{1'b0}}), .in13({32{1'b0}}), .in14({32{1'b0}}), .in15({32{1'b0}}),
    .out(Result_2), .sel(AluOP), .en(1'b1));
  and and_3 (and_3_out, X[31], ~ADD[31], Yin[31]);  // AND_Gate
  and and_4 (and_4_out, ~X[31], ADD[31], ~Yin[31]);  // AND_Gate
  or or_3 (or_3_out, and_3_out, and_4_out);
  and and_5 (Signed_Overflow, or_3_out, A_S);

  // Other names for the same wires on the sheet: OF = Signed_Overflow; Result2[31:0] = Result_2; S[3:0] = AluOP;
  //   UOF = UnSigned_Overflow

  // Notes on the sheet:
  //   不要改变此引脚区域内容，也不要改变ALU封装形式
  //   输入引脚
  //   请在下方利用上方输入输出引脚的隧道信号构建ALU电路，ctrl+d复制选择部件
  //   华中科技大学计算机学院 计算机组成原理，鸣谢加州大学伯克利CS61C课程
  //   输出引脚
  //   探测区域
endmodule

module \演示电路  (
  input  [31:0] X,
  input  [31:0] Y,
  input  [3:0] ALUOP,
  output Signed_Overflow,
  output Unsigned_overflow,
  output [31:0] Result,
  output [31:0] Result_2,
  output Equal
);

  // Probe on X
  // Probe on X
  ALU alu_1 (
    .AluOP(ALUOP), .X(X), .Equal(Equal), .Result(Result), .Signed_Overflow(Signed_Overflow), .Y(Y),
    .Result_2(Result_2), .UnSigned_Overflow(Unsigned_overflow));
  // Probe on ALUOP
  // Probe on Y
  // Probe on Y
  // Probe on Result
  // Probe on Result
  // Probe on Result_2

  // Notes on the sheet:
  //   ALu电路无需调整位置即可连接在该电路中，并且不能出现蓝色线缆和三态输出
endmodule

module \等差数列  (
  input  [31:0] \数列初始值 ,
  input  [31:0] \等差值 ,
  input  \时钟 ,
  output [31:0] Result
);

  // Probe on \数列初始值 
  // Probe on \数列初始值 
  // Probe on \等差值 
  // Probe on \等差值 
  // Probe on Result
  // Probe on Result

  // Other names for the same wires on the sheet: 数列初值[31:0] = \数列初始值 ; 累加和[31:0] = Result

  // Notes on the sheet:
  //   不要改变此引脚区域内容，也不要改变ALU封装形式
  //   请在下方利用上方输入输出引脚的隧道信号构建等差数列求和电路，ctrl+d复制选择部件
  //   华中科技大学计算机学院 计算机组成原理，鸣谢加州大学伯克利CS61C课程
  //   输出引脚
  //   探测区域
endmodule

module _74182 (
  input  in_1,
  input  in_2,
  input  in_3,
  input  in_4,
  input  in_5,
  input  in_6,
  input  P,
  input  in_8,
  input  P_2,
  output out_10,
  output out_11,
  output out_12,
  output out_13,
  output G4_star,
  output P4_star
);

  wire and_1_out, and_2_out, and_3_out, and_5_out, and_6_out, and_7_out, and_8_out, and_9_out, and_10_out,
       and_11_out;

  and and_1 (and_1_out, in_3, in_4);
  or or_1 (G4_star, in_2, and_1_out, and_2_out, and_3_out);
  and and_2 (and_2_out, in_3, in_5, in_6);
  and and_3 (and_3_out, in_3, in_5, P, in_8);
  or or_2 (out_10, in_2, and_1_out, and_2_out, and_3_out, and_5_out);
  and and_4 (P4_star, in_3, in_5, P, P_2);
  and and_5 (and_5_out, in_3, in_5, P, P_2, in_1);
  or or_3 (out_11, in_4, and_6_out, and_7_out, and_8_out);
  and and_6 (and_6_out, in_5, in_6);
  and and_7 (and_7_out, in_5, P, in_8);
  and and_8 (and_8_out, in_5, P, P_2, in_1);
  or or_4 (out_12, in_6, and_9_out, and_10_out);
  and and_9 (and_9_out, P, in_8);
  and and_10 (and_10_out, P, in_1, P_2);
  or or_5 (out_13, in_8, and_11_out);
  and and_11 (and_11_out, P_2, in_1);

  // Notes on the sheet:
  //   G
  //   4 ------>  1
  //   P
  //   G
  //   P
  //   G
  //   G
endmodule

module _4BitParalAdder (
  input  in_1,
  input  [3:0] in_2,
  input  [3:0] in_3,
  output out,
  output out_2,
  output out_3,
  output [3:0] out_4
);

  wire temp_1_out_9, temp_1_out_11, temp_1_out_13, temp_1_out_15;
  wire [3:0] P;
  wire [3:1] C;

  temp temp_1 (
    .out_9(temp_1_out_9), .out_10(P[3]), .out_11(temp_1_out_11), .out_12(P[2]), .out_13(temp_1_out_13),
    .out_14(P[1]), .out_15(temp_1_out_15), .out_16(P[0]), .in_1(in_2[3]), .in_2(in_3[3]), .in_3(in_2[2]),
    .in_4(in_3[2]), .in_5(in_2[1]), .in_6(in_3[1]), .in_7(in_2[0]), .in_8(in_3[0]));
  _74182 u_74182_1 (
    .in_1(in_1), .G4_star(out), .out_10(out_3), .P4_star(out_2), .out_11(C[3]), .out_12(C[2]), .out_13(C[1]),
    .in_2(temp_1_out_9), .in_3(P[3]), .in_4(temp_1_out_11), .in_5(P[2]), .in_6(temp_1_out_13), .P(P[1]),
    .in_8(temp_1_out_15), .P_2(P[0]));
  xor xor_1 (out_4[3], P[3], C[3]);
  xor xor_2 (out_4[2], P[2], C[2]);
  xor xor_3 (out_4[1], P[1], C[1]);
  xor xor_4 (out_4[0], P[0], in_1);

  // Other names for the same wires on the sheet: C[0] = in_1; F[3:0] = out_4; X[3:0] = in_2; Y[3:0] = in_3
endmodule

module _16BitParalAdder (
  input  in_1,
  input  [15:0] in_2,
  input  [15:0] in_3,
  output out,
  output out_2,
  output [15:0] out_3,
  output out_4
);

  wire n4bitparaladder_1_out, n4bitparaladder_1_out_2, n4bitparaladder_2_out, n4bitparaladder_2_out_2,
       n4bitparaladder_3_out, n4bitparaladder_3_out_2, n4bitparaladder_4_out, n4bitparaladder_4_out_2;
  wire [3:1] C;

  // Probe on in_2
  // Probe on in_3
  // Probe on out_3
  _4BitParalAdder u_4bitparaladder_1 (
    .in_2(in_2[15:12]), .in_3(in_3[15:12]), .in_1(C[3]), .out_4(out_3[15:12]), .out(n4bitparaladder_1_out),
    .out_2(n4bitparaladder_1_out_2));  // open: out_3
  _4BitParalAdder u_4bitparaladder_2 (
    .in_2(in_2[11:8]), .in_3(in_3[11:8]), .in_1(C[2]), .out_4(out_3[11:8]), .out(n4bitparaladder_2_out),
    .out_2(n4bitparaladder_2_out_2));  // open: out_3
  _74182 u_74182_1 (
    .in_1(in_1), .G4_star(out), .out_10(out_4), .P4_star(out_2), .out_11(C[3]), .out_12(C[2]), .out_13(C[1]),
    .in_2(n4bitparaladder_1_out), .in_3(n4bitparaladder_1_out_2), .in_4(n4bitparaladder_2_out),
    .in_5(n4bitparaladder_2_out_2), .in_6(n4bitparaladder_3_out), .P(n4bitparaladder_3_out_2),
    .in_8(n4bitparaladder_4_out), .P_2(n4bitparaladder_4_out_2));
  _4BitParalAdder u_4bitparaladder_3 (
    .in_2(in_2[7:4]), .in_3(in_3[7:4]), .in_1(C[1]), .out_4(out_3[7:4]), .out(n4bitparaladder_3_out),
    .out_2(n4bitparaladder_3_out_2));  // open: out_3
  _4BitParalAdder u_4bitparaladder_4 (
    .in_2(in_2[3:0]), .in_3(in_3[3:0]), .in_1(in_1), .out_4(out_3[3:0]), .out(n4bitparaladder_4_out),
    .out_2(n4bitparaladder_4_out_2));  // open: out_3

  // Other names for the same wires on the sheet: C[0] = in_1; F[15:0] = out_3; X[15:0] = in_2; Y[15:0] = in_3
endmodule

module temp (
  input  in_1,
  input  in_2,
  input  in_3,
  input  in_4,
  input  in_5,
  input  in_6,
  input  in_7,
  input  in_8,
  output out_9,
  output out_10,
  output out_11,
  output out_12,
  output out_13,
  output out_14,
  output out_15,
  output out_16
);

  and and_1 (out_9, in_1, in_2);
  xor xor_1 (out_10, in_1, in_2);
  and and_2 (out_11, in_3, in_4);
  xor xor_2 (out_12, in_3, in_4);
  and and_3 (out_13, in_5, in_6);
  xor xor_3 (out_14, in_5, in_6);
  and and_4 (out_15, in_7, in_8);
  xor xor_4 (out_16, in_7, in_8);
endmodule

module _32BitParalAdder (
  input  in_1,
  input  [31:0] in_2,
  input  [31:0] in_3,
  output [31:0] out,
  output out_2
);

  wire n16bitparaladder_1_out, n16bitparaladder_1_out_2, n16bitparaladder_2_out, n16bitparaladder_2_out_2,
       n74182_1_out_13;

  // Probe on out
  // Probe on in_2
  // Probe on in_3
  _16BitParalAdder u_16bitparaladder_1 (
    .out_3(out[31:16]), .out_4(out_2), .in_2(in_2[31:16]), .in_3(in_3[31:16]), .in_1(n74182_1_out_13),
    .out(n16bitparaladder_1_out), .out_2(n16bitparaladder_1_out_2));
  _74182 u_74182_1 (
    .in_1(in_1), .out_13(n74182_1_out_13), .in_2(1'b0), .in_3(1'b0), .in_4(1'b0), .in_5(1'b0),
    .in_6(n16bitparaladder_1_out), .P(n16bitparaladder_1_out_2), .in_8(n16bitparaladder_2_out),
    .P_2(n16bitparaladder_2_out_2));  // open: G4_star, out_10, P4_star, out_11, out_12
  _16BitParalAdder u_16bitparaladder_2 (
    .out_3(out[15:0]), .in_2(in_2[15:0]), .in_3(in_3[15:0]), .in_1(in_1), .out(n16bitparaladder_2_out),
    .out_2(n16bitparaladder_2_out_2));  // open: out_4

  // Other names for the same wires on the sheet: F[31:0] = out; X[31:0] = in_2; Y[31:0] = in_3
endmodule
