// Logisim project ACM1401_U201414697_朱谷才_cpu.circ as structural Verilog: 9 circuits, main circuit main
module main (
);

  wire ALUSrc, and_1_out, and_2_out, and_3_out, beq, bne, Branch, clk, clkin, d_ff_1_q, Equal, Halt, I, J,
       Jal, Jr, Jump, MemRead, MemtoReg, MemWrite, R, RegDst, RegWrite, Shift, syscall, Unsigned;
  wire [3:0] ALUOp;
  wire [4:0] multiplexer_2_out, multiplexer_3_out, rd, rs, rt;
  wire [27:0] adder_1_out;
  wire [31:0] adder_2_out, adder_3_out, alures, bit_extender_1_out, bit_extender_2_out, bit_extender_3_out,
       cnt, counter_4_q, Icnt, Jcnt, main_1_p10, main_1_p11, multiplexer_6_out, multiplexer_8_out,
       multiplexer_9_out, multiplexer_11_out, multiplexer_12_out, multiplexer_14_out, multiplexer_15_out,
       multiplexer_16_out, PC_q, ra, ram_2_data, Rcnt, s0, s1, shifter_1_out, x, y;
  wire [31:2] ram_1_data_2;
  wire [31:26] ram_1_data;

  Clock clock_1 (.out(clkin));
  Adder #(.width(32)) adder_1 (.a(32'h4), .b(PC_q), .out({ram_1_data_2[31:28], adder_1_out}));  // open: cin, cout
  Register #(.width(32)) PC (.D(multiplexer_16_out), .Q(PC_q), .clk(clk));  // open: en, clr
  Multiplexer #(.enable("false")) multiplexer_1 (.in0(clkin), .in1(1'b0), .out(clk), .sel(Halt));
  Counter #(.width(32), .max('hffffffff)) u_R (.count(J), .Q(Jcnt), .clk(clk));  // open: load, D, carry, clr
  Counter #(.width(32), .max('hffffffff)) counter_1 (.count(R), .Q(Rcnt), .clk(clk));  // open: load, D, carry, clr
  RAM #(.addrWidth(10), .dataWidth(32)) ram_1 (
    .addr(PC_q[11:2]), .data({ram_1_data, ram_1_data_2[27:2]}), .ld(1'b1));  // open: sel, clk, clr
  Adder #(.width(32)) adder_2 (.a(32'h4), .b(PC_q), .out(adder_2_out));  // open: cin, cout
  Counter #(.width(32), .max('hffffffff)) counter_2 (.count(I), .Q(Icnt), .clk(clk));  // open: load, D, carry, clr
  and and_1 (and_1_out, syscall, Equal);
  Multiplexer #(.width(5), .enable("false")) multiplexer_2 (
    .in0(ram_1_data_2[22:18]), .in1(ram_1_data_2[17:13]), .out(multiplexer_2_out), .sel(RegDst));
  assign bit_extender_1_out = {{16{ram_1_data_2[17]}}, ram_1_data_2[17:2]};  // Bit_Extender bit_extender_1
  assign bit_extender_2_out = {{16{1'b0}}, ram_1_data_2[17:2]};  // Bit_Extender bit_extender_2
  Counter #(.width(32), .max('hffffffff)) counter_3 (.count(1'b1), .Q(cnt), .clk(clk));  // open: load, D, carry, clr
  D_Flip_Flop d_ff_1 (.clk(and_1_out), .D(1'b1), .Q(d_ff_1_q), .preset(1'b0));  // open: Qn, en, reset
  Multiplexer #(.width(5), .enable("false")) multiplexer_3 (
    .in0(ram_1_data_2[27:23]), .in1(5'b00010), .out(multiplexer_3_out), .sel(syscall));
  Multiplexer #(.width(5), .enable("false")) multiplexer_4 (
    .in0(ram_1_data_2[22:18]), .in1(5'b00100), .out(rt), .sel(syscall));
  Multiplexer #(.width(5), .enable("false")) multiplexer_5 (
    .in0(multiplexer_2_out), .in1({5{1'b1}}), .out(rd), .sel(Jal));
  assign bit_extender_3_out = {{27{1'b0}}, ram_1_data_2[12:8]};  // Bit_Extender bit_extender_3
  Multiplexer #(.width(32), .enable("false")) multiplexer_6 (
    .in0(bit_extender_1_out), .in1(bit_extender_2_out), .out(multiplexer_6_out), .sel(Unsigned));
  // Probe on {ram_1_data_2, 2'b00}
  Multiplexer #(.width(5), .enable("false")) multiplexer_7 (
    .in0(multiplexer_3_out), .in1({5{1'b1}}), .out(rs), .sel(Jr));
  D_Flip_Flop d_ff_2 (.clk(clkin), .D(d_ff_1_q), .Q(Halt), .preset(1'b0));  // open: Qn, en, reset
  Multiplexer #(.width(32), .enable("false")) multiplexer_8 (
    .in0(multiplexer_14_out), .in1(adder_2_out), .out(multiplexer_8_out), .sel(Jal));
  // Probe on Icnt
  // Probe on Rcnt
  // Probe on Jcnt
  // Probe on cnt
  Control_unit control_unit_1 (
    .in_1({ram_1_data, ram_1_data_2[27:2]}), .J_type(J), .MemWrite(MemWrite), .MemRead(MemRead),
    .MemtoReg(MemtoReg), .AluSrc(ALUSrc), .RegWrite(RegWrite), .syscall(syscall), .shift(Shift),
    .\unsigned (Unsigned), .jr(Jr), .jal(Jal), .jump(Jump), .I_type(I), .R_type(R), .RegDst(RegDst),
    .beq(beq), .bne(bne), .ALUOp(ALUOp));
  // ACM1401_U201414697_朱谷才_regfile_main main_1: pin names not known; wires that end beside it: rs, rt, rd, s0, multiplexer_8_out, s1, RegWrite, clk, ra, main_1_p10, main_1_p11
  // Probe on main_1_p11
  // Probe on multiplexer_8_out
  // Probe on main_1_p10
  Multiplexer #(.width(32), .enable("false")) multiplexer_9 (
    .in0(main_1_p11), .in1(multiplexer_6_out), .out(multiplexer_9_out), .sel(ALUSrc));
  // Probe on s0
  // Probe on s1
  // Probe on rs
  // Probe on rt
  // Probe on rd
  // Probe on ra
  Shifter #(.width(32)) shifter_1 (.in(multiplexer_6_out), .\dist (5'b00010), .out(shifter_1_out));
  and and_2 (and_2_out, beq, Equal);
  and and_3 (and_3_out, ~Equal, bne);  // AND_Gate
  Multiplexer #(.width(32), .enable("false")) multiplexer_10 (.in0(main_1_p10), .in1(main_1_p11), .out(x), .sel(Shift));
  // Probe on ALUOp
  Adder #(.width(32)) adder_3 (
    .a({ram_1_data_2[31:28], adder_1_out}), .b(shifter_1_out), .out(adder_3_out));  // open: cin, cout
  or or_1 (Branch, and_2_out, and_3_out);
  Multiplexer #(.width(32), .enable("false")) multiplexer_11 (
    .in0(multiplexer_9_out), .in1(bit_extender_3_out), .out(multiplexer_11_out), .sel(Shift));
  Multiplexer #(.width(32), .enable("false")) multiplexer_12 (
    .in0({ram_1_data_2[31:28], adder_1_out}), .in1(adder_3_out), .out(multiplexer_12_out), .sel(Branch));
  ALU alu_1 (
    .AluOP(ALUOp), .X(x), .Equal(Equal), .Result(alures), .Y(y));  // open: Signed_Overflow, Result_2, UnSigned_Overflow
  Multiplexer #(.width(32), .enable("false")) multiplexer_13 (
    .in0(multiplexer_11_out), .in1(32'ha), .out(y), .sel(syscall));
  Multiplexer #(.width(32), .enable("false")) multiplexer_14 (
    .in0(alures), .in1(ram_2_data), .out(multiplexer_14_out), .sel(MemtoReg));
  // Probe on x
  // Probe on y
  // Probe on alures
  // Probe on alures
  Multiplexer #(.width(32), .enable("false")) multiplexer_15 (
    .in0(multiplexer_12_out), .in1({ram_1_data_2, 2'b00}), .out(multiplexer_15_out), .sel(Jump));
  Multiplexer #(.width(32), .enable("false")) multiplexer_16 (
    .in0(multiplexer_15_out), .in1(main_1_p10), .out(multiplexer_16_out), .sel(Jr));
  Hex_Digit_Display hex_digit_display_1 (.value(counter_4_q[31:28]));  // open: dp
  Counter #(.width(32), .max('hffffffff), .ongoal("load")) counter_4 (
    .load(syscall), .D(main_1_p11), .count(1'b0), .Q(counter_4_q), .clk(clk));  // open: carry, clr
  Hex_Digit_Display hex_digit_display_2 (.value(counter_4_q[23:20]));  // open: dp
  Hex_Digit_Display hex_digit_display_3 (.value(counter_4_q[27:24]));  // open: dp
  RAM #(.addrWidth(10), .dataWidth(32), .bus("separate")) ram_2 (
    .addr(alures[11:2]), .din(main_1_p11), .data(ram_2_data), .str(MemWrite), .clk(clk), .ld(MemRead));  // open: sel, clr
  Hex_Digit_Display hex_digit_display_4 (.value(counter_4_q[15:12]));  // open: dp
  Hex_Digit_Display hex_digit_display_5 (.value(counter_4_q[19:16]));  // open: dp
  Hex_Digit_Display hex_digit_display_6 (.value(counter_4_q[7:4]));  // open: dp
  Hex_Digit_Display hex_digit_display_7 (.value(counter_4_q[11:8]));  // open: dp
  Hex_Digit_Display hex_digit_display_8 (.value(counter_4_q[3:0]));  // open: dp

  // Notes on the sheet:
  //   rs
  //   rd
  //   rt
  //   顺序地址
  //   直接跳转地址
  //   条件跳转
  //   寄存器跳转
  //   $a0
endmodule

module Control_unit (
  input  [31:0] in_1,
  output MemWrite,
  output J_type,
  output I_type,
  output R_type,
  output MemRead,
  output RegDst,
  output jump,
  output MemtoReg,
  output AluSrc,
  output beq,
  output bne,
  output RegWrite,
  output shift,
  output syscall,
  output \unsigned ,
  output jr,
  output jal,
  output [3:0] ALUOp
);

  wire add, addi, addiu, addu, \and , and_1_out, andi, COM, isAdd, isAnd, isOr, jump_t, \nor , not_1_out,
       \or , or_3_out, or_4_out, ori, r_type2_1_sllv, r_type2_1_srav, r_type2_1_srlv, shamt_is_0, sll, slt,
       slti, sltu, sra, srl, sub;
  wire [3:0] multiplexer_1_out, multiplexer_2_out, multiplexer_3_out, multiplexer_4_out, multiplexer_5_out,
       multiplexer_6_out, multiplexer_7_out, multiplexer_8_out;

  nor nor_1 (shamt_is_0, in_1[6], in_1[7], in_1[8], in_1[9], in_1[10]);
  nor nor_2 (R_type, in_1[26], in_1[27], in_1[28], in_1[29], in_1[30], in_1[31]);
  I_type i_type_1 (
    .op5(in_1[31]), .op4(in_1[30]), .op3(in_1[29]), .op2(in_1[28]), .op1(in_1[27]), .op0(in_1[26]),
    .addi(addi), .addiu(addiu), .andi(andi), .ori(ori), .lw(MemRead), .sw(MemWrite), .beq(beq), .bne(bne),
    .slti(slti));  // open: xori, lui, sltiu
  J_type j_type_1 (
    .op5(in_1[31]), .op4(in_1[30]), .op3(in_1[29]), .op2(in_1[28]), .op1(in_1[27]), .op0(in_1[26]),
    .j(jump_t), .jal(jal));
  R_type2 r_type2_1 (
    .func5(in_1[5]), .func4(in_1[4]), .sra(sra), .func3(in_1[3]), .func2(in_1[2]), .func1(in_1[1]),
    .sllv(r_type2_1_sllv), .func0(in_1[0]), .opiszero(R_type), .srlv(r_type2_1_srlv), .srav(r_type2_1_srav),
    .jr(jr), .syscall(syscall));
  R_type r_type_1 (
    .func5(in_1[5]), .func4(in_1[4]), .add(add), .func3(in_1[3]), .func2(in_1[2]), .func1(in_1[1]),
    .addu(addu), .func0(in_1[0]), .opiszero(R_type), .sub(sub), .\and (\and ), .\or (\or ), .\nor (\nor ),
    .slt(slt), .sltu(sltu), .sll(sll), .srl(srl));  // open: subu, xor
  or or_1 (J_type, jump_t, jal);
  Multiplexer #(.width(4), .enable("false")) multiplexer_1 (
    .in0(4'b0000), .in1(4'b0001), .out(multiplexer_1_out), .sel(sra));
  or or_2 (isAnd, \and , andi);
  or or_3 (or_3_out, addi, jal, addiu, andi);
  or or_4 (or_4_out, ori, MemRead, slti);
  and and_1 (and_1_out, R_type, ~jr, ~syscall);  // AND_Gate
  Multiplexer #(.width(4), .enable("false")) multiplexer_2 (
    .in0(multiplexer_1_out), .in1(4'b0010), .out(multiplexer_2_out), .sel(srl));
  or or_5 (RegWrite, or_3_out, or_4_out, and_1_out);
  Multiplexer #(.width(4), .enable("false")) multiplexer_3 (
    .in0(multiplexer_2_out), .in1(4'b0101), .out(multiplexer_3_out), .sel(isAdd));
  Multiplexer #(.width(4), .enable("false")) multiplexer_4 (
    .in0(multiplexer_3_out), .in1(4'b0110), .out(multiplexer_4_out), .sel(sub));
  or or_6 (COM, slt, slti);
  Multiplexer #(.width(4), .enable("false")) multiplexer_5 (
    .in0(multiplexer_4_out), .in1(4'b0111), .out(multiplexer_5_out), .sel(isAnd));
  Multiplexer #(.width(4), .enable("false")) multiplexer_6 (
    .in0(multiplexer_5_out), .in1(4'b1000), .out(multiplexer_6_out), .sel(isOr));
  or or_7 (isAdd, MemRead, addu, addiu, addi, add, MemWrite);
  or or_8 (shift, sll, srl, sra);
  Multiplexer #(.width(4), .enable("false")) multiplexer_7 (
    .in0(multiplexer_6_out), .in1(4'b1010), .out(multiplexer_7_out), .sel(\nor ));
  Multiplexer #(.width(4), .enable("false")) multiplexer_8 (
    .in0(multiplexer_7_out), .in1(4'b1011), .out(multiplexer_8_out), .sel(COM));
  Multiplexer #(.width(4), .enable("false")) multiplexer_9 (
    .in0(multiplexer_8_out), .in1(4'b1100), .out(ALUOp), .sel(sltu));
  or or_9 (isOr, ori, \or );
  not not_1 (not_1_out, R_type);
  or or_10 (\unsigned , addiu, addu, sltu);
  and and_2 (I_type, not_1_out, ~jal, ~jump_t);  // AND_Gate
  and and_3 (AluSrc, I_type, ~beq, ~bne);  // AND_Gate

  assign jump = J_type;
  assign MemtoReg = MemRead;
  assign RegDst = R_type;

  // Other names for the same wires on the sheet: func[5:0] = in_1[5:0]; shamt[4:0] = in_1[10:6];
  //   rd[4:0] = in_1[15:11]; rt[4:0] = in_1[20:16]; rs[4:0] = in_1[25:21]; op[5:0] = in_1[31:26]; lw = MemRead;
  //   op_is_0 = R_type; sw = MemWrite
endmodule

module Control_Unit (
  input  [31:0] in_1,
  output addi,
  output sra,
  output addiu,
  output andi,
  output ori,
  output lw,
  output sw,
  output beq,
  output bne,
  output slti,
  output jr,
  output syscall,
  output add,
  output addu,
  output sub,
  output j,
  output \and ,
  output \or ,
  output \nor ,
  output slt,
  output jal,
  output sltu,
  output sll,
  output srl
);

  wire i_type_1_lui, i_type_1_sltiu, i_type_1_xori, op_is_0, r_type2_1_sllv, r_type2_1_srav, r_type2_1_srlv,
       shamt_is_0;

  nor nor_1 (shamt_is_0, in_1[6], in_1[7], in_1[8], in_1[9], in_1[10]);
  nor nor_2 (op_is_0, in_1[26], in_1[27], in_1[28], in_1[29], in_1[30], in_1[31]);
  I_type i_type_1 (
    .op5(in_1[31]), .op4(in_1[30]), .op3(in_1[29]), .op2(in_1[28]), .op1(in_1[27]), .op0(in_1[26]),
    .addi(addi), .addiu(addiu), .andi(andi), .ori(ori), .xori(i_type_1_xori), .lui(i_type_1_lui), .lw(lw),
    .sw(sw), .beq(beq), .bne(bne), .slti(slti), .sltiu(i_type_1_sltiu));
  J_type j_type_1 (
    .op5(in_1[31]), .op4(in_1[30]), .op3(in_1[29]), .op2(in_1[28]), .op1(in_1[27]), .op0(in_1[26]), .j(j),
    .jal(jal));
  R_type2 r_type2_1 (
    .func5(in_1[5]), .func4(in_1[4]), .sra(sra), .func3(in_1[3]), .func2(in_1[2]), .func1(in_1[1]),
    .sllv(r_type2_1_sllv), .func0(in_1[0]), .opiszero(op_is_0), .srlv(r_type2_1_srlv), .srav(r_type2_1_srav),
    .jr(jr), .syscall(syscall));
  R_type r_type_1 (
    .func5(in_1[5]), .func4(in_1[4]), .add(add), .func3(in_1[3]), .func2(in_1[2]), .func1(in_1[1]),
    .addu(addu), .func0(in_1[0]), .opiszero(op_is_0), .sub(sub), .\and (\and ), .\or (\or ), .\nor (\nor ),
    .slt(slt), .sltu(sltu), .sll(sll), .srl(srl));  // open: subu, xor

  // Other names for the same wires on the sheet: func[5:0] = in_1[5:0]; shamt[4:0] = in_1[10:6];
  //   rd[4:0] = in_1[15:11]; rt[4:0] = in_1[20:16]; rs[4:0] = in_1[25:21]; op[5:0] = in_1[31:26]
endmodule

module I_type (
  input  op5,
  input  op4,
  input  op3,
  input  op2,
  input  op1,
  input  op0,
  output addi,
  output addiu,
  output andi,
  output ori,
  output xori,
  output lui,
  output lw,
  output sw,
  output beq,
  output bne,
  output slti,
  output sltiu
);

  wire not_1_out, not_2_out, not_3_out, not_4_out, not_5_out, not_6_out, not_7_out, not_8_out, not_9_out,
       not_10_out, not_11_out, not_12_out, not_13_out, not_14_out, not_15_out, not_16_out, not_17_out,
       not_18_out, not_19_out, not_20_out, not_21_out, not_22_out, not_23_out, not_24_out, not_25_out,
       not_26_out, not_27_out, not_28_out, not_29_out, not_30_out, not_31_out, not_32_out, not_33_out,
       not_34_out, not_35_out, not_36_out, not_37_out, not_38_out, not_39_out, not_40_out, not_41_out,
       not_42_out;

  not not_1 (not_1_out, op5);
  not not_2 (not_2_out, op4);
  not not_3 (not_3_out, op2);
  not not_4 (not_4_out, op1);
  not not_5 (not_5_out, op0);
  not not_6 (not_6_out, op5);
  not not_7 (not_7_out, op4);
  not not_8 (not_8_out, op2);
  not not_9 (not_9_out, op1);
  not not_10 (not_10_out, op5);
  not not_11 (not_11_out, op4);
  not not_12 (not_12_out, op1);
  not not_13 (not_13_out, op0);
  not not_14 (not_14_out, op5);
  not not_15 (not_15_out, op4);
  not not_16 (not_16_out, op1);
  not not_17 (not_17_out, op5);
  not not_18 (not_18_out, op4);
  not not_19 (not_19_out, op0);
  not not_20 (not_20_out, op5);
  not not_21 (not_21_out, op4);
  not not_22 (not_22_out, op4);
  not not_23 (not_23_out, op3);
  not not_24 (not_24_out, op2);
  not not_25 (not_25_out, op4);
  not not_26 (not_26_out, op2);
  not not_27 (not_27_out, op5);
  not not_28 (not_28_out, op4);
  not not_29 (not_29_out, op3);
  not not_30 (not_30_out, op1);
  not not_31 (not_31_out, op0);
  not not_32 (not_32_out, op5);
  not not_33 (not_33_out, op4);
  not not_34 (not_34_out, op3);
  not not_35 (not_35_out, op1);
  not not_36 (not_36_out, op5);
  not not_37 (not_37_out, op4);
  not not_38 (not_38_out, op2);
  not not_39 (not_39_out, op0);
  not not_40 (not_40_out, op5);
  not not_41 (not_41_out, op4);
  not not_42 (not_42_out, op2);
  and and_1 (addi, not_1_out, not_2_out, op3, not_3_out, not_4_out, not_5_out);
  and and_2 (addiu, not_6_out, not_7_out, op3, not_8_out, not_9_out, op0);
  and and_3 (andi, not_10_out, not_11_out, op3, op2, not_12_out, not_13_out);
  and and_4 (ori, not_14_out, not_15_out, op3, op2, not_16_out, op0);
  and and_5 (xori, not_17_out, not_18_out, op3, op2, op1, not_19_out);
  and and_6 (lui, not_20_out, not_21_out, op3, op2, op1, op0);
  and and_7 (lw, op5, not_22_out, not_23_out, not_24_out, op1, op0);
  and and_8 (sw, op5, not_25_out, op3, not_26_out, op1, op0);
  and and_9 (beq, not_27_out, not_28_out, not_29_out, op2, not_30_out, not_31_out);
  and and_10 (bne, not_32_out, not_33_out, not_34_out, op2, not_35_out, op0);
  and and_11 (slti, not_36_out, not_37_out, op3, not_38_out, op1, not_39_out);
  and and_12 (sltiu, not_40_out, not_41_out, op3, not_42_out, op1, op0);
endmodule

module R_type (
  input  func5,
  input  func4,
  input  func3,
  input  func2,
  input  func1,
  input  func0,
  input  opiszero,
  output add,
  output addu,
  output sub,
  output subu,
  output \and ,
  output \or ,
  output \xor ,
  output \nor ,
  output slt,
  output sltu,
  output sll,
  output srl
);

  wire not_1_out, not_2_out, not_3_out, not_4_out, not_5_out, not_6_out, not_7_out, not_8_out, not_9_out,
       not_10_out, not_11_out, not_12_out, not_13_out, not_14_out, not_15_out, not_16_out, not_17_out,
       not_18_out, not_19_out, not_20_out, not_21_out, not_22_out, not_23_out, not_24_out, not_25_out,
       not_26_out, not_27_out, not_28_out, not_29_out, not_30_out, not_31_out, not_32_out, not_33_out,
       not_34_out, not_35_out, not_36_out, not_37_out, not_38_out, not_39_out, not_40_out, not_41_out,
       not_42_out, not_43_out, not_44_out;

  not not_1 (not_1_out, func4);
  not not_2 (not_2_out, func3);
  not not_3 (not_3_out, func2);
  not not_4 (not_4_out, func1);
  not not_5 (not_5_out, func0);
  not not_6 (not_6_out, func4);
  not not_7 (not_7_out, func3);
  not not_8 (not_8_out, func2);
  not not_9 (not_9_out, func1);
  not not_10 (not_10_out, func4);
  not not_11 (not_11_out, func3);
  not not_12 (not_12_out, func2);
  not not_13 (not_13_out, func0);
  not not_14 (not_14_out, func4);
  not not_15 (not_15_out, func3);
  not not_16 (not_16_out, func2);
  not not_17 (not_17_out, func4);
  not not_18 (not_18_out, func3);
  not not_19 (not_19_out, func1);
  not not_20 (not_20_out, func0);
  not not_21 (not_21_out, func4);
  not not_22 (not_22_out, func3);
  not not_23 (not_23_out, func1);
  not not_24 (not_24_out, func4);
  not not_25 (not_25_out, func3);
  not not_26 (not_26_out, func0);
  not not_27 (not_27_out, func4);
  not not_28 (not_28_out, func3);
  not not_29 (not_29_out, func4);
  not not_30 (not_30_out, func2);
  not not_31 (not_31_out, func0);
  not not_32 (not_32_out, func4);
  not not_33 (not_33_out, func2);
  not not_34 (not_34_out, func5);
  not not_35 (not_35_out, func4);
  not not_36 (not_36_out, func3);
  not not_37 (not_37_out, func2);
  not not_38 (not_38_out, func1);
  not not_39 (not_39_out, func0);
  not not_40 (not_40_out, func5);
  not not_41 (not_41_out, func4);
  not not_42 (not_42_out, func3);
  not not_43 (not_43_out, func2);
  not not_44 (not_44_out, func0);
  and and_1 (add, func5, not_1_out, not_2_out, not_3_out, not_4_out, not_5_out, opiszero);
  and and_2 (addu, func5, not_6_out, not_7_out, not_8_out, not_9_out, func0, opiszero);
  and and_3 (sub, func5, not_10_out, not_11_out, not_12_out, func1, not_13_out, opiszero);
  and and_4 (subu, func5, not_14_out, not_15_out, not_16_out, func1, func0, opiszero);
  and and_5 (\and , func5, not_17_out, not_18_out, func2, not_19_out, not_20_out, opiszero);
  and and_6 (\or , func5, not_21_out, not_22_out, func2, not_23_out, func0, opiszero);
  and and_7 (\xor , func5, not_24_out, not_25_out, func2, func1, not_26_out, opiszero);
  and and_8 (\nor , func5, not_27_out, not_28_out, func2, func1, func0, opiszero);
  and and_9 (slt, func5, not_29_out, func3, not_30_out, func1, not_31_out, opiszero);
  and and_10 (sltu, func5, not_32_out, func3, not_33_out, func1, func0, opiszero);
  and and_11 (sll, not_34_out, not_35_out, not_36_out, not_37_out, not_38_out, not_39_out, opiszero);
  and and_12 (srl, not_40_out, not_41_out, not_42_out, not_43_out, func1, not_44_out, opiszero);
endmodule

module R_type2 (
  input  func5,
  input  func4,
  input  func3,
  input  func2,
  input  func1,
  input  func0,
  input  opiszero,
  output sra,
  output sllv,
  output srlv,
  output srav,
  output jr,
  output syscall
);

  wire not_1_out, not_2_out, not_3_out, not_4_out, not_5_out, not_6_out, not_7_out, not_8_out, not_9_out,
       not_10_out, not_11_out, not_12_out, not_13_out, not_14_out, not_15_out, not_16_out, not_17_out,
       not_18_out, not_19_out, not_20_out, not_21_out, not_22_out, not_23_out, not_24_out;

  not not_1 (not_1_out, func5);
  not not_2 (not_2_out, func4);
  not not_3 (not_3_out, func3);
  not not_4 (not_4_out, func2);
  not not_5 (not_5_out, func5);
  not not_6 (not_6_out, func4);
  not not_7 (not_7_out, func3);
  not not_8 (not_8_out, func2);
  not not_9 (not_9_out, func5);
  not not_10 (not_10_out, func4);
  not not_11 (not_11_out, func3);
  not not_12 (not_12_out, func0);
  not not_13 (not_13_out, func5);
  not not_14 (not_14_out, func4);
  not not_15 (not_15_out, func3);
  not not_16 (not_16_out, func5);
  not not_17 (not_17_out, func4);
  not not_18 (not_18_out, func2);
  not not_19 (not_19_out, func1);
  not not_20 (not_20_out, func0);
  not not_21 (not_21_out, func5);
  not not_22 (not_22_out, func4);
  not not_23 (not_23_out, func1);
  not not_24 (not_24_out, func0);
  and and_1 (sra, not_1_out, not_2_out, not_3_out, not_4_out, func1, func0, opiszero);
  and and_2 (sllv, not_5_out, not_6_out, not_7_out, not_8_out, func1, func0, opiszero);
  and and_3 (srlv, not_9_out, not_10_out, not_11_out, func2, func1, not_12_out, opiszero);
  and and_4 (srav, not_13_out, not_14_out, not_15_out, func2, func1, func0, opiszero);
  and and_5 (jr, not_16_out, not_17_out, func3, not_18_out, not_19_out, not_20_out, opiszero);
  and and_6 (syscall, not_21_out, not_22_out, func3, func2, not_23_out, not_24_out, opiszero);
endmodule

module J_type (
  input  op5,
  input  op4,
  input  op3,
  input  op2,
  input  op1,
  input  op0,
  output j,
  output jal
);

  wire not_1_out, not_2_out, not_3_out, not_4_out, not_5_out, not_6_out, not_7_out, not_8_out, not_9_out;

  not not_1 (not_1_out, op5);
  not not_2 (not_2_out, op4);
  not not_3 (not_3_out, op3);
  not not_4 (not_4_out, op2);
  not not_5 (not_5_out, op0);
  not not_6 (not_6_out, op5);
  not not_7 (not_7_out, op4);
  not not_8 (not_8_out, op3);
  not not_9 (not_9_out, op2);
  and and_1 (j, not_1_out, not_2_out, not_3_out, not_4_out, op1, not_5_out);
  and and_2 (jal, not_6_out, not_7_out, not_8_out, not_9_out, op1, op0);
endmodule

module newUnit (
  input  [31:0] in_1,
  output MemWrite,
  output J_type,
  output I_type,
  output R_type,
  output MemRead,
  output RegDst,
  output AluSrc,
  output jump,
  output MemtoReg,
  output RegWrite,
  output shift,
  output syscall,
  output \unsigned ,
  output jr,
  output jal
);

  wire add, addi, addiu, addu, \and , and_2_out, andi, beq, bne, \nor , not_1_out, \or , or_1_out, or_2_out,
       ori, r_type2_1_sllv, r_type2_1_srav, r_type2_1_srlv, shamt_is_0, sll, slt, slti, sltu, sra, srl, sub;

  nor nor_1 (shamt_is_0, in_1[6], in_1[7], in_1[8], in_1[9], in_1[10]);
  nor nor_2 (R_type, in_1[26], in_1[27], in_1[28], in_1[29], in_1[30], in_1[31]);
  I_type i_type_1 (
    .op5(in_1[31]), .op4(in_1[30]), .op3(in_1[29]), .op2(in_1[28]), .op1(in_1[27]), .op0(in_1[26]),
    .addi(addi), .addiu(addiu), .andi(andi), .ori(ori), .lw(MemRead), .sw(MemWrite), .beq(beq), .bne(bne),
    .slti(slti));  // open: xori, lui, sltiu
  J_type j_type_1 (
    .op5(in_1[31]), .op4(in_1[30]), .op3(in_1[29]), .op2(in_1[28]), .op1(in_1[27]), .op0(in_1[26]), .j(jump),
    .jal(jal));
  R_type2 r_type2_1 (
    .func5(in_1[5]), .func4(in_1[4]), .sra(sra), .func3(in_1[3]), .func2(in_1[2]), .func1(in_1[1]),
    .sllv(r_type2_1_sllv), .func0(in_1[0]), .opiszero(R_type), .srlv(r_type2_1_srlv), .srav(r_type2_1_srav),
    .jr(jr), .syscall(syscall));
  R_type r_type_1 (
    .func5(in_1[5]), .func4(in_1[4]), .add(add), .func3(in_1[3]), .func2(in_1[2]), .func1(in_1[1]),
    .addu(addu), .func0(in_1[0]), .opiszero(R_type), .sub(sub), .\and (\and ), .\or (\or ), .\nor (\nor ),
    .slt(slt), .sltu(sltu), .sll(sll), .srl(srl));  // open: subu, xor
  and and_1 (J_type, jump, jal);
  or or_1 (or_1_out, addi, addiu, andi);
  or or_2 (or_2_out, ori, MemRead, slti);
  and and_2 (and_2_out, R_type, ~jr);  // AND_Gate
  or or_3 (RegWrite, or_1_out, or_2_out, and_2_out);
  or or_4 (shift, sll, srl, sra);
  not not_1 (not_1_out, R_type);
  or or_5 (\unsigned , addiu, addu, sltu);
  and and_3 (AluSrc, not_1_out, ~jal, ~jump);  // AND_Gate

  assign I_type = AluSrc;
  assign MemtoReg = MemRead;
  assign RegDst = R_type;

  // Other names for the same wires on the sheet: func[5:0] = in_1[5:0]; shamt[4:0] = in_1[10:6];
  //   rd[4:0] = in_1[15:11]; rt[4:0] = in_1[20:16]; rs[4:0] = in_1[25:21]; op[5:0] = in_1[31:26]; lw = MemRead;
  //   op_is_0 = R_type; sw = MemWrite
endmodule

module Latch (
  input  clk,
  input  syscall,
  input  equal,
  output halt
);

  wire and_1_out, d_ff_1_q;

  and and_1 (and_1_out, syscall, equal);
  D_Flip_Flop d_ff_1 (.clk(and_1_out), .D(1'b1), .Q(d_ff_1_q));  // open: Qn, preset, en, reset
  D_Flip_Flop d_ff_2 (.clk(clk), .D(d_ff_1_q), .Q(halt));  // open: Qn, preset, en, reset
endmodule
