// Logisim project regfile.circ as structural Verilog: 2 circuits, main circuit main
module main (
  input  [4:0] Reg1_num,
  input  [4:0] Reg2,
  input  [4:0] Write_Reg_num,
  input  [31:0] Din,
  input  Write_Enable,
  input  Clock,
  output [31:0] Reg1,
  output [31:0] s0_Value,
  output [31:0] s1_Value,
  output [31:0] s2_Value,
  output [31:0] ra_Value,
  output [31:0] Reg2_2
);

  wire _01_in, _02_in, _03_in, _04_in, _05_in, _06_in, _07_in, _08_in, _09_in, _10_in, _11_in, _12_in,
       _13_in, _14_in, _15_in, _16_in, _17_in, _18_in, _19_in, _20_in, _21_in, _22_in, _23_in, _24_in,
       _25_in, _26_in, _27_in, _28_in, _29_in, _30_in, _31_in;
  wire [31:0] _00_out, _01_out, _02_out, _03_out, _04_out, _05_out, _06_out, _07_out, _08_out, _09_out,
       _10_out, _11_out, _12_out, _13_out, _14_out, _15_out, _19_out, _20_out, _21_out, _22_out, _23_out,
       _24_out, _25_out, _26_out, _27_out, _28_out, _29_out, _30_out;

  Register #(.width(32)) _0 (.D({32{1'b0}}), .en(1'b0), .Q(_00_out), .clk(Clock), .clr(1'b1));
  Register #(.width(32)) _1 (.D(Din), .en(_01_in), .Q(_01_out), .clk(Clock), .clr(1'b0));
  Register #(.width(32)) _2 (.D(Din), .en(_02_in), .Q(_02_out), .clk(Clock), .clr(1'b0));
  Register #(.width(32)) _3 (.D(Din), .en(_03_in), .Q(_03_out), .clk(Clock), .clr(1'b0));
  Register #(.width(32)) _4 (.D(Din), .en(_04_in), .Q(_04_out), .clk(Clock), .clr(1'b0));
  Register #(.width(32)) _5 (.D(Din), .en(_05_in), .Q(_05_out), .clk(Clock), .clr(1'b0));
  Register #(.width(32)) _6 (.D(Din), .en(_06_in), .Q(_06_out), .clk(Clock), .clr(1'b0));
  Register #(.width(32)) _7 (.D(Din), .en(_07_in), .Q(_07_out), .clk(Clock), .clr(1'b0));
  Register #(.width(32)) _8 (.D(Din), .en(_08_in), .Q(_08_out), .clk(Clock), .clr(1'b0));
  Register #(.width(32)) _9 (.D(Din), .en(_09_in), .Q(_09_out), .clk(Clock), .clr(1'b0));
  Register #(.width(32)) _10 (.D(Din), .en(_10_in), .Q(_10_out), .clk(Clock), .clr(1'b0));
  Register #(.width(32)) _11 (.D(Din), .en(_11_in), .Q(_11_out), .clk(Clock), .clr(1'b0));
  Register #(.width(32)) _12 (.D(Din), .en(_12_in), .Q(_12_out), .clk(Clock), .clr(1'b0));
  Register #(.width(32)) _13 (.D(Din), .en(_13_in), .Q(_13_out), .clk(Clock), .clr(1'b0));
  Register #(.width(32)) _14 (.D(Din), .en(_14_in), .Q(_14_out), .clk(Clock), .clr(1'b0));
  Register #(.width(32)) _15 (.D(Din), .en(_15_in), .Q(_15_out), .clk(Clock), .clr(1'b0));
  Register #(.width(32)) _16 (.D(Din), .en(_16_in), .Q(s0_Value), .clk(Clock), .clr(1'b0));
  Register #(.width(32)) _17 (.D(Din), .en(_17_in), .Q(s1_Value), .clk(Clock), .clr(1'b0));
  Register #(.width(32)) _18 (.D(Din), .en(_18_in), .Q(s2_Value), .clk(Clock), .clr(1'b0));
  Register #(.width(32)) _19 (.D(Din), .en(_19_in), .Q(_19_out), .clk(Clock), .clr(1'b0));
  Register #(.width(32)) _20 (.D(Din), .en(_20_in), .Q(_20_out), .clk(Clock), .clr(1'b0));
  Register #(.width(32)) _21 (.D(Din), .en(_21_in), .Q(_21_out), .clk(Clock), .clr(1'b0));
  Register #(.width(32)) _22 (.D(Din), .en(_22_in), .Q(_22_out), .clk(Clock), .clr(1'b0));
  Register #(.width(32)) _23 (.D(Din), .en(_23_in), .Q(_23_out), .clk(Clock), .clr(1'b0));
  Register #(.width(32)) _24 (.D(Din), .en(_24_in), .Q(_24_out), .clk(Clock), .clr(1'b0));
  Register #(.width(32)) _25 (.D(Din), .en(_25_in), .Q(_25_out), .clk(Clock), .clr(1'b0));
  Register #(.width(32)) _26 (.D(Din), .en(_26_in), .Q(_26_out), .clk(Clock), .clr(1'b0));
  Register #(.width(32)) _27 (.D(Din), .en(_27_in), .Q(_27_out), .clk(Clock), .clr(1'b0));
  Register #(.width(32)) _28 (.D(Din), .en(_28_in), .Q(_28_out), .clk(Clock), .clr(1'b0));
  Register #(.width(32)) _29 (.D(Din), .en(_29_in), .Q(_29_out), .clk(Clock), .clr(1'b0));
  Register #(.width(32)) _30 (.D(Din), .en(_30_in), .Q(_30_out), .clk(Clock), .clr(1'b0));
  Register #(.width(32)) _31 (.D(Din), .en(_31_in), .Q(ra_Value), .clk(Clock), .clr(1'b0));
  Multiplexer #(.select(5), .width(32), .enable("false")) multiplexer_1 (
    .in0(_00_out), .in1(_01_out), .in2(_02_out), .in3(_03_out), .in4(_04_out), .in5(_05_out), .in6(_06_out),
    .in7(_07_out), .in8(_08_out), .in9(_09_out), .in10(_10_out), .in11(_11_out), .in12(_12_out),
    .in13(_13_out), .in14(_14_out), .in15(_15_out), .in16(s0_Value), .in17(s1_Value), .in18(s2_Value),
    .in19(_19_out), .in20(_20_out), .in21(_21_out), .in22(_22_out), .in23(_23_out), .in24(_24_out),
    .in25(_25_out), .in26(_26_out), .in27(_27_out), .in28(_28_out), .in29(_29_out), .in30(_30_out),
    .in31(ra_Value), .out(Reg1), .sel(Reg1_num));
  Multiplexer #(.select(5), .width(32), .enable("false")) multiplexer_2 (
    .in0(_00_out), .in1(_01_out), .in2(_02_out), .in3(_03_out), .in4(_04_out), .in5(_05_out), .in6(_06_out),
    .in7(_07_out), .in8(_08_out), .in9(_09_out), .in10(_10_out), .in11(_11_out), .in12(_12_out),
    .in13(_13_out), .in14(_14_out), .in15(_15_out), .in16(s0_Value), .in17(s1_Value), .in18(s2_Value),
    .in19(_19_out), .in20(_20_out), .in21(_21_out), .in22(_22_out), .in23(_23_out), .in24(_24_out),
    .in25(_25_out), .in26(_26_out), .in27(_27_out), .in28(_28_out), .in29(_29_out), .in30(_30_out),
    .in31(ra_Value), .out(Reg2_2), .sel(Reg2));
  Decoder #(.select(5), .disabled(0)) decoder_1 (
    .out1(_01_in), .out2(_02_in), .out3(_03_in), .out4(_04_in), .out5(_05_in), .out6(_06_in), .out7(_07_in),
    .out8(_08_in), .out9(_09_in), .out10(_10_in), .out11(_11_in), .out12(_12_in), .out13(_13_in),
    .out14(_14_in), .out15(_15_in), .out16(_16_in), .out17(_17_in), .out18(_18_in), .out19(_19_in),
    .out20(_20_in), .out21(_21_in), .out22(_22_in), .out23(_23_in), .out24(_24_in), .out25(_25_in),
    .out26(_26_in), .out27(_27_in), .out28(_28_in), .out29(_29_in), .out30(_30_in), .out31(_31_in),
    .sel(Write_Reg_num), .en(Write_Enable));  // open: out0

  // Other names for the same wires on the sheet: _16_out[31:0] = s0_Value; s0[31:0] = s0_Value;
  //   _17_out[31:0] = s1_Value; s1[31:0] = s1_Value; _18_out[31:0] = s2_Value; s2[31:0] = s2_Value;
  //   _31_out[31:0] = ra_Value; ra[31:0] = ra_Value; clk = Clock; reg2_num[4:0] = Reg2; reg2_t[31:0] = Reg2_2;
  //   WE = Write_Enable; write_data[31:0] = Din

  // Notes on the sheet:
  //   输入引脚
  //   输出引脚
  //   Debug引脚，便于观测寄存器值
  //   请勿修改引脚以及封装，直接使用隧道连接电路
endmodule

module test (
);

  wire button_1_out, clock_1_out, comparator_1_eq;
  wire [5:0] adder_1_out, bit_extender_1_out, counter_1_q, multiplexer_1_out;
  wire [31:0] _1, alu_1_result, multiplexer_2_out, ram_1_data;

  main main_1 (
    .Reg2(5'b00001), .Write_Reg_num(5'b00001), .Din(multiplexer_2_out), .Write_Enable(1'b1),
    .Clock(clock_1_out), .Reg2_2(_1));  // open: Reg1_num, Reg1, s0_Value, s1_Value, s2_Value, ra_Value
  Clock clock_1 (.out(clock_1_out));
  Counter #(.width(6), .max('h3f)) counter_1 (
    .Q(counter_1_q), .clk(clock_1_out), .clr(button_1_out));  // open: load, D, count, carry
  Button button_1 (.out(button_1_out));
  Multiplexer #(.width(6), .enable("false")) multiplexer_1 (
    .in0(bit_extender_1_out), .in1(adder_1_out), .out(multiplexer_1_out), .sel(counter_1_q[0]));
  assign bit_extender_1_out = {{1{1'b0}}, counter_1_q[5:1]};  // Bit_Extender bit_extender_1
  // Probe on ram_1_data
  Comparator #(.width(6), .mode("unsigned")) comparator_1 (
    .a(counter_1_q), .b({6{1'b0}}), .eq(comparator_1_eq));  // open: gt, lt
  RAM #(.addrWidth(6), .dataWidth(32), .bus("separate")) ram_1 (
    .addr(multiplexer_1_out), .din(alu_1_result), .data(ram_1_data), .str(counter_1_q[0]), .clk(clock_1_out),
    .ld(1'b1));  // open: sel, clr
  Adder #(.width(6)) adder_1 (.a(bit_extender_1_out), .b(6'b100000), .out(adder_1_out));  // open: cin, cout
  Multiplexer #(.width(32), .enable("false")) multiplexer_2 (
    .in0(alu_1_result), .in1(ram_1_data), .out(multiplexer_2_out), .sel(comparator_1_eq));
  // Probe on _1
  // Probe on alu_1_result
  ALU alu_1 (
    .AluOP(4'b0101), .X(ram_1_data), .Result(alu_1_result), .Y(_1));  // open: Equal, Signed_Overflow, Result_2, UnSigned_Overflow

  // Notes on the sheet:
  //   内存值
  //   中间结果
  //   和
endmodule
