// Logisim project 嵌套中断版本1.circ as structural Verilog: 17 circuits, main circuit main
module main (
);

  wire \_1号中断_out , \_1按键 , \_1灯 , \_2按键 , \_2灯 , \_3按键 , \_3灯 , ALUSrc, and_4_out, and_7_out, beq, bne,
       Branch, clk, clkforcpu, ComBranch, d_ff_1_q, Equal, HaflWord, Halt, I, IR1, isCop, isCopread,
       isCopWrite, isCopwrite_t, isreset, isTrap, J, Jal, Jr, Jump, MemRead, MemtoReg, MemWrite,
       multiplexer_1_out, not_1_out, or_1_out, R, RegDst, RegWrite, rs_is0, Shift, syscall, Unsigned, \有中断等待 ;
  wire [1:0] cause_t;
  wire [2:0] PC_q_3;
  wire [3:0] ALUOp;
  wire [4:0] multiplexer_3_out, multiplexer_4_out, rd, rs, rt;
  wire [9:0] PC_q_2;
  wire [28:0] PC_q;
  wire [31:0] adder_1_out, adder_2_out, adder_3_out, alures, BadAddr, Badaddr1, bit_extender_1_out,
       bit_extender_2_out, bit_extender_3_out, bit_extender_4_out, Cause, cnt, counter_4_q, data2reg, datain,
       ge_data_in, Icnt, IE, IR1InstructionOut, Jcnt, main_1_p10, multiplexer_7_out, multiplexer_12_out,
       multiplexer_13_out, multiplexer_14_out, n3roms_for_trap_prog_1_ie, PC, PCin, ra, ram_1_data,
       ram_2_data, Rcnt, s0, s1, shifter_1_out, trapNo, x, y;

  Register #(.width(32)) u_PC (
    .D(PCin), .en(or_1_out), .Q({PC_q_3, PC_q[28:12], PC_q_2, PC_q[1:0]}), .clk(clk));  // open: clr
  or or_1 (or_1_out, not_1_out, \有中断等待 );
  not not_1 (not_1_out, Halt);
  Clock clock_1 (.out(clk));
  Adder #(.width(32)) adder_1 (
    .a(32'h4), .b({PC_q_3, PC_q[28:12], PC_q_2, PC_q[1:0]}), .out(adder_1_out));  // open: cin, cout
  Multiplexer #(.enable("false")) multiplexer_1 (.in0(clk), .in1(1'b0), .out(multiplexer_1_out), .sel(Halt));
  and and_1 (clkforcpu, multiplexer_1_out, ~IR1);  // AND_Gate
  Counter #(.width(32), .max('hffffffff)) u_R (.count(J), .Q(Jcnt), .clk(clk));  // open: load, D, carry, clr
  or or_2 (\有中断等待 , \_1灯 , \_2灯 , \_3灯 );
  _3Roms_for_trap_prog u_3roms_for_trap_prog_1 (.addr(PC_q_2), .intNo(PC_q_3[1:0]), .IE(n3roms_for_trap_prog_1_ie));
  Counter #(.width(32), .max('hffffffff)) counter_1 (.count(R), .Q(Rcnt), .clk(clk));  // open: load, D, carry, clr
  CP0 cp0_1 (
    .eret(isreset), .clk(clk), .no1(\_1按键 ), .\_1号灯 (\_1灯 ), .no2(\_2按键 ), .\_2号灯 (\_2灯 ), .no3(\_3按键 ),
    .\_3号灯 (\_3灯 ), .IEin(ge_data_in), .PCin(PC), .cause(cause_t), .PCout(PCin), .IE(IE),
    .CIE(IR1InstructionOut[12:11]), .BadAddr1(Badaddr1), .isWrite(isCopWrite));
  RAM #(.addrWidth(10), .dataWidth(32)) ram_1 (.addr(PC_q_2), .data(ram_1_data));  // open: sel, clk, ld, clr
  Multiplexer #(.width(32), .enable("false")) multiplexer_2 (
    .in0(ram_1_data), .in1(n3roms_for_trap_prog_1_ie), .out(IR1InstructionOut), .sel(PC_q_3[2]));
  Adder #(.width(32)) adder_2 (
    .a(32'h4), .b({PC_q_3, PC_q[28:12], PC_q_2, PC_q[1:0]}), .out(adder_2_out));  // open: cin, cout
  Counter #(.width(32), .max('hffffffff)) counter_2 (.count(I), .Q(Icnt), .clk(clk));  // open: load, D, carry, clr
  and and_2 (Halt, syscall, Equal);
  Multiplexer #(.width(5), .enable("false")) multiplexer_3 (
    .in0(IR1InstructionOut[20:16]), .in1(IR1InstructionOut[15:11]), .out(multiplexer_3_out), .sel(RegDst));
  Counter #(.width(32), .max('hffffffff)) counter_3 (.count(1'b1), .Q(cnt), .clk(clk));  // open: load, D, carry, clr
  ROM #(.addrWidth(10), .dataWidth(32)) rom_1 ();  // open: addr, data, sel
  D_Flip_Flop d_ff_1 (.clk(Halt), .D(1'b1), .Q(d_ff_1_q), .preset(1'b0), .reset(isTrap));  // open: Qn, en
  Multiplexer #(.width(5), .enable("false")) multiplexer_4 (
    .in0(IR1InstructionOut[25:21]), .in1(5'b00010), .out(multiplexer_4_out), .sel(syscall));
  Multiplexer #(.width(5), .enable("false")) multiplexer_5 (
    .in0(IR1InstructionOut[20:16]), .in1(5'b00100), .out(rt), .sel(syscall));
  Multiplexer #(.width(5), .enable("false")) multiplexer_6 (
    .in0(multiplexer_3_out), .in1({5{1'b1}}), .out(rd), .sel(Jal));
  assign bit_extender_1_out = {{27{1'b0}}, IR1InstructionOut[10:6]};  // Bit_Extender bit_extender_1
  assign bit_extender_2_out = {{16{IR1InstructionOut[15]}}, IR1InstructionOut[15:0]};  // Bit_Extender bit_extender_2
  Multiplexer #(.width(32), .enable("false")) multiplexer_7 (
    .in0(bit_extender_2_out), .in1(bit_extender_3_out), .out(multiplexer_7_out), .sel(Unsigned));
  assign bit_extender_3_out = {{16{1'b0}}, IR1InstructionOut[15:0]};  // Bit_Extender bit_extender_3
  // Probe on {adder_1_out[31:28], IR1InstructionOut[25:0], 2'b00}
  Multiplexer #(.width(5), .enable("false")) multiplexer_8 (
    .in0(multiplexer_4_out), .in1({5{1'b1}}), .out(rs), .sel(Jr));
  D_Flip_Flop d_ff_2 (.clk(clk), .D(d_ff_1_q), .preset(1'b0), .reset(isreset));  // open: Q, Qn, en
  Multiplexer #(.width(32), .enable("false")) multiplexer_9 (
    .in0(multiplexer_13_out), .in1(adder_2_out), .out(datain), .sel(Jal));
  // Probe on Icnt
  // Probe on Rcnt
  // Probe on Jcnt
  // Probe on cnt
  // RegisterFile registerfile_1: pin names not known; wires that end beside it: data2reg, clk, RegWrite, rd, rs, rt
  and and_3 (isCopWrite, isCop, and_4_out);
  and and_4 (and_4_out, ~rs[0], ~rs[1], rs[2], ~rs[3], ~rs[4]);  // AND_Gate
  Control_unit control_unit_1 (
    .in_1(IR1InstructionOut), .J_type(J), .MemWrite(MemWrite), .MemRead(MemRead), .MemtoReg(MemtoReg),
    .AluSrc(ALUSrc), .RegWrite(RegWrite), .syscall(syscall), .shift(Shift), .\unsigned (Unsigned), .jr(Jr),
    .jal(Jal), .jump(Jump), .I_type(I), .R_type(R), .RegDst(RegDst), .beq(beq), .bne(bne), .ALUOp(ALUOp),
    .isHalf(HaflWord), .bltz(ComBranch), .isCop(isCop), .isCopread(rs_is0));
  // ACM1401_U201414697_朱谷才_regfile_main main_1: pin names not known; wires that end beside it: rs, rt, rd, s0, data2reg, s1, RegWrite, clk, ra, main_1_p10, ge_data_in
  // Probe on main_1_p10
  // Probe on ge_data_in
  and and_5 (isCopread, isCop, rs_is0);
  // Probe on s0
  // Probe on s1
  // Probe on rs
  // Probe on rt
  // Probe on rd
  // Probe on ra
  Shifter #(.width(32)) shifter_1 (.in(multiplexer_7_out), .\dist (5'b00010), .out(shifter_1_out));
  // Probe on ALUOp
  Adder #(.width(32)) adder_3 (.a(adder_1_out), .b(shifter_1_out), .out(adder_3_out));  // open: cin, cout
  branch_decoder branch_decoder_1 (
    .beq(beq), .Equal(Equal), .bne(bne), .true(alures[0]), .nEqualComBranch(ComBranch), .Branch(Branch));
  Multiplexer #(.width(32), .enable("false")) multiplexer_10 (.in0(main_1_p10), .in1(ge_data_in), .out(x), .sel(Shift));
  Multiplexer #(.width(32), .enable("false")) multiplexer_11 (
    .in0(datain), .in1(multiplexer_12_out), .out(data2reg), .sel(isCopread));
  Multiplexer #(.select(2), .width(32), .enable("false")) multiplexer_12 (
    .in1(Badaddr1), .in2(IE), .out(multiplexer_12_out), .sel(IR1InstructionOut[12:11]));  // open: in0, in3
  ALU alu_1 (
    .AluOP(ALUOp), .X(x), .Equal(Equal), .Result(alures), .Y(y));  // open: Signed_Overflow, Result_2, UnSigned_Overflow
  ALUSrc_Mux alusrc_mux_1 (
    .R2(ge_data_in), .extend(multiplexer_7_out), .shift_2(bit_extender_1_out), .output2AluY(y),
    .ALUSrc(ALUSrc), .Shift(Shift), .ComBranch(ComBranch), .syscall(syscall));
  Multiplexer #(.width(32), .enable("false")) multiplexer_13 (
    .in0(alures), .in1(multiplexer_14_out), .out(multiplexer_13_out), .sel(MemtoReg));
  // Probe on x
  // Probe on y
  // Probe on alures
  // Probe on alures
  // Probe on data2reg
  jump_dst_mux jump_dst_mux_1 (
    .sequencial_dst(adder_1_out), .Branch_dst(adder_3_out),
    .Jump_dst({adder_1_out[31:28], IR1InstructionOut[25:0], 2'b00}), .Jr_dst(main_1_p10), .PC_dst(PC),
    .Branch(Branch), .Jump(Jump), .Jr(Jr));
  Multiplexer #(.width(32), .enable("false")) multiplexer_14 (
    .in0(ram_2_data), .in1(bit_extender_4_out), .out(multiplexer_14_out), .sel(HaflWord));
  Button \_1号中断  (.out(\_1号中断_out ));
  and and_6 (isCopwrite_t, isCop, ~rs_is0);  // AND_Gate
  Hex_Digit_Display hex_digit_display_1 (.value(counter_4_q[31:28]));  // open: dp
  Counter #(.width(32), .max('hffffffff), .ongoal("load")) counter_4 (
    .load(syscall), .D(ge_data_in), .count(1'b0), .Q(counter_4_q), .clk(clk));  // open: carry, clr
  Register #(.width(32)) u_BadAddr (.D(PC), .en(IR1), .Q(BadAddr), .clk(clk));  // open: clr
  interrupt interrupt_1 (.clkin(clk), .\_1号中断 (\_1号中断_out ), .\同步清零信号 (IR1), .\与中断屏蔽位与 (IR1));  // open: 中断等待灯
  Hex_Digit_Display hex_digit_display_2 (.value(counter_4_q[23:20]));  // open: dp
  Hex_Digit_Display hex_digit_display_3 (.value(counter_4_q[27:24]));  // open: dp
  RAM #(.addrWidth(10), .dataWidth(32), .bus("separate")) ram_2 (
    .addr(alures[11:2]), .din(ge_data_in), .data(ram_2_data), .str(MemWrite), .clk(clk), .ld(MemRead));  // open: sel, clr
  // Probe on BadAddr
  D_Flip_Flop d_ff_3 (.clk(IR1), .D(1'b1), .Q(isTrap), .reset(isreset));  // open: Qn, preset, en
  and and_7 (and_7_out, ~IR1InstructionOut[5], IR1InstructionOut[4], IR1InstructionOut[3], ~IR1InstructionOut[2], ~IR1InstructionOut[1], ~IR1InstructionOut[0]);  // AND_Gate
  Hex_Digit_Display hex_digit_display_4 (.value(counter_4_q[19:16]));  // open: dp
  Hex_Digit_Display hex_digit_display_5 (.value(counter_4_q[15:12]));  // open: dp
  Button _1 (.out(\_1按键 ));
  Button _2 (.out(\_2按键 ));
  Button _3 (.out(\_3按键 ));
  assign bit_extender_4_out = {{16{ram_2_data[15]}}, ram_2_data[15:0]};  // Bit_Extender bit_extender_4
  and and_8 (isreset, and_7_out, isCop);
  Hex_Digit_Display hex_digit_display_6 (.value(counter_4_q[11:8]));  // open: dp
  Hex_Digit_Display hex_digit_display_7 (.value(counter_4_q[7:4]));  // open: dp
  LED led_1 (.in(\_1灯 ));
  LED led_2 (.in(\_2灯 ));
  LED led_3 (.in(\_3灯 ));
  // Probe on cause_t
  Hex_Digit_Display hex_digit_display_8 (.value(counter_4_q[3:0]));  // open: dp
  Register #(.width(32)) casuse (.D(trapNo), .en(IR1), .Q(Cause), .clk(clk));  // open: clr

  // Other names for the same wires on the sheet: selno[1:0] = IR1InstructionOut[12:11]; true = alures[0]; clkin = clk;
  //   IR1清零 = IR1

  // Notes on the sheet:
  //   rs
  //   rt
  //   rd
  //   contents of rom_1 (hex, n*v repeats v):
  //   401a0800 401b1000 afba0000 23bd0004 afbb0000 23bd0004 201a0008 409a1000 201a0003 409a1000 afa40000
  //   23bd0004 afa50000 23bd0004 afa60000 23bd0004 afa70000 23bd0004 afb00000 23bd0004 afb10000 23bd0004
  //   afb20000 23bd0004 afb30000 23bd0004 afb40000 23bd0004 afb50000 23bd0004 afb60000 23bd0004 afb70000
  //   23bd0004 3a0f020 20160003 20140006 20150001 168020 108100 2149825 132020 20020022 c 1600fffa 295a022
  //   1680fff7 23bdfffc 8fb70000 23bdfffc 8fb60000 23bdfffc 8fb50000 23bdfffc 8fb40000 23bdfffc 8fb30000
  //   23bdfffc 8fb20000 23bdfffc 8fb10000 23bdfffc 8fb00000 23bdfffc 8fa70000 23bdfffc 8fa60000 23bdfffc
  //   8fa50000 23bdfffc 8fa40000 23bdfffc 8fbb0000 23bdfffc 8fba0000 40041000 409a0800 375b0008 409b1000
  //   20020022 c 42000018
  //   顺序地址
  //   直接跳转地址
  //   条件跳转
  //   寄存器跳转
  //   $a0
endmodule

module jump_dst_mux (
  input  [31:0] sequencial_dst,
  input  [31:0] Branch_dst,
  input  Branch,
  input  Jump,
  input  Jr,
  input  [31:0] Jump_dst,
  input  [31:0] Jr_dst,
  output [31:0] PC_dst
);

  wire [31:0] multiplexer_1_out, multiplexer_2_out;

  Multiplexer #(.width(32), .enable("false")) multiplexer_1 (
    .in0(sequencial_dst), .in1(Branch_dst), .out(multiplexer_1_out), .sel(Branch));
  Multiplexer #(.width(32), .enable("false")) multiplexer_2 (
    .in0(multiplexer_1_out), .in1(Jump_dst), .out(multiplexer_2_out), .sel(Jump));
  Multiplexer #(.width(32), .enable("false")) multiplexer_3 (
    .in0(multiplexer_2_out), .in1(Jr_dst), .out(PC_dst), .sel(Jr));
endmodule

module ALUSrc_Mux (
  input  [31:0] R2,
  input  ALUSrc,
  input  Shift,
  input  ComBranch,
  input  syscall,
  input  [31:0] extend,
  input  [31:0] shift_2,
  output [31:0] output2AluY
);

  wire [31:0] multiplexer_1_out, multiplexer_2_out, multiplexer_3_out;

  Multiplexer #(.width(32), .enable("false")) multiplexer_1 (
    .in0(R2), .in1(extend), .out(multiplexer_1_out), .sel(ALUSrc));
  Multiplexer #(.width(32), .enable("false")) multiplexer_2 (
    .in0(multiplexer_1_out), .in1(shift_2), .out(multiplexer_2_out), .sel(Shift));
  Multiplexer #(.width(32), .enable("false")) multiplexer_3 (
    .in0(multiplexer_2_out), .in1({32{1'b0}}), .out(multiplexer_3_out), .sel(ComBranch));
  Multiplexer #(.width(32), .enable("false")) multiplexer_4 (
    .in0(multiplexer_3_out), .in1(32'ha), .out(output2AluY), .sel(syscall));
endmodule

module branch_decoder (
  input  beq,
  input  Equal,
  input  bne,
  input  true,
  input  nEqualComBranch,
  output Branch
);

  wire and_1_out, and_2_out, and_3_out;

  and and_1 (and_1_out, beq, Equal);
  and and_2 (and_2_out, ~Equal, bne);  // AND_Gate
  and and_3 (and_3_out, ~Equal, true, nEqualComBranch);  // AND_Gate
  or or_1 (Branch, and_1_out, and_2_out, and_3_out);
endmodule

module interrupt (
  input  clkin,
  input  \_1号中断 ,
  input  \同步清零信号 ,
  output \与中断屏蔽位与 ,
  output \中断等待灯 
);

  wire and_1_out, d_ff_1_q, or_2_out;

  D_Flip_Flop d_ff_1 (.clk(\_1号中断 ), .D(1'b1), .Q(d_ff_1_q), .reset(\与中断屏蔽位与 ));  // open: Qn, preset, en
  or or_1 (\中断等待灯 , \与中断屏蔽位与 , d_ff_1_q);
  or or_2 (or_2_out, d_ff_1_q, \与中断屏蔽位与 );
  and and_1 (and_1_out, or_2_out, ~\同步清零信号 );  // AND_Gate
  D_Flip_Flop IR1 (.clk(clkin), .D(and_1_out), .Q(\与中断屏蔽位与 ));  // open: Qn, preset, en, reset

  // Notes on the sheet:
  //   中断信号采样参考电路
  //   Reset 
endmodule

module CP0 (
  input  isWrite,
  input  [1:0] CIE,
  input  eret,
  input  no1,
  input  clk,
  input  no2,
  input  no3,
  input  [31:0] IEin,
  input  [31:0] PCin,
  output [31:0] BadAddr1,
  output [1:0] cause,
  output \_1号灯 ,
  output \_2号灯 ,
  output \_3号灯 ,
  output [31:0] IE,
  output [31:0] PCout
);

  wire and_1_out, and_3_out, and_4_out, and_5_out, and_8_out, \interrupt_1_与中断屏蔽位与 , \interrupt_2_与中断屏蔽位与 ,
       \interrupt_3_与中断屏蔽位与 , \IR1清零 , \IR2清零 , \IR3清零 , istrap, nmb, nor_1_out, not_1_out, not_2_out,
       not_3_out, notrap, or_1_out, or_2_out, or_4_out, priority_encoder_1_gs, write2Epc;
  wire [1:0] priority_encoder_1_out, trapNo;
  wire [31:0] _2IE, and_7_out, inIE, mask, multiplexer_4_out, multiplexer_5_out, multiplexer_6_out;

  // Probe on PCin
  interrupt interrupt_1 (
    .clkin(clk), .\_1号中断 (no1), .\中断等待灯 (\_1号灯 ), .\同步清零信号 (\IR1清零 ), .\与中断屏蔽位与 (\interrupt_1_与中断屏蔽位与 ));
  interrupt interrupt_2 (
    .clkin(clk), .\_1号中断 (no3), .\中断等待灯 (\_3号灯 ), .\同步清零信号 (\IR3清零 ), .\与中断屏蔽位与 (\interrupt_2_与中断屏蔽位与 ));
  not not_1 (not_1_out, IE[0]);
  not not_2 (not_2_out, IE[1]);
  not not_3 (not_3_out, IE[2]);
  interrupt interrupt_3 (
    .clkin(clk), .\_1号中断 (no2), .\中断等待灯 (\_2号灯 ), .\同步清零信号 (\IR2清零 ), .\与中断屏蔽位与 (\interrupt_3_与中断屏蔽位与 ));
  and and_1 (and_1_out, isWrite, CIE[1]);
  and and_2 (write2Epc, isWrite, CIE[0]);
  and and_3 (and_3_out, \interrupt_1_与中断屏蔽位与 , not_1_out);
  and and_4 (and_4_out, \interrupt_3_与中断屏蔽位与 , not_2_out);
  and and_5 (and_5_out, \interrupt_2_与中断屏蔽位与 , not_3_out);
  or or_1 (or_1_out, istrap, eret);
  Priority_Encoder #(.select(2)) priority_encoder_1 (
    .in0(1'b0), .in1(and_3_out), .in2(and_4_out), .in3(and_5_out), .out(priority_encoder_1_out),
    .gs(priority_encoder_1_gs), .en_out(notrap));  // open: en_in
  or or_2 (or_2_out, and_1_out, istrap, eret);
  Register #(.width(32)) u_IE (.D(inIE), .en(or_2_out), .Q(IE), .clk(clk));  // open: clr
  assign _2IE = IEin | mask;  // OR_Gate or_3, 32 bits wide
  Register #(.width(2)) casuse (.D(trapNo), .en(or_1_out), .Q(cause), .clk(clk));  // open: clr
  and and_6 (istrap, priority_encoder_1_gs, ~IE[3]);  // AND_Gate
  nor nor_1 (nor_1_out, cause[0], cause[1]);
  Multiplexer #(.width(2), .disabled(0), .enable("false")) multiplexer_1 (
    .in0(priority_encoder_1_out), .in1(2'b00), .out(trapNo), .sel(notrap));
  Decoder #(.select(2), .disabled(0), .enable("false")) decoder_1 (
    .out1(\IR1清零 ), .out2(\IR2清零 ), .out3(\IR3清零 ), .sel(cause));  // open: out0
  Multiplexer #(.width(32), .enable("false")) multiplexer_2 (.in0({32{1'b0}}), .in1(32'h8), .out(mask), .sel(istrap));
  assign and_7_out = IE & 32'h7;  // AND_Gate and_7, 32 bits wide
  Multiplexer #(.width(32), .disabled(0), .enable("false")) multiplexer_3 (
    .in0(_2IE), .in1(and_7_out), .out(inIE), .sel(eret));
  Multiplexer #(.width(32), .disabled(0), .enable("false")) multiplexer_4 (
    .in0(PCin), .in1(IEin), .out(multiplexer_4_out), .sel(write2Epc));
  interrupt interrupt_4 (.clkin(clk), .\_1号中断 (istrap), .\同步清零信号 (eret), .\与中断屏蔽位与 (nmb));  // open: 中断等待灯
  Multiplexer #(.select(2), .width(32), .disabled(0), .enable("false")) multiplexer_5 (
    .in0(PCin), .in1(32'h80000000), .in2(32'ha0000000), .in3(32'hc0000000), .out(multiplexer_5_out),
    .sel(trapNo));
  or or_4 (or_4_out, and_8_out, write2Epc);
  Multiplexer #(.width(32), .disabled(0), .enable("false")) multiplexer_6 (
    .in0(PCin), .in1(multiplexer_5_out), .out(multiplexer_6_out), .sel(istrap));
  Multiplexer #(.width(32), .disabled(0), .enable("false")) multiplexer_7 (
    .in0(multiplexer_6_out), .in1(BadAddr1), .out(PCout), .sel(eret));
  Register #(.width(32)) BadAddr (.D(multiplexer_4_out), .en(or_4_out), .Q(BadAddr1), .clk(clk));  // open: clr
  // Probe on BadAddr1
  D_Flip_Flop d_ff_1 (.clk(write2Epc), .D(1'b1));  // open: Q, Qn, preset, en, reset
  and and_8 (and_8_out, istrap, ~eret);  // AND_Gate

  // Other names for the same wires on the sheet: BadAddr[31:0] = BadAddr1; clkin = clk; PC[31:0] = PCin;
  //   regdatain[31:0] = IEin
endmodule

module Control_unit (
  input  [31:0] in_1,
  output MemWrite,
  output J_type,
  output I_type,
  output R_type,
  output MemRead,
  output RegDst,
  output jump,
  output MemtoReg,
  output AluSrc,
  output beq,
  output bne,
  output RegWrite,
  output shift,
  output syscall,
  output \unsigned ,
  output jr,
  output jal,
  output isHalf,
  output bltz,
  output [3:0] ALUOp,
  output isCop,
  output isCopread
);

  wire add, addi, addiu, addu, \and , and_3_out, and_7_out, and_8_out, andi, COM, com_branch, isAdd, isAnd,
       isOr, isSub, isXor, jump_t, lw, \nor , not_1_out, \or , or_4_out, or_5_out, ori, r_type2_1_sllv,
       r_type2_1_srav, r_type2_1_srlv, shamt_is_0, sll, slt, slti, sltu, sra, srl, sub, subu;
  wire [3:0] multiplexer_1_out, multiplexer_2_out, multiplexer_3_out, multiplexer_4_out, multiplexer_5_out,
       multiplexer_6_out, multiplexer_7_out, multiplexer_8_out, multiplexer_9_out;

  or or_1 (MemRead, lw, isHalf);
  nor nor_1 (shamt_is_0, in_1[6], in_1[7], in_1[8], in_1[9], in_1[10]);
  and and_1 (isHalf, in_1[31], ~in_1[30], ~in_1[29], ~in_1[28], ~in_1[27], in_1[26]);  // AND_Gate
  and and_2 (com_branch, ~in_1[31], ~in_1[30], ~in_1[29], ~in_1[28], ~in_1[27], in_1[26]);  // AND_Gate
  and and_3 (and_3_out, ~in_1[16], ~in_1[17], ~in_1[18], ~in_1[19], ~in_1[20]);  // AND_Gate
  and and_4 (isCopread, ~in_1[21], ~in_1[22], ~in_1[23], ~in_1[24], ~in_1[25]);  // AND_Gate
  nor nor_2 (R_type, in_1[26], in_1[27], in_1[28], in_1[29], in_1[30], in_1[31]);
  and and_5 (bltz, com_branch, and_3_out);
  and and_6 (isCop, ~in_1[31], in_1[30], ~in_1[29], ~in_1[28], ~in_1[27], ~in_1[26]);  // AND_Gate
  I_type i_type_1 (
    .op5(in_1[31]), .op4(in_1[30]), .op3(in_1[29]), .op2(in_1[28]), .op1(in_1[27]), .op0(in_1[26]),
    .addi(addi), .addiu(addiu), .andi(andi), .ori(ori), .xori(isXor), .lw(lw), .sw(MemWrite), .beq(beq),
    .bne(bne), .slti(slti));  // open: lui, sltiu
  J_type j_type_1 (
    .op5(in_1[31]), .op4(in_1[30]), .op3(in_1[29]), .op2(in_1[28]), .op1(in_1[27]), .op0(in_1[26]),
    .j(jump_t), .jal(jal));
  R_type2 r_type2_1 (
    .func5(in_1[5]), .func4(in_1[4]), .sra(sra), .func3(in_1[3]), .func2(in_1[2]), .func1(in_1[1]),
    .sllv(r_type2_1_sllv), .func0(in_1[0]), .opiszero(R_type), .srlv(r_type2_1_srlv), .srav(r_type2_1_srav),
    .jr(jr), .syscall(syscall));
  R_type r_type_1 (
    .func5(in_1[5]), .func4(in_1[4]), .add(add), .func3(in_1[3]), .func2(in_1[2]), .func1(in_1[1]),
    .addu(addu), .func0(in_1[0]), .opiszero(R_type), .sub(sub), .subu(subu), .\and (\and ), .\or (\or ),
    .\nor (\nor ), .slt(slt), .sltu(sltu), .sll(sll), .srl(srl));  // open: xor
  or or_2 (J_type, jump_t, jal);
  Multiplexer #(.width(4), .enable("false")) multiplexer_1 (
    .in0(4'b0000), .in1(4'b0001), .out(multiplexer_1_out), .sel(sra));
  or or_3 (isAnd, \and , andi);
  or or_4 (or_4_out, addi, jal, addiu, andi);
  or or_5 (or_5_out, ori, MemRead, isXor, slti);
  and and_7 (and_7_out, isCop, isCopread);
  and and_8 (and_8_out, R_type, ~jr, ~syscall);  // AND_Gate
  Multiplexer #(.width(4), .enable("false")) multiplexer_2 (
    .in0(multiplexer_1_out), .in1(4'b0010), .out(multiplexer_2_out), .sel(srl));
  or or_6 (RegWrite, or_4_out, or_5_out, and_7_out, and_8_out);
  Multiplexer #(.width(4), .enable("false")) multiplexer_3 (
    .in0(multiplexer_2_out), .in1(4'b0101), .out(multiplexer_3_out), .sel(isAdd));
  Multiplexer #(.width(4), .enable("false")) multiplexer_4 (
    .in0(multiplexer_3_out), .in1(4'b0110), .out(multiplexer_4_out), .sel(isSub));
  or or_7 (COM, slt, bltz, slti);
  Multiplexer #(.width(4), .enable("false")) multiplexer_5 (
    .in0(multiplexer_4_out), .in1(4'b0111), .out(multiplexer_5_out), .sel(isAnd));
  Multiplexer #(.width(4), .enable("false")) multiplexer_6 (
    .in0(multiplexer_5_out), .in1(4'b1000), .out(multiplexer_6_out), .sel(isOr));
  or or_8 (isAdd, lw, addu, addiu, addi, add, MemWrite);
  or or_9 (shift, sll, srl, sra);
  Multiplexer #(.width(4), .enable("false")) multiplexer_7 (
    .in0(multiplexer_6_out), .in1(4'b1001), .out(multiplexer_7_out), .sel(isXor));
  Multiplexer #(.width(4), .enable("false")) multiplexer_8 (
    .in0(multiplexer_7_out), .in1(4'b1010), .out(multiplexer_8_out), .sel(\nor ));
  Multiplexer #(.width(4), .enable("false")) multiplexer_9 (
    .in0(multiplexer_8_out), .in1(4'b1011), .out(multiplexer_9_out), .sel(COM));
  or or_10 (isOr, ori, \or );
  Multiplexer #(.width(4), .enable("false")) multiplexer_10 (
    .in0(multiplexer_9_out), .in1(4'b1100), .out(ALUOp), .sel(sltu));
  or or_11 (isSub, sub, subu);
  not not_1 (not_1_out, R_type);
  or or_12 (\unsigned , addiu, addu, subu, sltu);
  and and_9 (I_type, not_1_out, ~jal, ~jump_t);  // AND_Gate
  and and_10 (AluSrc, I_type, ~beq, ~bne);  // AND_Gate

  assign jump = J_type;
  assign MemtoReg = MemRead;
  assign RegDst = R_type;

  // Other names for the same wires on the sheet: func[5:0] = in_1[5:0]; shamt[4:0] = in_1[10:6];
  //   rd[4:0] = in_1[15:11]; rt[4:0] = in_1[20:16]; rs[4:0] = in_1[25:21]; op[5:0] = in_1[31:26]; isLoad = MemRead;
  //   lh = isHalf; op_is_0 = R_type; sw = MemWrite; xori = isXor
endmodule

module Control_Unit (
  input  [31:0] in_1,
  output addi,
  output sra,
  output addiu,
  output andi,
  output ori,
  output lw,
  output sw,
  output beq,
  output bne,
  output slti,
  output jr,
  output syscall,
  output add,
  output addu,
  output sub,
  output j,
  output \and ,
  output \or ,
  output \nor ,
  output slt,
  output jal,
  output sltu,
  output sll,
  output srl
);

  wire i_type_1_lui, i_type_1_sltiu, i_type_1_xori, op_is_0, r_type2_1_sllv, r_type2_1_srav, r_type2_1_srlv,
       shamt_is_0;

  nor nor_1 (shamt_is_0, in_1[6], in_1[7], in_1[8], in_1[9], in_1[10]);
  nor nor_2 (op_is_0, in_1[26], in_1[27], in_1[28], in_1[29], in_1[30], in_1[31]);
  I_type i_type_1 (
    .op5(in_1[31]), .op4(in_1[30]), .op3(in_1[29]), .op2(in_1[28]), .op1(in_1[27]), .op0(in_1[26]),
    .addi(addi), .addiu(addiu), .andi(andi), .ori(ori), .xori(i_type_1_xori), .lui(i_type_1_lui), .lw(lw),
    .sw(sw), .beq(beq), .bne(bne), .slti(slti), .sltiu(i_type_1_sltiu));
  J_type j_type_1 (
    .op5(in_1[31]), .op4(in_1[30]), .op3(in_1[29]), .op2(in_1[28]), .op1(in_1[27]), .op0(in_1[26]), .j(j),
    .jal(jal));
  R_type2 r_type2_1 (
    .func5(in_1[5]), .func4(in_1[4]), .sra(sra), .func3(in_1[3]), .func2(in_1[2]), .func1(in_1[1]),
    .sllv(r_type2_1_sllv), .func0(in_1[0]), .opiszero(op_is_0), .srlv(r_type2_1_srlv), .srav(r_type2_1_srav),
    .jr(jr), .syscall(syscall));
  R_type r_type_1 (
    .func5(in_1[5]), .func4(in_1[4]), .add(add), .func3(in_1[3]), .func2(in_1[2]), .func1(in_1[1]),
    .addu(addu), .func0(in_1[0]), .opiszero(op_is_0), .sub(sub), .\and (\and ), .\or (\or ), .\nor (\nor ),
    .slt(slt), .sltu(sltu), .sll(sll), .srl(srl));  // open: subu, xor

  // Other names for the same wires on the sheet: func[5:0] = in_1[5:0]; shamt[4:0] = in_1[10:6];
  //   rd[4:0] = in_1[15:11]; rt[4:0] = in_1[20:16]; rs[4:0] = in_1[25:21]; op[5:0] = in_1[31:26]
endmodule

module I_type (
  input  op5,
  input  op4,
  input  op3,
  input  op2,
  input  op1,
  input  op0,
  output addi,
  output addiu,
  output andi,
  output ori,
  output xori,
  output lui,
  output lw,
  output sw,
  output beq,
  output bne,
  output slti,
  output sltiu
);

  wire not_1_out, not_2_out, not_3_out, not_4_out, not_5_out, not_6_out, not_7_out, not_8_out, not_9_out,
       not_10_out, not_11_out, not_12_out, not_13_out, not_14_out, not_15_out, not_16_out, not_17_out,
       not_18_out, not_19_out, not_20_out, not_21_out, not_22_out, not_23_out, not_24_out, not_25_out,
       not_26_out, not_27_out, not_28_out, not_29_out, not_30_out, not_31_out, not_32_out, not_33_out,
       not_34_out, not_35_out, not_36_out, not_37_out, not_38_out, not_39_out, not_40_out, not_41_out,
       not_42_out;

  not not_1 (not_1_out, op5);
  not not_2 (not_2_out, op4);
  not not_3 (not_3_out, op2);
  not not_4 (not_4_out, op1);
  not not_5 (not_5_out, op0);
  not not_6 (not_6_out, op5);
  not not_7 (not_7_out, op4);
  not not_8 (not_8_out, op2);
  not not_9 (not_9_out, op1);
  not not_10 (not_10_out, op5);
  not not_11 (not_11_out, op4);
  not not_12 (not_12_out, op1);
  not not_13 (not_13_out, op0);
  not not_14 (not_14_out, op5);
  not not_15 (not_15_out, op4);
  not not_16 (not_16_out, op1);
  not not_17 (not_17_out, op5);
  not not_18 (not_18_out, op4);
  not not_19 (not_19_out, op0);
  not not_20 (not_20_out, op5);
  not not_21 (not_21_out, op4);
  not not_22 (not_22_out, op4);
  not not_23 (not_23_out, op3);
  not not_24 (not_24_out, op2);
  not not_25 (not_25_out, op4);
  not not_26 (not_26_out, op2);
  not not_27 (not_27_out, op5);
  not not_28 (not_28_out, op4);
  not not_29 (not_29_out, op3);
  not not_30 (not_30_out, op1);
  not not_31 (not_31_out, op0);
  not not_32 (not_32_out, op5);
  not not_33 (not_33_out, op4);
  not not_34 (not_34_out, op3);
  not not_35 (not_35_out, op1);
  not not_36 (not_36_out, op5);
  not not_37 (not_37_out, op4);
  not not_38 (not_38_out, op2);
  not not_39 (not_39_out, op0);
  not not_40 (not_40_out, op5);
  not not_41 (not_41_out, op4);
  not not_42 (not_42_out, op2);
  and and_1 (addi, not_1_out, not_2_out, op3, not_3_out, not_4_out, not_5_out);
  and and_2 (addiu, not_6_out, not_7_out, op3, not_8_out, not_9_out, op0);
  and and_3 (andi, not_10_out, not_11_out, op3, op2, not_12_out, not_13_out);
  and and_4 (ori, not_14_out, not_15_out, op3, op2, not_16_out, op0);
  and and_5 (xori, not_17_out, not_18_out, op3, op2, op1, not_19_out);
  and and_6 (lui, not_20_out, not_21_out, op3, op2, op1, op0);
  and and_7 (lw, op5, not_22_out, not_23_out, not_24_out, op1, op0);
  and and_8 (sw, op5, not_25_out, op3, not_26_out, op1, op0);
  and and_9 (beq, not_27_out, not_28_out, not_29_out, op2, not_30_out, not_31_out);
  and and_10 (bne, not_32_out, not_33_out, not_34_out, op2, not_35_out, op0);
  and and_11 (slti, not_36_out, not_37_out, op3, not_38_out, op1, not_39_out);
  and and_12 (sltiu, not_40_out, not_41_out, op3, not_42_out, op1, op0);
endmodule

module R_type (
  input  func5,
  input  func4,
  input  func3,
  input  func2,
  input  func1,
  input  func0,
  input  opiszero,
  output add,
  output addu,
  output sub,
  output subu,
  output \and ,
  output \or ,
  output \xor ,
  output \nor ,
  output slt,
  output sltu,
  output sll,
  output srl
);

  wire not_1_out, not_2_out, not_3_out, not_4_out, not_5_out, not_6_out, not_7_out, not_8_out, not_9_out,
       not_10_out, not_11_out, not_12_out, not_13_out, not_14_out, not_15_out, not_16_out, not_17_out,
       not_18_out, not_19_out, not_20_out, not_21_out, not_22_out, not_23_out, not_24_out, not_25_out,
       not_26_out, not_27_out, not_28_out, not_29_out, not_30_out, not_31_out, not_32_out, not_33_out,
       not_34_out, not_35_out, not_36_out, not_37_out, not_38_out, not_39_out, not_40_out, not_41_out,
       not_42_out, not_43_out, not_44_out;

  not not_1 (not_1_out, func4);
  not not_2 (not_2_out, func3);
  not not_3 (not_3_out, func2);
  not not_4 (not_4_out, func1);
  not not_5 (not_5_out, func0);
  not not_6 (not_6_out, func4);
  not not_7 (not_7_out, func3);
  not not_8 (not_8_out, func2);
  not not_9 (not_9_out, func1);
  not not_10 (not_10_out, func4);
  not not_11 (not_11_out, func3);
  not not_12 (not_12_out, func2);
  not not_13 (not_13_out, func0);
  not not_14 (not_14_out, func4);
  not not_15 (not_15_out, func3);
  not not_16 (not_16_out, func2);
  not not_17 (not_17_out, func4);
  not not_18 (not_18_out, func3);
  not not_19 (not_19_out, func1);
  not not_20 (not_20_out, func0);
  not not_21 (not_21_out, func4);
  not not_22 (not_22_out, func3);
  not not_23 (not_23_out, func1);
  not not_24 (not_24_out, func4);
  not not_25 (not_25_out, func3);
  not not_26 (not_26_out, func0);
  not not_27 (not_27_out, func4);
  not not_28 (not_28_out, func3);
  not not_29 (not_29_out, func4);
  not not_30 (not_30_out, func2);
  not not_31 (not_31_out, func0);
  not not_32 (not_32_out, func4);
  not not_33 (not_33_out, func2);
  not not_34 (not_34_out, func5);
  not not_35 (not_35_out, func4);
  not not_36 (not_36_out, func3);
  not not_37 (not_37_out, func2);
  not not_38 (not_38_out, func1);
  not not_39 (not_39_out, func0);
  not not_40 (not_40_out, func5);
  not not_41 (not_41_out, func4);
  not not_42 (not_42_out, func3);
  not not_43 (not_43_out, func2);
  not not_44 (not_44_out, func0);
  and and_1 (add, func5, not_1_out, not_2_out, not_3_out, not_4_out, not_5_out, opiszero);
  and and_2 (addu, func5, not_6_out, not_7_out, not_8_out, not_9_out, func0, opiszero);
  and and_3 (sub, func5, not_10_out, not_11_out, not_12_out, func1, not_13_out, opiszero);
  and and_4 (subu, func5, not_14_out, not_15_out, not_16_out, func1, func0, opiszero);
  and and_5 (\and , func5, not_17_out, not_18_out, func2, not_19_out, not_20_out, opiszero);
  and and_6 (\or , func5, not_21_out, not_22_out, func2, not_23_out, func0, opiszero);
  and and_7 (\xor , func5, not_24_out, not_25_out, func2, func1, not_26_out, opiszero);
  and and_8 (\nor , func5, not_27_out, not_28_out, func2, func1, func0, opiszero);
  and and_9 (slt, func5, not_29_out, func3, not_30_out, func1, not_31_out, opiszero);
  and and_10 (sltu, func5, not_32_out, func3, not_33_out, func1, func0, opiszero);
  and and_11 (sll, not_34_out, not_35_out, not_36_out, not_37_out, not_38_out, not_39_out, opiszero);
  and and_12 (srl, not_40_out, not_41_out, not_42_out, not_43_out, func1, not_44_out, opiszero);
endmodule

module R_type2 (
  input  func5,
  input  func4,
  input  func3,
  input  func2,
  input  func1,
  input  func0,
  input  opiszero,
  output sra,
  output sllv,
  output srlv,
  output srav,
  output jr,
  output syscall
);

  wire not_1_out, not_2_out, not_3_out, not_4_out, not_5_out, not_6_out, not_7_out, not_8_out, not_9_out,
       not_10_out, not_11_out, not_12_out, not_13_out, not_14_out, not_15_out, not_16_out, not_17_out,
       not_18_out, not_19_out, not_20_out, not_21_out, not_22_out, not_23_out, not_24_out;

  not not_1 (not_1_out, func5);
  not not_2 (not_2_out, func4);
  not not_3 (not_3_out, func3);
  not not_4 (not_4_out, func2);
  not not_5 (not_5_out, func5);
  not not_6 (not_6_out, func4);
  not not_7 (not_7_out, func3);
  not not_8 (not_8_out, func2);
  not not_9 (not_9_out, func5);
  not not_10 (not_10_out, func4);
  not not_11 (not_11_out, func3);
  not not_12 (not_12_out, func0);
  not not_13 (not_13_out, func5);
  not not_14 (not_14_out, func4);
  not not_15 (not_15_out, func3);
  not not_16 (not_16_out, func5);
  not not_17 (not_17_out, func4);
  not not_18 (not_18_out, func2);
  not not_19 (not_19_out, func1);
  not not_20 (not_20_out, func0);
  not not_21 (not_21_out, func5);
  not not_22 (not_22_out, func4);
  not not_23 (not_23_out, func1);
  not not_24 (not_24_out, func0);
  and and_1 (sra, not_1_out, not_2_out, not_3_out, not_4_out, func1, func0, opiszero);
  and and_2 (sllv, not_5_out, not_6_out, not_7_out, not_8_out, func1, func0, opiszero);
  and and_3 (srlv, not_9_out, not_10_out, not_11_out, func2, func1, not_12_out, opiszero);
  and and_4 (srav, not_13_out, not_14_out, not_15_out, func2, func1, func0, opiszero);
  and and_5 (jr, not_16_out, not_17_out, func3, not_18_out, not_19_out, not_20_out, opiszero);
  and and_6 (syscall, not_21_out, not_22_out, func3, func2, not_23_out, not_24_out, opiszero);
endmodule

module J_type (
  input  op5,
  input  op4,
  input  op3,
  input  op2,
  input  op1,
  input  op0,
  output j,
  output jal
);

  wire not_1_out, not_2_out, not_3_out, not_4_out, not_5_out, not_6_out, not_7_out, not_8_out, not_9_out;

  not not_1 (not_1_out, op5);
  not not_2 (not_2_out, op4);
  not not_3 (not_3_out, op3);
  not not_4 (not_4_out, op2);
  not not_5 (not_5_out, op0);
  not not_6 (not_6_out, op5);
  not not_7 (not_7_out, op4);
  not not_8 (not_8_out, op3);
  not not_9 (not_9_out, op2);
  and and_1 (j, not_1_out, not_2_out, not_3_out, not_4_out, op1, not_5_out);
  and and_2 (jal, not_6_out, not_7_out, not_8_out, not_9_out, op1, op0);
endmodule

module newUnit (
  input  [31:0] in_1,
  output MemWrite,
  output J_type,
  output I_type,
  output R_type,
  output MemRead,
  output RegDst,
  output AluSrc,
  output jump,
  output MemtoReg,
  output RegWrite,
  output shift,
  output syscall,
  output \unsigned ,
  output jr,
  output jal
);

  wire add, addi, addiu, addu, \and , and_2_out, andi, beq, bne, \nor , not_1_out, \or , or_1_out, or_2_out,
       ori, r_type2_1_sllv, r_type2_1_srav, r_type2_1_srlv, shamt_is_0, sll, slt, slti, sltu, sra, srl, sub;

  nor nor_1 (shamt_is_0, in_1[6], in_1[7], in_1[8], in_1[9], in_1[10]);
  nor nor_2 (R_type, in_1[26], in_1[27], in_1[28], in_1[29], in_1[30], in_1[31]);
  I_type i_type_1 (
    .op5(in_1[31]), .op4(in_1[30]), .op3(in_1[29]), .op2(in_1[28]), .op1(in_1[27]), .op0(in_1[26]),
    .addi(addi), .addiu(addiu), .andi(andi), .ori(ori), .lw(MemRead), .sw(MemWrite), .beq(beq), .bne(bne),
    .slti(slti));  // open: xori, lui, sltiu
  J_type j_type_1 (
    .op5(in_1[31]), .op4(in_1[30]), .op3(in_1[29]), .op2(in_1[28]), .op1(in_1[27]), .op0(in_1[26]), .j(jump),
    .jal(jal));
  R_type2 r_type2_1 (
    .func5(in_1[5]), .func4(in_1[4]), .sra(sra), .func3(in_1[3]), .func2(in_1[2]), .func1(in_1[1]),
    .sllv(r_type2_1_sllv), .func0(in_1[0]), .opiszero(R_type), .srlv(r_type2_1_srlv), .srav(r_type2_1_srav),
    .jr(jr), .syscall(syscall));
  R_type r_type_1 (
    .func5(in_1[5]), .func4(in_1[4]), .add(add), .func3(in_1[3]), .func2(in_1[2]), .func1(in_1[1]),
    .addu(addu), .func0(in_1[0]), .opiszero(R_type), .sub(sub), .\and (\and ), .\or (\or ), .\nor (\nor ),
    .slt(slt), .sltu(sltu), .sll(sll), .srl(srl));  // open: subu, xor
  and and_1 (J_type, jump, jal);
  or or_1 (or_1_out, addi, addiu, andi);
  or or_2 (or_2_out, ori, MemRead, slti);
  and and_2 (and_2_out, R_type, ~jr);  // AND_Gate
  or or_3 (RegWrite, or_1_out, or_2_out, and_2_out);
  or or_4 (shift, sll, srl, sra);
  not not_1 (not_1_out, R_type);
  or or_5 (\unsigned , addiu, addu, sltu);
  and and_3 (AluSrc, not_1_out, ~jal, ~jump);  // AND_Gate

  assign I_type = AluSrc;
  assign MemtoReg = MemRead;
  assign RegDst = R_type;

  // Other names for the same wires on the sheet: func[5:0] = in_1[5:0]; shamt[4:0] = in_1[10:6];
  //   rd[4:0] = in_1[15:11]; rt[4:0] = in_1[20:16]; rs[4:0] = in_1[25:21]; op[5:0] = in_1[31:26]; lw = MemRead;
  //   op_is_0 = R_type; sw = MemWrite
endmodule

module Latch (
  input  clk,
  input  syscall,
  input  equal,
  output halt
);

  wire and_1_out, d_ff_1_q;

  and and_1 (and_1_out, syscall, equal);
  D_Flip_Flop d_ff_1 (.clk(and_1_out), .D(1'b1), .Q(d_ff_1_q));  // open: Qn, preset, en, reset
  D_Flip_Flop d_ff_2 (.clk(clk), .D(d_ff_1_q), .Q(halt));  // open: Qn, preset, en, reset
endmodule

module status_machine (
  input  in_1,
  input  in_2,
  input  in_3,
  input  in_4
);

  Register #(.width(2)) register_1 ();  // open: D, en, Q, clk, clr
endmodule

module _3Roms_for_trap_prog (
  input  [9:0] addr,
  input  [1:0] intNo,
  output [31:0] IE
);

  wire [31:0] rom_1_data, rom_2_data, rom_3_data;

  ROM #(.addrWidth(10), .dataWidth(32)) rom_1 (.addr(addr), .data(rom_1_data));  // open: sel
  ROM #(.addrWidth(10), .dataWidth(32)) rom_2 (.addr(addr), .data(rom_2_data));  // open: sel
  ROM #(.addrWidth(10), .dataWidth(32)) rom_3 (.addr(addr), .data(rom_3_data));  // open: sel
  Multiplexer #(.select(2), .width(32), .enable("false")) multiplexer_1 (
    .in0(rom_1_data), .in1(rom_2_data), .in2(rom_3_data), .out(IE), .sel(intNo));  // open: in3

  // Notes on the sheet:
  //   contents of rom_1 (hex, n*v repeats v):
  //   401a0800 401b1000 afba0000 23bd0004 afbb0000 23bd0004 201a0008 409a1000 201a0001 409a1000 afa40000
  //   23bd0004 afa50000 23bd0004 afa60000 23bd0004 afa70000 23bd0004 afb00000 23bd0004 afb10000 23bd0004
  //   afb20000 23bd0004 afb30000 23bd0004 afb40000 23bd0004 afb50000 23bd0004 afb60000 23bd0004 afb70000
  //   23bd0004 3a0f020 20160001 20140006 20150001 168020 108100 2149825 132020 20020022 c 1600fffa 295a022
  //   1680fff7 23bdfffc 8fb70000 23bdfffc 8fb60000 23bdfffc 8fb50000 23bdfffc 8fb40000 23bdfffc 8fb30000
  //   23bdfffc 8fb20000 23bdfffc 8fb10000 23bdfffc 8fb00000 23bdfffc 8fa70000 23bdfffc 8fa60000 23bdfffc
  //   8fa50000 23bdfffc 8fa40000 23bdfffc 8fbb0000 23bdfffc 8fba0000 40041000 409a0800 375b0008 409b1000
  //   20020022 c 42000018
  //   contents of rom_2 (hex, n*v repeats v):
  //   401a0800 401b1000 afba0000 23bd0004 afbb0000 23bd0004 201a0008 409a1000 201a0003 409a1000 afa40000
  //   23bd0004 afa50000 23bd0004 afa60000 23bd0004 afa70000 23bd0004 afb00000 23bd0004 afb10000 23bd0004
  //   afb20000 23bd0004 afb30000 23bd0004 afb40000 23bd0004 afb50000 23bd0004 afb60000 23bd0004 afb70000
  //   23bd0004 3a0f020 20160002 20140006 20150001 168020 108100 2149825 132020 20020022 c 1600fffa 295a022
  //   1680fff7 23bdfffc 8fb70000 23bdfffc 8fb60000 23bdfffc 8fb50000 23bdfffc 8fb40000 23bdfffc 8fb30000
  //   23bdfffc 8fb20000 23bdfffc 8fb10000 23bdfffc 8fb00000 23bdfffc 8fa70000 23bdfffc 8fa60000 23bdfffc
  //   8fa50000 23bdfffc 8fa40000 23bdfffc 8fbb0000 23bdfffc 8fba0000 40041000 409a0800 375b0008 409b1000
  //   20020022 c 42000018
  //   contents of rom_3 (hex, n*v repeats v):
  //   401a0800 401b1000 afba0000 23bd0004 afbb0000 23bd0004 201a0008 409a1000 201a0003 409a1000 afa40000
  //   23bd0004 afa50000 23bd0004 afa60000 23bd0004 afa70000 23bd0004 afb00000 23bd0004 afb10000 23bd0004
  //   afb20000 23bd0004 afb30000 23bd0004 afb40000 23bd0004 afb50000 23bd0004 afb60000 23bd0004 afb70000
  //   23bd0004 3a0f020 20160003 20140006 20150001 168020 108100 2149825 132020 20020022 c 1600fffa 295a022
  //   1680fff7 23bdfffc 8fb70000 23bdfffc 8fb60000 23bdfffc 8fb50000 23bdfffc 8fb40000 23bdfffc 8fb30000
  //   23bdfffc 8fb20000 23bdfffc 8fb10000 23bdfffc 8fb00000 23bdfffc 8fa70000 23bdfffc 8fa60000 23bdfffc
  //   8fa50000 23bdfffc 8fa40000 23bdfffc 8fbb0000 23bdfffc 8fba0000 40041000 409a0800 375b0008 409b1000
  //   20020022 c 42000018
endmodule

module circuit (
);

  wire and_1_out, eret, istrap, or_1_out, write2Epc;
  wire [31:0] BadAddr, multiplexer_1_out, PC, regdatain;

  Multiplexer #(.width(32), .disabled(0), .enable("false")) multiplexer_1 (
    .in0(PC), .in1(regdatain), .out(multiplexer_1_out), .sel(write2Epc));
  or or_1 (or_1_out, and_1_out, write2Epc);
  and and_1 (and_1_out, istrap, ~eret);  // AND_Gate
  D_Flip_Flop d_ff_1 (.clk(write2Epc), .D(1'b1));  // open: Q, Qn, preset, en, reset
  Register #(.width(32), .trigger("falling")) u_BadAddr (
    .D(multiplexer_1_out), .Q(BadAddr), .clk(or_1_out));  // open: en, clr
  // Probe on BadAddr
endmodule
