// Logisim project 重定向流水线正确版本2298.circ as structural Verilog: 29 circuits, main circuit 新流水线
module \新流水线  (
);

  wire ALUSrc, and_1_out, and_2_out, and_3_out, and_4_out, and_5_out, and_6_out, and_7_out, and_9_out,
       and_10_out, and_11_out, and_13_out, and_24_out, beq, bne, Branch, check_rs, check_rs_rt, clk,
       ComBranch, comparator_3_eq, comparator_4_eq, comparator_5_eq, comparator_6_eq, comparator_7_eq,
       comparator_8_eq, d_ff_1_q, data_relative, Equal, EX_ALUSrc, EX_beq, EX_bne, EX_ComBranch, EX_Halt,
       EX_I, EX_isCop, EX_J, EX_Jal, EX_Jr, EX_Jump, EX_MemRead, EX_MemWrite, EX_R, EX_RegWrite, EX_rs_is0,
       EX_Shift, EX_syscall, HaflWord, Halt, halt_t, I, ID_EX_isNop, IF_ID_isNop, isBranch, load_use,
       load_use_relative, load_usecheck_rs, load_usecheck_rs_rt, MEM_MemRead, MEM_MemWrite, MEM_RegWrite,
       new_ex_mem_1_out_20, or_2_out, or_3_out, or_4_out, or_6_out, or_8_out, or_9_out, or_10_out, or_11_out,
       or_12_out, PCdst, RegDst, rs_load_use, rs_MEM, rs_MEM_relative, rs_WB, rs_WB_relative, rt_load_use,
       rt_MEM, rt_MEM_relative, rt_WB, rt_WB_relative, Stop, Unsigned, WB_HaflWord, WB_Jal, WB_MemtoReg,
       WB_RegWrite;
  wire [1:0] EX_selno;
  wire [3:0] ALUOp, EX_ALUOp;
  wire [4:0] EX_RegWrite_num, EX_rs, EX_rt, MEM_RegWrite_num, multiplexer_2_out, multiplexer_3_out, rd, rt,
       Write_num;
  wire [9:0] PC_q_2;
  wire [15:0] new_mem_wb_1_readdata_2;
  wire [29:3] \ID产生信号 ;
  wire [31:0] adder_1_out, adder_2_out, adder_3_out, alures, bit_extender_1_out, bit_extender_2_out,
       bit_extender_3_out, bit_extender_4_out, Branch_dst, cnt, counter_6_q, data2rs, data2rt, data_from_MEM,
       data_from_WB, EX_alures, EX_MEM_IR, EX_PC, EX_rs_val, EX_rt_val, Icnt, ID_EX_IR, ID_PC, IF_ID_IR,
       Jcnt, load_use_cnt, main_1_p10, main_1_p11, MEM_PC, MEM_WB_IR, \MEM使用信号信号 , multiplexer_1_out,
       multiplexer_6_out, multiplexer_8_out, multiplexer_9_out, multiplexer_13_out, multiplexer_14_out,
       new_ex_mem_1_data, new_id_ex_1_out_18, new_id_ex_1_out_19, new_id_ex_1_out_22, new_id_ex_1_out_23,
       new_if_id_1_pc_4out, nop_Icnt, PC_branch_cnt, PC_q, ra, ram_1_data, Rcnt, rom_1_data, s0, s1, s2,
       shifter_1_out, WB_PC, \WB使用信号信号 , x, y;
  wire [31:12] \EX使用信号信号 ;
  wire [31:16] new_mem_wb_1_readdata_2_2;

  Multiplexer #(.width(32), .enable("false")) multiplexer_1 (
    .in0(adder_1_out), .in1(Branch_dst), .out(multiplexer_1_out), .sel(PCdst));
  and and_1 (and_1_out, ~halt_t, ~load_use);  // AND_Gate
  Clock clock_1 (.out(clk));
  Register #(.width(32)) PC (
    .D(multiplexer_1_out), .en(and_1_out), .Q({PC_q[31:12], PC_q_2, PC_q[1:0]}), .clk(clk));  // open: clr
  Clock clock_2 (.out(clk));
  Counter #(.width(32), .max('hffffffff)) R (
    .count(\ID产生信号 [18]), .Q(Jcnt), .clk(and_2_out));  // open: load, D, carry, clr
  and and_2 (and_2_out, ~halt_t, clk);  // AND_Gate
  or or_1 (halt_t, Halt, Stop);
  // Probe on {IF_ID_IR[31:13], \ID产生信号 [22:21], IF_ID_IR[10:0]}
  // Probe on ID_EX_IR
  // Probe on EX_MEM_IR
  // Probe on MEM_WB_IR
  // Probe on EX_alures
  or or_2 (or_2_out, beq, bne, \ID产生信号 [20]);
  Adder #(.width(32)) adder_1 (.a(32'h4), .b({PC_q[31:12], PC_q_2, PC_q[1:0]}), .out(adder_1_out));  // open: cin, cout
  and and_3 (and_3_out, \ID产生信号 [20], ~data_relative);  // AND_Gate
  Counter #(.width(32), .max('hffffffff)) counter_1 (
    .count(and_3_out), .Q(Rcnt), .clk(and_2_out));  // open: load, D, carry, clr
  D_Flip_Flop #(.trigger("falling")) d_ff_1 (.clk(Halt), .D(1'b1), .Q(d_ff_1_q));  // open: Qn, preset, en, reset
  or or_3 (or_3_out, \ID产生信号 [13], \ID产生信号 [14], or_2_out);
  and and_4 (and_4_out, I, ~data_relative);  // AND_Gate
  Counter #(.width(32), .max('hffffffff)) counter_2 (
    .count(and_4_out), .Q(Icnt), .clk(and_2_out));  // open: load, D, carry, clr
  D_Flip_Flop #(.trigger("falling")) d_ff_2 (.clk(clk), .D(d_ff_1_q), .Q(Stop));  // open: Qn, preset, en, reset
  and and_5 (and_5_out, or_3_out, ~\ID产生信号 [11]);  // AND_Gate
  or or_4 (or_4_out, I, \ID产生信号 [11]);
  ROM #(.addrWidth(10), .dataWidth(32)) rom_1 (.addr(PC_q_2), .data(rom_1_data));  // open: sel
  new_IF_ID new_if_id_1 (
    .IRin(rom_1_data), .PC_4(adder_1_out), .PC({PC_q[31:12], PC_q_2, PC_q[1:0]}),
    .IRout({IF_ID_IR[31:13], \ID产生信号 [22:21], IF_ID_IR[10:0]}), .PC_4out(new_if_id_1_pc_4out), .PC_2(ID_PC),
    .in_2(clk), .insert_nop(load_use), .PCdst(PCdst));
  Counter #(.width(32), .max('hffffffff)) counter_3 (
    .count(load_use), .Q(load_use_cnt), .clk(and_2_out));  // open: load, D, carry, clr
  or or_5 (isBranch, \ID产生信号 [28], \ID产生信号 [4], \ID产生信号 [3], bne, beq);
  and and_6 (and_6_out, and_5_out, load_usecheck_rs_rt);
  and and_7 (and_7_out, or_4_out, load_usecheck_rs);
  or or_6 (or_6_out, and_6_out, and_7_out);
  // Probe on {IF_ID_IR[31:13], \ID产生信号 [22:21], IF_ID_IR[10:0]}
  Counter #(.width(32), .max('hffffffff)) counter_4 (
    .count(PCdst), .Q(PC_branch_cnt), .clk(and_2_out));  // open: load, D, carry, clr
  // RegisterFile registerfile_1: pin names not known; wires that end beside it: EX_beq, Equal, EX_bne, EX_ComBranch, EX_Jal, EX_Jr, EX_Jump, data_from_WB, clk, WB_RegWrite, rd, \ID产生信号 [27:23], rt, ID_PC, EX_PC, MEM_PC, WB_PC
  and and_8 (load_use_relative, or_6_out, ~ID_EX_isNop);  // AND_Gate
  Counter #(.width(32), .max('hffffffff)) counter_5 (
    .count(1'b1), .Q(cnt), .clk(and_2_out));  // open: load, D, carry, clr
  // Probe on PC_branch_cnt
  // Probe on load_use_cnt
  or or_7 (PCdst, EX_Jr, Branch, EX_Jump);
  // Probe on Icnt
  // Probe on Rcnt
  // Probe on Jcnt
  // Probe on cnt
  // Probe on nop_Icnt
  Multiplexer #(.width(5), .enable("false")) multiplexer_2 (
    .in0(IF_ID_IR[20:16]), .in1({IF_ID_IR[15:13], \ID产生信号 [22:21]}), .out(multiplexer_2_out), .sel(RegDst));
  Comparator #(.width(32), .mode("unsigned")) comparator_1 (
    .a({IF_ID_IR[31:13], \ID产生信号 [22:21], IF_ID_IR[10:0]}), .b({32{1'b0}}), .eq(IF_ID_isNop));  // open: gt, lt
  Comparator #(.width(32), .mode("unsigned")) comparator_2 (
    .a(ID_EX_IR), .b({32{1'b0}}), .eq(ID_EX_isNop));  // open: gt, lt
  or or_8 (or_8_out, EX_beq, EX_bne, EX_R);
  Multiplexer #(.width(5), .enable("false")) multiplexer_3 (
    .in0(IF_ID_IR[25:21]), .in1(5'b00010), .out(multiplexer_3_out), .sel(\ID产生信号 [11]));
  Multiplexer #(.width(5), .enable("false")) multiplexer_4 (
    .in0(IF_ID_IR[20:16]), .in1(5'b00100), .out(rt), .sel(\ID产生信号 [11]));
  Multiplexer #(.width(5), .enable("false")) multiplexer_5 (
    .in0(multiplexer_2_out), .in1({5{1'b1}}), .out(Write_num), .sel(\ID产生信号 [28]));
  assign bit_extender_1_out = {{27{1'b0}}, IF_ID_IR[10:6]};  // Bit_Extender bit_extender_1
  assign bit_extender_2_out = {{16{IF_ID_IR[15]}}, {IF_ID_IR[15:13], \ID产生信号 [22:21], IF_ID_IR[10:0]}};  // Bit_Extender bit_extender_2
  Multiplexer #(.width(32), .enable("false")) multiplexer_6 (
    .in0(bit_extender_2_out), .in1(bit_extender_3_out), .out(multiplexer_6_out), .sel(Unsigned));
  assign bit_extender_3_out = {{16{1'b0}}, {IF_ID_IR[15:13], \ID产生信号 [22:21], IF_ID_IR[10:0]}};  // Bit_Extender bit_extender_3
  or or_9 (or_9_out, EX_MemWrite, EX_MemRead, or_8_out);
  // Probe on {new_if_id_1_pc_4out[31:28], IF_ID_IR[25:13], \ID产生信号 [22:21], IF_ID_IR[10:0], 2'b00}
  Multiplexer #(.width(5), .enable("false")) multiplexer_7 (
    .in0(multiplexer_3_out), .in1({5{1'b1}}), .out(\ID产生信号 [27:23]), .sel(\ID产生信号 [4]));
  and and_9 (and_9_out, or_9_out, ~EX_syscall);  // AND_Gate
  and and_10 (and_10_out, and_9_out, check_rs_rt);
  or or_10 (or_10_out, EX_I, EX_syscall);
  and and_11 (and_11_out, or_10_out, check_rs);
  or or_11 (or_11_out, and_10_out, and_11_out);
  Multiplexer #(.width(32), .enable("false")) multiplexer_8 (
    .in0(EX_rs_val), .in1(data_from_WB), .out(multiplexer_8_out), .sel(rs_WB));
  Control_unit control_unit_1 (
    .in_1({IF_ID_IR[31:13], \ID产生信号 [22:21], IF_ID_IR[10:0]}), .J_type(\ID产生信号 [18]),
    .MemWrite(\ID产生信号 [13]), .MemRead(\ID产生信号 [14]), .MemtoReg(\ID产生信号 [12]), .AluSrc(ALUSrc),
    .RegWrite(\ID产生信号 [29]), .syscall(\ID产生信号 [11]), .shift(\ID产生信号 [5]), .\unsigned (Unsigned),
    .jr(\ID产生信号 [4]), .jal(\ID产生信号 [28]), .jump(\ID产生信号 [3]), .I_type(I), .R_type(\ID产生信号 [20]),
    .RegDst(RegDst), .beq(beq), .bne(bne), .ALUOp(ALUOp), .isHalf(HaflWord), .bltz(ComBranch),
    .isCop(\ID产生信号 [15]), .isCopread(\ID产生信号 [17]));
  // ACM1401_U201414697_朱谷才_regfile_main main_1: pin names not known; wires that end beside it: \ID产生信号 [27:23], rt, rd, s0, data_from_WB, s1, WB_RegWrite, s2, ra, main_1_p10, main_1_p11, main_1_p11
  // NOT_Gate not_1 has open pins: in=clk, out=open
  and and_12 (data_relative, or_11_out, ~ID_EX_isNop);  // AND_Gate
  Multiplexer #(.width(32), .enable("false")) multiplexer_9 (
    .in0(EX_rt_val), .in1(data_from_WB), .out(multiplexer_9_out), .sel(rt_WB));
  // Probe on main_1_p10
  // Probe on main_1_p11
  Multiplexer #(.width(32), .enable("false")) multiplexer_10 (
    .in0(multiplexer_8_out), .in1(data_from_MEM), .out(data2rs), .sel(rs_MEM));
  Multiplexer #(.width(32), .enable("false")) multiplexer_11 (
    .in0(multiplexer_9_out), .in1(data_from_MEM), .out(data2rt), .sel(rt_MEM));
  Multiplexer #(.width(32), .enable("false")) multiplexer_12 (
    .in0(multiplexer_13_out), .in1(adder_3_out), .out(data_from_WB), .sel(WB_Jal));
  and and_13 (and_13_out, Equal, EX_syscall);
  Comparator #(.width(5), .mode("unsigned")) comparator_3 (
    .a(EX_rt), .b(MEM_RegWrite_num), .eq(comparator_3_eq));  // open: gt, lt
  Comparator #(.width(5), .mode("unsigned")) comparator_4 (.a(EX_rt), .b(rd), .eq(comparator_4_eq));  // open: gt, lt
  Comparator #(.width(5), .mode("unsigned")) comparator_5 (
    .a(EX_rs), .b(MEM_RegWrite_num), .eq(comparator_5_eq));  // open: gt, lt
  Comparator #(.width(5), .mode("unsigned")) comparator_6 (.a(EX_rs), .b(rd), .eq(comparator_6_eq));  // open: gt, lt
  new_ID_EX new_id_ex_1 (
    .\信号输入 ({2'b00, \ID产生信号 [29:20], I, \ID产生信号 [18:17], HaflWord, \ID产生信号 [15:11], ALUOp, ALUSrc, \ID产生信号 [5:3], ComBranch, bne, beq}),
    .PCjmp({new_if_id_1_pc_4out[31:28], IF_ID_IR[25:13], \ID产生信号 [22:21], IF_ID_IR[10:0], 2'b00}),
    .PC_4Out(new_if_id_1_pc_4out), .R1Out(main_1_p10), .R2Out(main_1_p11), .shiftNum(bit_extender_1_out),
    .extend(multiplexer_6_out), .RDin(Write_num), .IR({IF_ID_IR[31:13], \ID产生信号 [22:21], IF_ID_IR[10:0]}),
    .PC(ID_PC),
    .out_17({\EX使用信号信号 [31:30], EX_RegWrite, \EX使用信号信号 [28], EX_rs, EX_selno, EX_R, EX_I, EX_J, EX_rs_is0, \EX使用信号信号 [16], EX_isCop, EX_MemRead, EX_MemWrite, \EX使用信号信号 [12], EX_syscall, EX_ALUOp, EX_ALUSrc, EX_Shift, EX_Jr, EX_Jump, EX_ComBranch, EX_bne, EX_beq}),
    .out_18(new_id_ex_1_out_18), .out_19(new_id_ex_1_out_19), .RDout(EX_RegWrite_num), .in_2(clk),
    .isNop(IF_ID_isNop), .load_use(load_use), .out_20(EX_rs_val), .out_21(EX_rt_val),
    .out_22(new_id_ex_1_out_22), .out_23(new_id_ex_1_out_23), .out_25(ID_EX_IR), .out_26(EX_PC),
    .PC_dst(PCdst), .halt(halt_t), .src_reg_num({rt, \ID产生信号 [27:23]}), .out_27({EX_rt, EX_rs}));
  D_Flip_Flop #(.trigger("falling")) d_ff_3 (
    .clk(clk), .D(and_13_out), .Q(EX_Halt), .preset(1'b0));  // open: Qn, en, reset
  and and_14 (rt_MEM_relative, comparator_3_eq, MEM_RegWrite);
  and and_15 (rt_WB_relative, comparator_4_eq, WB_RegWrite);
  and and_16 (rs_MEM_relative, comparator_5_eq, MEM_RegWrite);
  and and_17 (rs_WB_relative, comparator_6_eq, WB_RegWrite);
  and and_18 (rt_load_use, EX_MemRead, load_use_relative);
  and and_19 (rs_load_use, load_use_relative, EX_MemRead);
  // Probe on new_id_ex_1_out_18
  // Probe on data2rt
  Multiplexer #(.width(32), .enable("false")) multiplexer_13 (
    .in0(alures), .in1(multiplexer_14_out), .out(multiplexer_13_out), .sel(WB_MemtoReg));
  or or_12 (or_12_out, rt_MEM_relative, rt_WB_relative);
  or or_13 (load_use, rt_load_use, rs_load_use);
  and and_20 (rt_MEM, data_relative, rt_MEM_relative);
  and and_21 (rt_WB, data_relative, rt_WB_relative);
  and and_22 (rs_MEM, data_relative, rs_MEM_relative);
  and and_23 (rs_WB, data_relative, rs_WB_relative);
  or or_14 (check_rs, rs_MEM_relative, rs_WB_relative);
  Shifter #(.width(32)) shifter_1 (.in(new_id_ex_1_out_23), .\dist (5'b00010), .out(shifter_1_out));
  Multiplexer #(.width(32), .enable("false")) multiplexer_14 (
    .in0({new_mem_wb_1_readdata_2_2, new_mem_wb_1_readdata_2}), .in1(bit_extender_4_out),
    .out(multiplexer_14_out), .sel(WB_HaflWord));
  Adder #(.width(32)) adder_2 (.a(new_id_ex_1_out_19), .b(shifter_1_out), .out(adder_2_out));  // open: cin, cout
  Multiplexer #(.width(32), .enable("false")) multiplexer_15 (.in0(data2rs), .in1(data2rt), .out(x), .sel(EX_Shift));
  ALUSrc_Mux alusrc_mux_1 (
    .R2(data2rt), .extend(new_id_ex_1_out_23), .shift_2(new_id_ex_1_out_22), .output2AluY(y),
    .ALUSrc(EX_ALUSrc), .Shift(EX_Shift), .ComBranch(EX_ComBranch), .syscall(EX_syscall));
  or or_15 (check_rs_rt, or_12_out, check_rs);
  branch_decoder branch_decoder_1 (
    .beq(EX_beq), .Equal(Equal), .bne(EX_bne), .true(EX_alures[0]), .nEqualComBranch(EX_ComBranch),
    .Branch(Branch));
  Comparator #(.width(5), .mode("unsigned")) comparator_7 (
    .a(rt), .b(EX_RegWrite_num), .eq(comparator_7_eq));  // open: gt, lt
  Comparator #(.width(5), .mode("unsigned")) comparator_8 (
    .a(\ID产生信号 [27:23]), .b(EX_RegWrite_num), .eq(comparator_8_eq));  // open: gt, lt
  jump_dst_mux jump_dst_mux_1 (
    .sequencial_dst(new_id_ex_1_out_19), .Branch_dst(adder_2_out), .Jump_dst(new_id_ex_1_out_18),
    .Jr_dst(data2rs), .PC_dst(Branch_dst), .Branch(Branch), .Jump(EX_Jump), .Jr(EX_Jr));
  ALU alu_1 (
    .AluOP(EX_ALUOp), .X(x), .Equal(Equal), .Result(EX_alures), .Y(y));  // open: Signed_Overflow, Result_2, UnSigned_Overflow
  assign bit_extender_4_out = {{16{new_mem_wb_1_readdata_2[15]}}, new_mem_wb_1_readdata_2};  // Bit_Extender bit_extender_4
  and and_24 (and_24_out, comparator_7_eq, EX_RegWrite);
  or or_16 (load_usecheck_rs_rt, and_24_out, load_usecheck_rs);
  and and_25 (load_usecheck_rs, comparator_8_eq, EX_RegWrite);
  new_EX_MEM new_ex_mem_1 (
    .PCdstin(Branch_dst),
    .\信号 ({\EX使用信号信号 [31:30], EX_RegWrite, \EX使用信号信号 [28], EX_rs, EX_selno, EX_R, EX_I, EX_J, EX_rs_is0, \EX使用信号信号 [16], EX_isCop, EX_MemRead, EX_MemWrite, \EX使用信号信号 [12], EX_syscall, EX_ALUOp, EX_ALUSrc, EX_Shift, EX_Jr, EX_Jump, EX_ComBranch, EX_bne, EX_beq}),
    .AluOut(EX_alures), .R2out(data2rt), .IR(ID_EX_IR), .PC(EX_PC), .RDdst(EX_RegWrite_num), .in_11(EX_Halt),
    .\信号_2 ({\MEM使用信号信号 [31:30], MEM_RegWrite, \MEM使用信号信号 [28:15], MEM_MemRead, MEM_MemWrite, \MEM使用信号信号 [12:0]}),
    .ADDR(data_from_MEM), .Data(new_ex_mem_1_data), .IR_2(EX_MEM_IR), .PC_2(MEM_PC),
    .RDdst_2(MEM_RegWrite_num), .out_20(new_ex_mem_1_out_20), .in_2(clk), .src_reg_num({EX_rt, EX_rs}),
    .in_1(1'b0));  // open: PCdstOut, src_reg_num_2
  RAM #(.addrWidth(10), .dataWidth(32), .bus("separate")) ram_1 (
    .addr(data_from_MEM[11:2]), .din(new_ex_mem_1_data), .data(ram_1_data), .str(MEM_MemWrite), .clk(clk),
    .ld(MEM_MemRead));  // open: sel, clr
  new_MEM_WB new_mem_wb_1 (
    .readData(ram_1_data),
    .\信号 ({\MEM使用信号信号 [31:30], MEM_RegWrite, \MEM使用信号信号 [28:15], MEM_MemRead, MEM_MemWrite, \MEM使用信号信号 [12:0]}),
    .AluOut(data_from_MEM), .IR(EX_MEM_IR), .PC(MEM_PC), .RDdst(MEM_RegWrite_num),
    .in_8(new_ex_mem_1_out_20), .readData_2({new_mem_wb_1_readdata_2_2, new_mem_wb_1_readdata_2}),
    .\信号_2 ({\WB使用信号信号 [31:30], WB_RegWrite, WB_Jal, \WB使用信号信号 [27:17], WB_HaflWord, \WB使用信号信号 [15:13], WB_MemtoReg, \WB使用信号信号 [11:0]}),
    .ADDR(alures), .IR_2(MEM_WB_IR), .PC_2(WB_PC), .RDdst_2(rd), .out_15(Halt), .in_1(clk));
  Adder #(.width(32)) adder_3 (.a(WB_PC), .b(32'h4), .out(adder_3_out));  // open: cin, cout
  Counter #(.width(32), .max('hffffffff), .ongoal("load")) counter_6 (
    .load(EX_syscall), .D(data2rt), .count(1'b0), .Q(counter_6_q), .clk(clk));  // open: carry, clr
  Hex_Digit_Display hex_digit_display_1 (.value(counter_6_q[31:28]));  // open: dp
  Hex_Digit_Display hex_digit_display_2 (.value(counter_6_q[27:24]));  // open: dp
  Hex_Digit_Display hex_digit_display_3 (.value(counter_6_q[19:16]));  // open: dp
  Hex_Digit_Display hex_digit_display_4 (.value(counter_6_q[23:20]));  // open: dp
  Hex_Digit_Display hex_digit_display_5 (.value(counter_6_q[11:8]));  // open: dp
  Hex_Digit_Display hex_digit_display_6 (.value(counter_6_q[15:12]));  // open: dp
  Hex_Digit_Display hex_digit_display_7 (.value(counter_6_q[3:0]));  // open: dp
  Hex_Digit_Display hex_digit_display_8 (.value(counter_6_q[7:4]));  // open: dp

  // Other names for the same wires on the sheet: rs[4:0] = \ID产生信号 [27:23]; clkin = clk; R2res[31:0] = data2rt;
  //   DataToReg[31:0] = data_from_WB; true = EX_alures[0];
  //   EX使用信号信号 (some bits) = {EX_RegWrite, EX_rs, EX_selno, EX_R, EX_I, EX_J, EX_rs_is0, EX_isCop, EX_MemRead, EX_MemWrite, EX_syscall, EX_ALUOp, EX_ALUSrc, EX_Shift, EX_Jr, EX_Jump, EX_ComBranch, EX_bne, EX_beq};
  //   ID产生信号 (some bits) = {I, HaflWord, ALUOp, ALUSrc, ComBranch, bne, beq}; Jump = \ID产生信号 [3]; Jr = \ID产生信号 [4];
  //   Shift = \ID产生信号 [5]; syscall = \ID产生信号 [11]; MemtoReg = \ID产生信号 [12]; MemWrite = \ID产生信号 [13];
  //   MemRead = \ID产生信号 [14]; isCop = \ID产生信号 [15]; rs_is0 = \ID产生信号 [17]; J = \ID产生信号 [18]; R = \ID产生信号 [20];
  //   IF_ID_IR[12:11] = \ID产生信号 [22:21]; selno[1:0] = \ID产生信号 [22:21]; Jal = \ID产生信号 [28]; RegWrite = \ID产生信号 [29];
  //   MEM使用信号信号 (some bits) = {MEM_RegWrite, MEM_MemRead, MEM_MemWrite}; WB_RegWrite_num[4:0] = rd;
  //   WB使用信号信号 (some bits) = {WB_RegWrite, WB_Jal, WB_HaflWord, WB_MemtoReg}; insert_nop = data_relative;
  //   重定向 = data_relative

  // Notes on the sheet:
  //   contents of rom_1 (hex, n*v repeats v):
  //   20110001 8000c05 20110001 20120002 20130003 8000c09 20110001 20120002 20130003 8000c0d 20110001
  //   20120002 20130003 8000c11 20110001 20120002 20130003 c000cb8 20100001 20110001 118fc0 112020
  //   20020022 c 118882 12200001 8000c15 112020 20020022 c 20110001 118880 112020 20020022 c 12200001
  //   8000c1f 20110001 118fc0 112020 20020022 c 1188c3 112020 20020022 c 118903 112020 20020022 c 118903
  //   112020 20020022 c 118903 112020 20020022 c 118903 112020 20020022 c 118903 112020 20020022 c 118903
  //   112020 20020022 c 118903 112020 20020022 c 20100001 109fc0 139fc3 8021 2012000c 24160003 26100001
  //   3210000f 20080008 20090001 139900 2709825 132020 20020022 c 1094022 1500fff9 22100001 2018000f
  //   2188024 108700 20080008 20090001 139902 2709825 132021 20020022 c 1094022 1500fff9 108702 2c9b022
  //   12c00001 8000c50 4020 1084027 84400 3508ffff 82021 20020022 c 2010ffff 20110000 ae300000 22100001
  //   22310004 ae300000 22100001 22310004 ae300000 22100001 22310004 ae300000 22100001 22310004 ae300000
  //   22100001 22310004 ae300000 22100001 22310004 ae300000 22100001 22310004 ae300000 22100001 22310004
  //   ae300000 22100001 22310004 ae300000 22100001 22310004 ae300000 22100001 22310004 ae300000 22100001
  //   22310004 ae300000 22100001 22310004 ae300000 22100001 22310004 ae300000 22100001 22310004 ae300000
  //   22100001 22310004 22100001 8020 2011003c 8e130000 8e340000 274402a 11000002 ae330000 ae140000
  //   2231fffc 1611fff8 102020 20020022 c 22100004 2011003c 1611fff2 2002000a c 20100000 22100001 102020
  //   20020022 c 22100002 102020 20020022 c 22100003 102020 20020022 c 22100004 102020 20020022 c 22100005
  //   102020 20020022 c 22100006 102020 20020022 c 22100007 102020 20020022 c 22100008 102020 20020022
  //   20020022 c 3e00008
  //   rs
  //   rt
  //   rd
  //   I型指令需要检查两个的特殊例子,branch和lwsw
  //   ID阶段要读两个寄存器
  //   顺序地址
  //   顺序地址
  //   直接跳转地址
  //   寄存器跳转
  //   条件跳转
  //   $a0
endmodule

module new_MEM_WB (
  input  in_1,
  input  [31:0] readData,
  input  [31:0] \信号 ,
  input  [31:0] AluOut,
  input  [31:0] IR,
  input  [31:0] PC,
  input  [4:0] RDdst,
  input  in_8,
  output [31:0] readData_2,
  output [31:0] \信号_2 ,
  output [31:0] ADDR,
  output [31:0] IR_2,
  output [31:0] PC_2,
  output [4:0] RDdst_2,
  output out_15
);

  Register #(.width(32)) register_1 (.D(readData), .Q(readData_2), .clk(in_1));  // open: en, clr
  Register #(.width(32)) register_2 (.D(\信号 ), .Q(\信号_2 ), .clk(in_1));  // open: en, clr
  Register #(.width(32)) register_3 (.D(AluOut), .Q(ADDR), .clk(in_1));  // open: en, clr
  Register #(.width(32)) register_4 (.D(IR), .Q(IR_2), .clk(in_1));  // open: en, clr
  Register #(.width(32)) register_5 (.D(PC), .Q(PC_2), .clk(in_1));  // open: en, clr
  Register #(.width(5)) register_6 (.D(RDdst), .Q(RDdst_2), .clk(in_1));  // open: en, clr
  Register #(.width(1)) register_7 (.D(in_8), .Q(out_15), .clk(in_1));  // open: en, clr
endmodule

module new_EX_MEM (
  input  in_1,
  input  in_2,
  input  [31:0] PCdstin,
  input  [31:0] \信号 ,
  input  [31:0] AluOut,
  input  [31:0] R2out,
  input  [31:0] IR,
  input  [9:0] src_reg_num,
  input  [31:0] PC,
  input  [4:0] RDdst,
  input  in_11,
  output [31:0] PCdstOut,
  output [31:0] \信号_2 ,
  output [31:0] ADDR,
  output [31:0] Data,
  output [31:0] IR_2,
  output [9:0] src_reg_num_2,
  output [31:0] PC_2,
  output [4:0] RDdst_2,
  output out_20
);

  wire multiplexer_9_out;
  wire [4:0] multiplexer_8_out;
  wire [9:0] multiplexer_6_out;
  wire [31:0] multiplexer_1_out, multiplexer_2_out, multiplexer_3_out, multiplexer_4_out, multiplexer_5_out,
       multiplexer_7_out;

  Register #(.width(32)) register_1 (.D(multiplexer_1_out), .Q(PCdstOut), .clk(in_2));  // open: en, clr
  Register #(.width(32)) register_2 (.D(multiplexer_2_out), .Q(\信号_2 ), .clk(in_2));  // open: en, clr
  Register #(.width(32)) register_3 (.D(multiplexer_3_out), .Q(ADDR), .clk(in_2));  // open: en, clr
  Register #(.width(32)) register_4 (.D(multiplexer_4_out), .Q(Data), .clk(in_2));  // open: en, clr
  Register #(.width(32)) register_5 (.D(multiplexer_5_out), .Q(IR_2), .clk(in_2));  // open: en, clr
  Register #(.width(10)) register_6 (.D(multiplexer_6_out), .Q(src_reg_num_2), .clk(in_2));  // open: en, clr
  Register #(.width(32)) register_7 (.D(multiplexer_7_out), .Q(PC_2), .clk(in_2));  // open: en, clr
  Register #(.width(5)) register_8 (.D(multiplexer_8_out), .Q(RDdst_2), .clk(in_2));  // open: en, clr
  Register #(.width(1)) register_9 (.D(multiplexer_9_out), .Q(out_20), .clk(in_2));  // open: en, clr
  Multiplexer #(.width(32), .enable("false")) multiplexer_1 (
    .in0(PCdstin), .in1({32{1'b0}}), .out(multiplexer_1_out), .sel(in_1));
  Multiplexer #(.width(32), .enable("false")) multiplexer_2 (
    .in0(\信号 ), .in1({32{1'b0}}), .out(multiplexer_2_out), .sel(in_1));
  Multiplexer #(.width(32), .enable("false")) multiplexer_3 (
    .in0(AluOut), .in1({32{1'b0}}), .out(multiplexer_3_out), .sel(in_1));
  Multiplexer #(.width(32), .enable("false")) multiplexer_4 (
    .in0(R2out), .in1({32{1'b0}}), .out(multiplexer_4_out), .sel(in_1));
  Multiplexer #(.width(32), .enable("false")) multiplexer_5 (
    .in0(IR), .in1({32{1'b0}}), .out(multiplexer_5_out), .sel(in_1));
  Multiplexer #(.width(10), .enable("false")) multiplexer_6 (
    .in0(src_reg_num), .in1({10{1'b0}}), .out(multiplexer_6_out), .sel(in_1));
  Multiplexer #(.width(32), .enable("false")) multiplexer_7 (
    .in0(PC), .in1({32{1'b0}}), .out(multiplexer_7_out), .sel(in_1));
  Multiplexer #(.width(5), .enable("false")) multiplexer_8 (
    .in0(RDdst), .in1({5{1'b0}}), .out(multiplexer_8_out), .sel(in_1));
  Multiplexer #(.enable("false")) multiplexer_9 (.in0(in_11), .in1(1'b0), .out(multiplexer_9_out), .sel(in_1));
endmodule

module new_ID_EX (
  input  PC_dst,
  input  in_2,
  input  load_use,
  input  halt,
  input  [31:0] \信号输入 ,
  input  isNop,
  input  [31:0] PCjmp,
  input  [31:0] PC_4Out,
  input  [31:0] R1Out,
  input  [31:0] R2Out,
  input  [31:0] shiftNum,
  input  [31:0] extend,
  input  [4:0] RDin,
  input  [31:0] IR,
  input  [31:0] PC,
  input  [9:0] src_reg_num,
  output [31:0] out_17,
  output [31:0] out_18,
  output [31:0] out_19,
  output [31:0] out_20,
  output [31:0] out_21,
  output [31:0] out_22,
  output [31:0] out_23,
  output [4:0] RDout,
  output [31:0] out_25,
  output [31:0] out_26,
  output [9:0] out_27
);

  wire insert_mop;
  wire [9:0] multiplexer_11_out;
  wire [31:0] multiplexer_1_out, multiplexer_2_out, multiplexer_3_out, multiplexer_4_out, multiplexer_5_out,
       multiplexer_6_out, multiplexer_7_out, multiplexer_8_out, multiplexer_9_out, multiplexer_10_out;

  Multiplexer #(.width(32), .enable("false")) multiplexer_1 (
    .in0(\信号输入 ), .in1({32{1'b0}}), .out(multiplexer_1_out), .sel(isNop));
  Multiplexer #(.width(32), .enable("false")) multiplexer_2 (
    .in0(multiplexer_1_out), .in1({32{1'b0}}), .out(multiplexer_2_out), .sel(insert_mop));
  Multiplexer #(.width(32), .enable("false")) multiplexer_3 (
    .in0(PCjmp), .in1({32{1'b0}}), .out(multiplexer_3_out), .sel(insert_mop));
  Multiplexer #(.width(32), .enable("false")) multiplexer_4 (
    .in0(PC_4Out), .in1({32{1'b0}}), .out(multiplexer_4_out), .sel(insert_mop));
  Multiplexer #(.width(32), .enable("false")) multiplexer_5 (
    .in0(R1Out), .in1({32{1'b0}}), .out(multiplexer_5_out), .sel(insert_mop));
  Multiplexer #(.width(32), .enable("false")) multiplexer_6 (
    .in0(R2Out), .in1({32{1'b0}}), .out(multiplexer_6_out), .sel(insert_mop));
  Multiplexer #(.width(32), .enable("false")) multiplexer_7 (
    .in0(shiftNum), .in1({32{1'b0}}), .out(multiplexer_7_out), .sel(insert_mop));
  Multiplexer #(.width(32), .enable("false")) multiplexer_8 (
    .in0(extend), .in1({32{1'b0}}), .out(multiplexer_8_out), .sel(insert_mop));
  Multiplexer #(.width(32), .enable("false")) multiplexer_9 (
    .in0(IR), .in1({32{1'b0}}), .out(multiplexer_9_out), .sel(insert_mop));
  Multiplexer #(.width(32), .enable("false")) multiplexer_10 (
    .in0(PC), .in1({32{1'b0}}), .out(multiplexer_10_out), .sel(insert_mop));
  Multiplexer #(.width(10), .enable("false")) multiplexer_11 (
    .in0(src_reg_num), .in1({10{1'b0}}), .out(multiplexer_11_out), .sel(insert_mop));
  or or_1 (insert_mop, PC_dst, load_use, halt);
  Register #(.width(32)) \u_信号  (.D(multiplexer_2_out), .Q(out_17), .clk(in_2));  // open: en, clr
  Register #(.width(32)) register_1 (.D(multiplexer_3_out), .Q(out_18), .clk(in_2));  // open: en, clr
  Register #(.width(32)) register_2 (.D(multiplexer_4_out), .Q(out_19), .clk(in_2));  // open: en, clr
  Register #(.width(32)) register_3 (.D(multiplexer_5_out), .Q(out_20), .clk(in_2));  // open: en, clr
  Register #(.width(32)) register_4 (.D(multiplexer_6_out), .Q(out_21), .clk(in_2));  // open: en, clr
  Register #(.width(32)) register_5 (.D(multiplexer_7_out), .Q(out_22), .clk(in_2));  // open: en, clr
  Register #(.width(32)) register_6 (.D(multiplexer_8_out), .Q(out_23), .clk(in_2));  // open: en, clr
  Register #(.width(5)) register_7 (.D(RDin), .Q(RDout), .clk(in_2));  // open: en, clr
  Register #(.width(32)) register_8 (.D(multiplexer_9_out), .Q(out_25), .clk(in_2));  // open: en, clr
  Register #(.width(32)) register_9 (.D(multiplexer_10_out), .Q(out_26), .clk(in_2));  // open: en, clr
  Register #(.width(10)) register_10 (.D(multiplexer_11_out), .Q(out_27), .clk(in_2));  // open: en, clr
endmodule

module new_IF_ID (
  input  insert_nop,
  input  in_2,
  input  PCdst,
  input  [31:0] IRin,
  input  [31:0] PC_4,
  input  [31:0] PC,
  output [31:0] IRout,
  output [31:0] PC_4out,
  output [31:0] PC_2
);

  wire not_1_out;
  wire [31:0] multiplexer_1_out, multiplexer_2_out, multiplexer_3_out;

  Multiplexer #(.width(32), .enable("false")) multiplexer_1 (
    .in0(IRin), .in1({32{1'b0}}), .out(multiplexer_1_out), .sel(PCdst));
  Multiplexer #(.width(32), .enable("false")) multiplexer_2 (
    .in0(PC_4), .in1({32{1'b0}}), .out(multiplexer_2_out), .sel(PCdst));
  Multiplexer #(.width(32), .enable("false")) multiplexer_3 (
    .in0(PC), .in1({32{1'b0}}), .out(multiplexer_3_out), .sel(PCdst));
  not not_1 (not_1_out, insert_nop);
  Register #(.width(32)) register_1 (.D(multiplexer_1_out), .en(not_1_out), .Q(IRout), .clk(in_2));  // open: clr
  Register #(.width(32)) register_2 (.D(multiplexer_2_out), .en(not_1_out), .Q(PC_4out), .clk(in_2));  // open: clr
  Register #(.width(32)) register_3 (.D(multiplexer_3_out), .en(not_1_out), .Q(PC_2), .clk(in_2));  // open: clr
endmodule

module main (
);

  wire \_1按键 , \_1灯 , \_2按键 , \_2灯 , \_3按键 , \_3灯 , ALUSrc, and_1_out, and_2_out, and_4_out, and_7_out, beq,
       bne, Branch, clk, ComBranch, d_ff_1_q, Equal, EX_Halt, ex_mem_1_out_17, EX_syscall, HaflWord, Halt, I,
       IR1, isCop, isCopread, isCopWrite, isCopwrite_t, isreset, isTrap, J, Jal, Jr, Jump, MemRead, MemtoReg,
       MemWrite, R, RegWrite, rs_is0, Shift, syscall, true, \有中断等待 ;
  wire [1:0] cause, selno;
  wire [3:0] ALUOp;
  wire [4:0] ex_mem_1_rddst_2, id_1_write_num, rd, RDex, rs, rt;
  wire [9:0] PCout;
  wire [15:0] mem_wb_1_readdata_2;
  wire [31:0] adder_1_out, adder_2_out, alures, BadAddr, Badaddr1, beforeif_1_irout, beforeif_1_pc,
       beforeif_1_pc_4, bit_extender_1_out, cnt, counter_4_q, data2reg, datain, DataToReg, ex_mem_1_addr,
       ex_mem_1_data, \ex_mem_1_信号_2 , extend, ge_data_in, Icnt, \id_1_信号out , id_ex_1_out_13,
       id_ex_1_out_14, id_ex_1_out_15, id_ex_1_out_17, id_ex_1_out_18, IE, if_id_1_pc_4out,
       IR1InstructionOut, IR_ex_mem, IR_id_ex, IR_mem_wb, Jcnt, jump_dst_mux_1_pc_dst, \mem_wb_1_信号_2 ,
       multiplexer_1_out, multiplexer_2_out, multiplexer_4_out, multiplexer_8_out, PC, PC_4OutinID,
       PC_ex_mem, PC_id_ex, PC_if_id, PC_mem_wb, PCin, PCjmp, R1, R2, ra, ram_1_data, Rcnt, s0, s1,
       shifter_1_out, shitNum, x, y;
  wire [31:1] alu_1_result;
  wire [31:12] \信号 ;
  wire [31:16] mem_wb_1_readdata_2_2;

  Clock clock_1 (.out(clk));
  Counter #(.width(32), .max('hffffffff)) u_R (.count(J), .Q(Jcnt), .clk(and_1_out));  // open: load, D, carry, clr
  and and_1 (and_1_out, ~Halt, clk);  // AND_Gate
  or or_1 (\有中断等待 , \_1灯 , \_2灯 , \_3灯 );
  beforeIF beforeif_1 (
    .Halt(Halt), .\有中断等待 (\有中断等待 ), .clk(clk), .PCin(beforeif_1_pc_4), .IRout(beforeif_1_irout),
    .PC_4(beforeif_1_pc_4), .PC(beforeif_1_pc));
  Counter #(.width(32), .max('hffffffff)) counter_1 (
    .count(R), .Q(Rcnt), .clk(and_1_out));  // open: load, D, carry, clr
  CP0 cp0_1 (
    .eret(isreset), .clk(clk), .no1(\_1按键 ), .\_1号灯 (\_1灯 ), .no2(\_2按键 ), .\_2号灯 (\_2灯 ), .no3(\_3按键 ),
    .\_3号灯 (\_3灯 ), .IEin(ge_data_in), .PCin(PC), .cause(cause), .PCout(PCin), .IE(IE), .CIE(selno),
    .BadAddr1(Badaddr1), .isWrite(isCopWrite));
  Counter #(.width(32), .max('hffffffff)) counter_2 (
    .count(I), .Q(Icnt), .clk(and_1_out));  // open: load, D, carry, clr
  and and_2 (and_2_out, EX_syscall, Equal);
  IF_ID if_id_1 (
    .IRin(beforeif_1_irout), .PC_4(beforeif_1_pc_4), .in_4(clk), .IRout(IR1InstructionOut),
    .PC_4out(if_id_1_pc_4out), .PC(beforeif_1_pc), .PC_2(PC_if_id));
  Counter #(.width(32), .max('hffffffff)) counter_3 (
    .count(1'b1), .Q(cnt), .clk(and_1_out));  // open: load, D, carry, clr
  D_Flip_Flop d_ff_1 (.clk(and_2_out), .D(1'b1), .Q(d_ff_1_q), .preset(1'b0), .reset(isTrap));  // open: Qn, en
  ROM #(.addrWidth(10), .dataWidth(32)) rom_1 ();  // open: addr, data, sel
  D_Flip_Flop d_ff_2 (.clk(clk), .D(d_ff_1_q), .Q(EX_Halt), .preset(1'b0), .reset(isreset));  // open: Qn, en
  ID id_1 (
    .PC_4(if_id_1_pc_4out), .IRin(IR1InstructionOut), .clk(clk), .PCjmp(PCjmp), .PC_4out(PC_4OutinID),
    .R1(R1), .R2(R2), .extend(shitNum), .shift_2(extend), .J(J), .I(I), .R(R), .dataoutfortrap(datain),
    .datain2Reg(DataToReg), .\信号out (\id_1_信号out ), .RW(rd), .Write_num(id_1_write_num), .in_6(RegWrite));  // open: beq, bne, ComBranch, Jump, Jr, shift, Alusrc, Aluop, syscall, MemtoReg, MemWrite, MemRead, isCop, HalfWord, rs_is0, selno, out_28
  // Probe on Icnt
  // Probe on Rcnt
  // Probe on Jcnt
  // Probe on cnt
  // RegisterFile registerfile_1: pin names not known; wires that end beside it: DataToReg, clk, RegWrite, rd, rs, rt
  and and_3 (isCopWrite, isCop, and_4_out);
  and and_4 (and_4_out, ~rs[0], ~rs[1], rs[2], ~rs[3], ~rs[4]);  // AND_Gate
  // Probe on IR1InstructionOut
  // Probe on IR_id_ex
  // Probe on IR_ex_mem
  // Probe on IR_mem_wb
  Multiplexer #(.width(32), .enable("false")) multiplexer_1 (
    .in0(PC), .in1(32'h80000000), .out(multiplexer_1_out), .sel(IR1));
  and and_5 (isCopread, isCop, rs_is0);
  ID_EX id_ex_1 (
    .\信号输入 (\id_1_信号out ), .PCjmp(PCjmp), .PC_4Out(PC_4OutinID), .R1Out(R1), .R2Out(R2), .shiftNum(shitNum),
    .extend(extend),
    .out_12({\信号 [31:28], rs, selno, \信号 [20:18], rs_is0, \信号 [16], isCop, \信号 [14:12], EX_syscall, ALUOp, ALUSrc, Shift, Jr, Jump, ComBranch, bne, beq}),
    .out_13(id_ex_1_out_13), .out_14(id_ex_1_out_14), .out_15(id_ex_1_out_15), .out_16(ge_data_in),
    .out_17(id_ex_1_out_17), .out_18(id_ex_1_out_18), .in_1(clk), .IR(IR1InstructionOut), .out_20(IR_id_ex),
    .RDin(id_1_write_num), .RDout(RDex), .PC(PC_if_id), .out_21(PC_id_ex));
  // Probe on s0
  // Probe on s1
  // Probe on rs
  // Probe on rt
  // Probe on rd
  // Probe on ra
  Multiplexer #(.width(32), .enable("false")) multiplexer_2 (
    .in0(multiplexer_1_out), .in1(BadAddr), .out(multiplexer_2_out), .sel(isreset));
  // Probe on ALUOp
  Multiplexer #(.width(32), .enable("false")) multiplexer_3 (
    .in0(datain), .in1(multiplexer_4_out), .out(data2reg), .sel(isCopread));
  Multiplexer #(.select(2), .width(32), .enable("false")) multiplexer_4 (
    .in1(Badaddr1), .in2(IE), .out(multiplexer_4_out), .sel(selno));  // open: in0, in3
  // Probe on id_ex_1_out_13
  // Probe on id_ex_1_out_15
  // Probe on ge_data_in
  // Probe on x
  // Probe on y
  // Probe on alures
  // Probe on alures
  // Probe on data2reg
  ROM #(.addrWidth(10), .dataWidth(32)) rom_2 (.addr(PCout));  // open: data, sel
  and and_6 (isCopwrite_t, isCop, ~rs_is0);  // AND_Gate
  // Probe on PC_if_id
  // Probe on PC_id_ex
  // Probe on PC_ex_mem
  // Probe on PC_mem_wb
  Shifter #(.width(32)) shifter_1 (.in(id_ex_1_out_18), .\dist (5'b00010), .out(shifter_1_out));
  Multiplexer #(.width(32), .enable("false")) multiplexer_5 (
    .in0(DataToReg), .in1(adder_2_out), .out(datain), .sel(Jal));
  Adder #(.width(32)) adder_1 (.a(id_ex_1_out_14), .b(shifter_1_out), .out(adder_1_out));  // open: cin, cout
  branch_decoder branch_decoder_1 (
    .beq(beq), .Equal(Equal), .bne(bne), .true(true), .nEqualComBranch(ComBranch), .Branch(Branch));
  Multiplexer #(.width(32), .enable("false")) multiplexer_6 (
    .in0(id_ex_1_out_15), .in1(ge_data_in), .out(x), .sel(Shift));
  ALU alu_1 (
    .AluOP(ALUOp), .X(x), .Equal(Equal), .Result({alu_1_result, true}), .Y(y));  // open: Signed_Overflow, Result_2, UnSigned_Overflow
  ALUSrc_Mux alusrc_mux_1 (
    .R2(ge_data_in), .extend(id_ex_1_out_18), .shift_2(id_ex_1_out_17), .output2AluY(y), .ALUSrc(ALUSrc),
    .Shift(Shift), .ComBranch(ComBranch), .syscall(EX_syscall));
  and and_7 (and_7_out, ~IR1InstructionOut[5], IR1InstructionOut[4], IR1InstructionOut[3], ~IR1InstructionOut[2], ~IR1InstructionOut[1], ~IR1InstructionOut[0]);  // AND_Gate
  jump_dst_mux jump_dst_mux_1 (
    .sequencial_dst(id_ex_1_out_14), .Branch_dst(adder_1_out), .Jump_dst(id_ex_1_out_13),
    .Jr_dst(id_ex_1_out_15), .PC_dst(jump_dst_mux_1_pc_dst), .Branch(Branch), .Jump(Jump), .Jr(Jr));
  and and_8 (isreset, and_7_out, isCop);
  EX_MEM ex_mem_1 (
    .PCdstin(jump_dst_mux_1_pc_dst), .AluOut({alu_1_result, true}), .R2out(ge_data_in), .IR(IR_id_ex),
    .PC(PC_id_ex), .PCdstOut(PC), .ADDR(ex_mem_1_addr), .Data(ex_mem_1_data), .IR_2(IR_ex_mem),
    .PC_2(PC_ex_mem), .in_1(clk), .RDdst(RDex), .RDdst_2(ex_mem_1_rddst_2),
    .\信号 ({\信号 [31:28], rs, selno, \信号 [20:18], rs_is0, \信号 [16], isCop, \信号 [14:12], EX_syscall, ALUOp, ALUSrc, Shift, Jr, Jump, ComBranch, bne, beq}),
    .\信号_2 ({\ex_mem_1_信号_2 [31:15], MemRead, MemWrite, \ex_mem_1_信号_2 [12:0]}), .in_9(EX_Halt),
    .out_17(ex_mem_1_out_17));
  Multiplexer #(.width(32), .enable("false")) multiplexer_7 (
    .in0(alures), .in1(multiplexer_8_out), .out(DataToReg), .sel(MemtoReg));
  Multiplexer #(.width(32), .enable("false")) multiplexer_8 (
    .in0({mem_wb_1_readdata_2_2, mem_wb_1_readdata_2}), .in1(bit_extender_1_out), .out(multiplexer_8_out),
    .sel(HaflWord));
  RAM #(.addrWidth(10), .dataWidth(32), .bus("separate")) ram_1 (
    .addr(ex_mem_1_addr[11:2]), .din(ex_mem_1_data), .data(ram_1_data), .str(MemWrite), .clk(clk),
    .ld(MemRead));  // open: sel, clr
  assign bit_extender_1_out = {{16{mem_wb_1_readdata_2[15]}}, mem_wb_1_readdata_2};  // Bit_Extender bit_extender_1
  MEM_WB mem_wb_1 (
    .readData(ram_1_data), .AluOut(ex_mem_1_addr), .IR(IR_ex_mem), .PC(PC_ex_mem), .RDdst(ex_mem_1_rddst_2),
    .readData_2({mem_wb_1_readdata_2_2, mem_wb_1_readdata_2}), .ADDR(alures), .IR_2(IR_mem_wb),
    .PC_2(PC_mem_wb), .RDdst_2(rd), .in_1(clk),
    .\信号 ({\ex_mem_1_信号_2 [31:15], MemRead, MemWrite, \ex_mem_1_信号_2 [12:0]}),
    .\信号_2 ({\mem_wb_1_信号_2 [31:30], RegWrite, Jal, \mem_wb_1_信号_2 [27:17], HaflWord, \mem_wb_1_信号_2 [15:13], MemtoReg, syscall, \mem_wb_1_信号_2 [10:0]}),
    .in_8(ex_mem_1_out_17), .out_15(Halt));
  Adder #(.width(32)) adder_2 (.a(PC_mem_wb), .b(32'h4), .out(adder_2_out));  // open: cin, cout
  Counter #(.width(32), .max('hffffffff), .ongoal("load")) counter_4 (
    .load(syscall), .D(ge_data_in), .count(1'b0), .Q(counter_4_q), .clk(clk));  // open: carry, clr
  Hex_Digit_Display hex_digit_display_1 (.value(counter_4_q[27:24]));  // open: dp
  Hex_Digit_Display hex_digit_display_2 (.value(counter_4_q[31:28]));  // open: dp
  Hex_Digit_Display hex_digit_display_3 (.value(counter_4_q[23:20]));  // open: dp
  Hex_Digit_Display hex_digit_display_4 (.value(counter_4_q[19:16]));  // open: dp
  Button _1 (.out(\_1按键 ));
  Button _2 (.out(\_2按键 ));
  Button _3 (.out(\_3按键 ));
  Hex_Digit_Display hex_digit_display_5 (.value(counter_4_q[15:12]));  // open: dp
  Hex_Digit_Display hex_digit_display_6 (.value(counter_4_q[11:8]));  // open: dp
  LED led_1 (.in(\_1灯 ));
  LED led_2 (.in(\_2灯 ));
  LED led_3 (.in(\_3灯 ));
  // Probe on cause
  Hex_Digit_Display hex_digit_display_7 (.value(counter_4_q[3:0]));  // open: dp
  Hex_Digit_Display hex_digit_display_8 (.value(counter_4_q[7:4]));  // open: dp

  // Other names for the same wires on the sheet: clkin = clk; R2res[31:0] = ge_data_in;
  //   IR_if_id[31:0] = IR1InstructionOut;
  //   信号 (some bits) = {rs, selno, rs_is0, isCop, EX_syscall, ALUOp, ALUSrc, Shift, Jr, Jump, ComBranch, bne, beq}

  // Notes on the sheet:
  //   contents of rom_1 (hex, n*v repeats v):
  //   401a0800 401b1000 afba0000 23bd0004 afbb0000 23bd0004 201a0008 409a1000 201a0003 409a1000 afa40000
  //   23bd0004 afa50000 23bd0004 afa60000 23bd0004 afa70000 23bd0004 afb00000 23bd0004 afb10000 23bd0004
  //   afb20000 23bd0004 afb30000 23bd0004 afb40000 23bd0004 afb50000 23bd0004 afb60000 23bd0004 afb70000
  //   23bd0004 3a0f020 20160003 20140006 20150001 168020 108100 2149825 132020 20020022 c 1600fffa 295a022
  //   1680fff7 23bdfffc 8fb70000 23bdfffc 8fb60000 23bdfffc 8fb50000 23bdfffc 8fb40000 23bdfffc 8fb30000
  //   23bdfffc 8fb20000 23bdfffc 8fb10000 23bdfffc 8fb00000 23bdfffc 8fa70000 23bdfffc 8fa60000 23bdfffc
  //   8fa50000 23bdfffc 8fa40000 23bdfffc 8fbb0000 23bdfffc 8fba0000 40041000 409a0800 375b0008 409b1000
  //   20020022 c 42000018
  //   顺序地址
  //   contents of rom_2 (hex, n*v repeats v):
  //   afa00000 afa10004 afa20008 afa3000c afa40010 afa50014 afa60018 afa7001c afa80020 afa90024 afaa0028
  //   afab002c afac0030 afad0034 afae0038 afaf003c afb00040 afb10044 afb20048 afb3004c afb40050 afb50054
  //   afb60058 afb7005c afb80060 afb90064 afba0068 afbb006c afbc0070 afbd0074 afbe0078 afbf007c 20010080
  //   3a1e822 3a0f020 20100001 109fc0 139fc3 8021 2012000c 24160003 26100001 3210000f 20080008 20090001
  //   139900 2709825 132020 20020022 c 1094022 1500fff9 22100001 2018000f 2188024 108700 20080008 20090001
  //   139902 2709825 132021 20020022 c 1094022 1500fff9 108702 2c9b022 12c00001 8000c29 4020 1084027 84400
  //   3508ffff 82021 20020022 c 8fdf0000 8fdd0008 8fdc000c 8fdb0010 8fda0014 8fd90018 8fd8001c 8fd70020
  //   8fd60024 8fd50028 8fd4002c 8fd30030 8fd20034 8fd10038 8fd0003c 8fcf0040 8fce0044 8fcd0048 8fcc004c
  //   8fcb0050 8fca0054 8fc90058 8fc8005c 8fc70060 8fc60064 8fc50068 8fc4006c 8fc30070 8fc20074 8fc10078
  //   8fc0007c 8fde0004 40040000 2002000a c 42000018
  //   直接跳转地址
  //   寄存器跳转
  //   条件跳转
  //   $a0
endmodule

module MEM_WB (
  input  in_1,
  input  [31:0] readData,
  input  [31:0] \信号 ,
  input  [31:0] AluOut,
  input  [31:0] IR,
  input  [31:0] PC,
  input  [4:0] RDdst,
  input  in_8,
  output [31:0] readData_2,
  output [31:0] \信号_2 ,
  output [31:0] ADDR,
  output [31:0] IR_2,
  output [31:0] PC_2,
  output [4:0] RDdst_2,
  output out_15
);

  Register #(.width(32)) register_1 (.D(readData), .Q(readData_2), .clk(in_1));  // open: en, clr
  Register #(.width(32)) register_2 (.D(\信号 ), .Q(\信号_2 ), .clk(in_1));  // open: en, clr
  Register #(.width(32)) register_3 (.D(AluOut), .Q(ADDR), .clk(in_1));  // open: en, clr
  Register #(.width(32)) register_4 (.D(IR), .Q(IR_2), .clk(in_1));  // open: en, clr
  Register #(.width(32)) register_5 (.D(PC), .Q(PC_2), .clk(in_1));  // open: en, clr
  Register #(.width(5)) register_6 (.D(RDdst), .Q(RDdst_2), .clk(in_1));  // open: en, clr
  Register #(.width(1)) register_7 (.D(in_8), .Q(out_15), .clk(in_1));  // open: en, clr
endmodule

module EX_MEM (
  input  in_1,
  input  [31:0] PCdstin,
  input  [31:0] \信号 ,
  input  [31:0] AluOut,
  input  [31:0] R2out,
  input  [31:0] IR,
  input  [31:0] PC,
  input  [4:0] RDdst,
  input  in_9,
  output [31:0] PCdstOut,
  output [31:0] \信号_2 ,
  output [31:0] ADDR,
  output [31:0] Data,
  output [31:0] IR_2,
  output [31:0] PC_2,
  output [4:0] RDdst_2,
  output out_17
);

  Register #(.width(32)) register_1 (.D(PCdstin), .Q(PCdstOut), .clk(in_1));  // open: en, clr
  Register #(.width(32)) register_2 (.D(\信号 ), .Q(\信号_2 ), .clk(in_1));  // open: en, clr
  Register #(.width(32)) register_3 (.D(AluOut), .Q(ADDR), .clk(in_1));  // open: en, clr
  Register #(.width(32)) register_4 (.D(R2out), .Q(Data), .clk(in_1));  // open: en, clr
  Register #(.width(32)) register_5 (.D(IR), .Q(IR_2), .clk(in_1));  // open: en, clr
  Register #(.width(32)) register_6 (.D(PC), .Q(PC_2), .clk(in_1));  // open: en, clr
  Register #(.width(5)) register_7 (.D(RDdst), .Q(RDdst_2), .clk(in_1));  // open: en, clr
  Register #(.width(1)) register_8 (.D(in_9), .Q(out_17), .clk(in_1));  // open: en, clr
endmodule

module EX (
);

  wire ALUSrc, beq, bne, Branch, ComBranch, Equal, Jr, Jump, MemtoReg, Shift, syscall, undriven_5;
  wire [3:0] ALUOp;
  wire [31:0] adder_1_out, alures, jump_dst_mux_1_pc_dst, multiplexer_3_out, shifter_1_out, undriven,
       undriven_2, undriven_3, undriven_4, x, y;

  Shifter #(.width(32)) shifter_1 (.in(undriven_2), .\dist (5'b00010), .out(shifter_1_out));
  Adder #(.width(32)) adder_1 (.a(undriven_3), .b(shifter_1_out), .out(adder_1_out));  // open: cin, cout
  Multiplexer #(.width(32), .enable("false")) multiplexer_1 (.in0(undriven_4), .in1(undriven), .out(x), .sel(Shift));
  branch_decoder branch_decoder_1 (
    .beq(beq), .Equal(Equal), .bne(bne), .true(alures[0]), .nEqualComBranch(ComBranch), .Branch(Branch));
  ALUSrc_Mux alusrc_mux_1 (
    .R2(undriven), .extend(undriven_2), .output2AluY(y), .ALUSrc(ALUSrc), .Shift(Shift),
    .ComBranch(ComBranch), .syscall(syscall));  // open: shift_2
  Multiplexer #(.width(32), .enable("false")) multiplexer_2 (
    .in0(alures), .in1(multiplexer_3_out), .sel(MemtoReg));  // open: out
  jump_dst_mux jump_dst_mux_1 (
    .sequencial_dst(undriven_3), .Branch_dst(adder_1_out), .Jr_dst(undriven_4),
    .PC_dst(jump_dst_mux_1_pc_dst), .Branch(Branch), .Jump(Jump), .Jr(Jr));  // open: Jump_dst
  ALU alu_1 (
    .AluOP(ALUOp), .X(x), .Equal(Equal), .Result(alures), .Y(y));  // open: Signed_Overflow, Result_2, UnSigned_Overflow
  Multiplexer #(.width(32), .enable("false")) multiplexer_3 (
    .out(multiplexer_3_out), .sel(undriven_5));  // open: in0, in1

  // Other names for the same wires on the sheet: true = alures[0]

  // Notes on the sheet:
  //   直接跳转地址
  //   寄存器跳转
  //   条件跳转
  //   $a0
endmodule

module ID_EX (
  input  in_1,
  input  [31:0] \信号输入 ,
  input  [31:0] PCjmp,
  input  [31:0] PC_4Out,
  input  [31:0] R1Out,
  input  [31:0] R2Out,
  input  [31:0] shiftNum,
  input  [31:0] extend,
  input  [4:0] RDin,
  input  [31:0] IR,
  input  [31:0] PC,
  output [31:0] out_12,
  output [31:0] out_13,
  output [31:0] out_14,
  output [31:0] out_15,
  output [31:0] out_16,
  output [31:0] out_17,
  output [31:0] out_18,
  output [4:0] RDout,
  output [31:0] out_20,
  output [31:0] out_21
);

  Register #(.width(32)) \u_信号  (.D(\信号输入 ), .Q(out_12), .clk(in_1));  // open: en, clr
  Register #(.width(32)) register_1 (.D(PCjmp), .Q(out_13), .clk(in_1));  // open: en, clr
  Register #(.width(32)) register_2 (.D(PC_4Out), .Q(out_14), .clk(in_1));  // open: en, clr
  Register #(.width(32)) register_3 (.D(R1Out), .Q(out_15), .clk(in_1));  // open: en, clr
  Register #(.width(32)) register_4 (.D(R2Out), .Q(out_16), .clk(in_1));  // open: en, clr
  Register #(.width(32)) register_5 (.D(shiftNum), .Q(out_17), .clk(in_1));  // open: en, clr
  Register #(.width(32)) register_6 (.D(extend), .Q(out_18), .clk(in_1));  // open: en, clr
  Register #(.width(5)) register_7 (.D(RDin), .Q(RDout), .clk(in_1));  // open: en, clr
  Register #(.width(32)) register_8 (.D(IR), .Q(out_20), .clk(in_1));  // open: en, clr
  Register #(.width(32)) register_9 (.D(PC), .Q(out_21), .clk(in_1));  // open: en, clr
endmodule

module ID (
  input  [31:0] PC_4,
  input  [31:0] IRin,
  input  clk,
  input  [31:0] datain2Reg,
  input  [4:0] RW,
  input  in_6,
  output [31:0] PCjmp,
  output [31:0] PC_4out,
  output beq,
  output bne,
  output ComBranch,
  output Jump,
  output Jr,
  output shift,
  output Alusrc,
  output [3:0] Aluop,
  output syscall,
  output MemtoReg,
  output MemWrite,
  output MemRead,
  output isCop,
  output HalfWord,
  output rs_is0,
  output J,
  output I,
  output R,
  output [1:0] selno,
  output [4:0] out_28,
  output [4:0] Write_num,
  output [31:0] R1,
  output [31:0] R2,
  output [31:0] extend,
  output [31:0] \信号out ,
  output [31:0] shift_2,
  output [31:0] dataoutfortrap
);

  wire RegDst, Unsigned;
  wire [4:0] multiplexer_1_out, multiplexer_2_out, rt;
  wire [31:0] bit_extender_2_out, bit_extender_3_out, ra, s0, s1, s2;

  // Probe on IRin
  Multiplexer #(.width(5), .enable("false")) multiplexer_1 (
    .in0(IRin[20:16]), .in1(IRin[15:11]), .out(multiplexer_1_out), .sel(RegDst));
  Multiplexer #(.width(5), .enable("false")) multiplexer_2 (
    .in0(IRin[25:21]), .in1(5'b00010), .out(multiplexer_2_out), .sel(syscall));
  Multiplexer #(.width(5), .enable("false")) multiplexer_3 (.in0(IRin[20:16]), .in1(5'b00100), .out(rt), .sel(syscall));
  Multiplexer #(.width(5), .enable("false")) multiplexer_4 (
    .in0(multiplexer_1_out), .in1({5{1'b1}}), .out(Write_num), .sel(\信号out [28]));
  assign extend = {{27{1'b0}}, IRin[10:6]};  // Bit_Extender bit_extender_1
  assign bit_extender_2_out = {{16{IRin[15]}}, IRin[15:0]};  // Bit_Extender bit_extender_2
  Multiplexer #(.width(32), .enable("false")) multiplexer_5 (
    .in0(bit_extender_2_out), .in1(bit_extender_3_out), .out(shift_2), .sel(Unsigned));
  assign bit_extender_3_out = {{16{1'b0}}, IRin[15:0]};  // Bit_Extender bit_extender_3
  // Probe on {PC_4[31:28], IRin[25:0], 2'b00}
  Multiplexer #(.width(5), .enable("false")) multiplexer_6 (
    .in0(multiplexer_2_out), .in1({5{1'b1}}), .out(out_28), .sel(Jr));
  // Probe on s2
  // Probe on s1
  Control_unit control_unit_1 (
    .in_1(IRin), .J_type(J), .MemWrite(MemWrite), .MemRead(MemRead), .MemtoReg(MemtoReg), .AluSrc(Alusrc),
    .RegWrite(\信号out [29]), .syscall(syscall), .shift(shift), .\unsigned (Unsigned), .jr(Jr),
    .jal(\信号out [28]), .jump(Jump), .I_type(I), .R_type(R), .RegDst(RegDst), .beq(beq), .bne(bne),
    .ALUOp(Aluop), .isHalf(HalfWord), .bltz(ComBranch), .isCop(isCop), .isCopread(rs_is0));
  // ACM1401_U201414697_朱谷才_regfile_main main_1: pin names not known; wires that end beside it: out_28, rt, RW, s0, datain2Reg, s1, in_6, s2, clk, ra, R1, R2
  // Probe on R1
  // Probe on R2

  assign PC_4out = PC_4;
  assign PCjmp = {PC_4[31:28], IRin[25:0], 2'b00};
  assign selno = IRin[12:11];
  assign {\信号out [31:30], \信号out [27:0]} = {2'b00, out_28, IRin[12:11], R, I, J, rs_is0, HalfWord, isCop, MemRead, MemWrite, MemtoReg, syscall, Aluop, Alusrc, shift, Jr, Jump, ComBranch, bne, beq};

  // Other names for the same wires on the sheet: data2reg[31:0] = datain2Reg; datain[31:0] = dataoutfortrap;
  //   extend_t[31:0] = shift_2; ge_data_in[31:0] = R2; rd[4:0] = RW; RegWriteIn = in_6; shift_t[31:0] = extend;
  //   HaflWord = HalfWord; rs[4:0] = out_28; Jal = \信号out [28]; RegWrite = \信号out [29]

  // Notes on the sheet:
  //   rs
  //   rt
  //   rd
  //   顺序地址
endmodule

module IF_ID (
  input  [31:0] IRin,
  input  [31:0] PC_4,
  input  [31:0] PC,
  input  in_4,
  output [31:0] IRout,
  output [31:0] PC_4out,
  output [31:0] PC_2
);

  Register #(.width(32)) register_1 (.D(IRin), .Q(IRout), .clk(in_4));  // open: en, clr
  Register #(.width(32)) register_2 (.D(PC_4), .Q(PC_4out), .clk(in_4));  // open: en, clr
  Register #(.width(32)) register_3 (.D(PC), .Q(PC_2), .clk(in_4));  // open: en, clr
endmodule

module beforeIF (
  input  [31:0] PCin,
  input  Halt,
  input  \有中断等待 ,
  input  clk,
  output [31:0] IRout,
  output [31:0] PC_4,
  output [31:0] PC
);

  wire not_1_out, or_1_out;
  wire [31:0] n3roms_for_trap_prog_1_ie, rom_1_data;

  or or_1 (or_1_out, not_1_out, \有中断等待 );
  not not_1 (not_1_out, Halt);
  Register #(.width(32)) u_PC (.D(PCin), .en(or_1_out), .Q(PC), .clk(clk));  // open: clr
  Adder #(.width(32)) adder_1 (.a(32'h4), .b(PC), .out(PC_4));  // open: cin, cout
  _3Roms_for_trap_prog u_3roms_for_trap_prog_1 (.addr(PC[11:2]), .intNo(PC[30:29]), .IE(n3roms_for_trap_prog_1_ie));
  ROM #(.addrWidth(10), .dataWidth(32)) rom_1 (.addr(PC[11:2]), .data(rom_1_data));  // open: sel
  Multiplexer #(.width(32), .enable("false")) multiplexer_1 (
    .in0(rom_1_data), .in1(n3roms_for_trap_prog_1_ie), .out(IRout), .sel(PC[31]));

  // Notes on the sheet:
  //   contents of rom_1 (hex, n*v repeats v):
  //   20100000 20110000 20120000 20130000 36100000 36310001 36520002 36730003 ae100000 ae110004 ae120008
  //   ae13000c 2002000a 20110000 20120000 20130000 c
endmodule

module jump_dst_mux (
  input  [31:0] sequencial_dst,
  input  [31:0] Branch_dst,
  input  Branch,
  input  Jump,
  input  Jr,
  input  [31:0] Jump_dst,
  input  [31:0] Jr_dst,
  output [31:0] PC_dst
);

  wire [31:0] multiplexer_1_out, multiplexer_2_out;

  Multiplexer #(.width(32), .enable("false")) multiplexer_1 (
    .in0(sequencial_dst), .in1(Branch_dst), .out(multiplexer_1_out), .sel(Branch));
  Multiplexer #(.width(32), .enable("false")) multiplexer_2 (
    .in0(multiplexer_1_out), .in1(Jump_dst), .out(multiplexer_2_out), .sel(Jump));
  Multiplexer #(.width(32), .enable("false")) multiplexer_3 (
    .in0(multiplexer_2_out), .in1(Jr_dst), .out(PC_dst), .sel(Jr));
endmodule

module ALUSrc_Mux (
  input  [31:0] R2,
  input  ALUSrc,
  input  Shift,
  input  ComBranch,
  input  syscall,
  input  [31:0] extend,
  input  [31:0] shift_2,
  output [31:0] output2AluY
);

  wire [31:0] multiplexer_1_out, multiplexer_2_out, multiplexer_3_out;

  Multiplexer #(.width(32), .enable("false")) multiplexer_1 (
    .in0(R2), .in1(extend), .out(multiplexer_1_out), .sel(ALUSrc));
  Multiplexer #(.width(32), .enable("false")) multiplexer_2 (
    .in0(multiplexer_1_out), .in1(shift_2), .out(multiplexer_2_out), .sel(Shift));
  Multiplexer #(.width(32), .enable("false")) multiplexer_3 (
    .in0(multiplexer_2_out), .in1({32{1'b0}}), .out(multiplexer_3_out), .sel(ComBranch));
  Multiplexer #(.width(32), .enable("false")) multiplexer_4 (
    .in0(multiplexer_3_out), .in1(32'ha), .out(output2AluY), .sel(syscall));
endmodule

module branch_decoder (
  input  beq,
  input  Equal,
  input  bne,
  input  true,
  input  nEqualComBranch,
  output Branch
);

  wire and_1_out, and_2_out, and_3_out;

  and and_1 (and_1_out, beq, Equal);
  and and_2 (and_2_out, ~Equal, bne);  // AND_Gate
  and and_3 (and_3_out, ~Equal, true, nEqualComBranch);  // AND_Gate
  or or_1 (Branch, and_1_out, and_2_out, and_3_out);
endmodule

module interrupt (
  input  clkin,
  input  \_1号中断 ,
  input  \同步清零信号 ,
  output \与中断屏蔽位与 ,
  output \中断等待灯 
);

  wire and_1_out, d_ff_1_q, or_2_out;

  D_Flip_Flop d_ff_1 (.clk(\_1号中断 ), .D(1'b1), .Q(d_ff_1_q), .reset(\与中断屏蔽位与 ));  // open: Qn, preset, en
  or or_1 (\中断等待灯 , \与中断屏蔽位与 , d_ff_1_q);
  or or_2 (or_2_out, d_ff_1_q, \与中断屏蔽位与 );
  and and_1 (and_1_out, or_2_out, ~\同步清零信号 );  // AND_Gate
  D_Flip_Flop IR1 (.clk(clkin), .D(and_1_out), .Q(\与中断屏蔽位与 ));  // open: Qn, preset, en, reset

  // Notes on the sheet:
  //   中断信号采样参考电路
  //   Reset 
endmodule

module CP0 (
  input  isWrite,
  input  [1:0] CIE,
  input  eret,
  input  no1,
  input  clk,
  input  no2,
  input  no3,
  input  [31:0] IEin,
  input  [31:0] PCin,
  output [31:0] BadAddr1,
  output [1:0] cause,
  output \_1号灯 ,
  output \_2号灯 ,
  output \_3号灯 ,
  output [31:0] IE,
  output [31:0] PCout
);

  wire and_1_out, and_3_out, and_4_out, and_5_out, and_8_out, \interrupt_1_与中断屏蔽位与 , \interrupt_2_与中断屏蔽位与 ,
       \interrupt_3_与中断屏蔽位与 , \IR1清零 , \IR2清零 , \IR3清零 , istrap, nmb, nor_1_out, not_1_out, not_2_out,
       not_3_out, notrap, or_1_out, or_2_out, or_4_out, priority_encoder_1_gs, write2Epc;
  wire [1:0] priority_encoder_1_out, trapNo;
  wire [31:0] _2IE, and_7_out, inIE, mask, multiplexer_4_out, multiplexer_5_out, multiplexer_6_out;

  // Probe on PCin
  interrupt interrupt_1 (
    .clkin(clk), .\_1号中断 (no1), .\中断等待灯 (\_1号灯 ), .\同步清零信号 (\IR1清零 ), .\与中断屏蔽位与 (\interrupt_1_与中断屏蔽位与 ));
  interrupt interrupt_2 (
    .clkin(clk), .\_1号中断 (no3), .\中断等待灯 (\_3号灯 ), .\同步清零信号 (\IR3清零 ), .\与中断屏蔽位与 (\interrupt_2_与中断屏蔽位与 ));
  not not_1 (not_1_out, IE[0]);
  not not_2 (not_2_out, IE[1]);
  not not_3 (not_3_out, IE[2]);
  interrupt interrupt_3 (
    .clkin(clk), .\_1号中断 (no2), .\中断等待灯 (\_2号灯 ), .\同步清零信号 (\IR2清零 ), .\与中断屏蔽位与 (\interrupt_3_与中断屏蔽位与 ));
  and and_1 (and_1_out, isWrite, CIE[1]);
  and and_2 (write2Epc, isWrite, CIE[0]);
  and and_3 (and_3_out, \interrupt_1_与中断屏蔽位与 , not_1_out);
  and and_4 (and_4_out, \interrupt_3_与中断屏蔽位与 , not_2_out);
  and and_5 (and_5_out, \interrupt_2_与中断屏蔽位与 , not_3_out);
  or or_1 (or_1_out, istrap, eret);
  Priority_Encoder #(.select(2)) priority_encoder_1 (
    .in0(1'b0), .in1(and_3_out), .in2(and_4_out), .in3(and_5_out), .out(priority_encoder_1_out),
    .gs(priority_encoder_1_gs), .en_out(notrap));  // open: en_in
  or or_2 (or_2_out, and_1_out, istrap, eret);
  Register #(.width(32)) u_IE (.D(inIE), .en(or_2_out), .Q(IE), .clk(clk));  // open: clr
  assign _2IE = IEin | mask;  // OR_Gate or_3, 32 bits wide
  Register #(.width(2)) casuse (.D(trapNo), .en(or_1_out), .Q(cause), .clk(clk));  // open: clr
  and and_6 (istrap, priority_encoder_1_gs, ~IE[3]);  // AND_Gate
  nor nor_1 (nor_1_out, cause[0], cause[1]);
  Multiplexer #(.width(2), .disabled(0), .enable("false")) multiplexer_1 (
    .in0(priority_encoder_1_out), .in1(2'b00), .out(trapNo), .sel(notrap));
  Decoder #(.select(2), .disabled(0), .enable("false")) decoder_1 (
    .out1(\IR1清零 ), .out2(\IR2清零 ), .out3(\IR3清零 ), .sel(cause));  // open: out0
  Multiplexer #(.width(32), .enable("false")) multiplexer_2 (.in0({32{1'b0}}), .in1(32'h8), .out(mask), .sel(istrap));
  assign and_7_out = IE & 32'h7;  // AND_Gate and_7, 32 bits wide
  Multiplexer #(.width(32), .disabled(0), .enable("false")) multiplexer_3 (
    .in0(_2IE), .in1(and_7_out), .out(inIE), .sel(eret));
  Multiplexer #(.width(32), .disabled(0), .enable("false")) multiplexer_4 (
    .in0(PCin), .in1(IEin), .out(multiplexer_4_out), .sel(write2Epc));
  interrupt interrupt_4 (.clkin(clk), .\_1号中断 (istrap), .\同步清零信号 (eret), .\与中断屏蔽位与 (nmb));  // open: 中断等待灯
  Multiplexer #(.select(2), .width(32), .disabled(0), .enable("false")) multiplexer_5 (
    .in0(PCin), .in1(32'h80000000), .in2(32'ha0000000), .in3(32'hc0000000), .out(multiplexer_5_out),
    .sel(trapNo));
  or or_4 (or_4_out, and_8_out, write2Epc);
  Multiplexer #(.width(32), .disabled(0), .enable("false")) multiplexer_6 (
    .in0(PCin), .in1(multiplexer_5_out), .out(multiplexer_6_out), .sel(istrap));
  Multiplexer #(.width(32), .disabled(0), .enable("false")) multiplexer_7 (
    .in0(multiplexer_6_out), .in1(BadAddr1), .out(PCout), .sel(eret));
  Register #(.width(32)) BadAddr (.D(multiplexer_4_out), .en(or_4_out), .Q(BadAddr1), .clk(clk));  // open: clr
  // Probe on BadAddr1
  D_Flip_Flop d_ff_1 (.clk(write2Epc), .D(1'b1));  // open: Q, Qn, preset, en, reset
  and and_8 (and_8_out, istrap, ~eret);  // AND_Gate

  // Other names for the same wires on the sheet: BadAddr[31:0] = BadAddr1; clkin = clk; PC[31:0] = PCin;
  //   regdatain[31:0] = IEin
endmodule

module Control_unit (
  input  [31:0] in_1,
  output MemWrite,
  output J_type,
  output I_type,
  output R_type,
  output MemRead,
  output RegDst,
  output jump,
  output MemtoReg,
  output AluSrc,
  output beq,
  output bne,
  output RegWrite,
  output shift,
  output syscall,
  output \unsigned ,
  output jr,
  output jal,
  output isHalf,
  output bltz,
  output [3:0] ALUOp,
  output isCop,
  output isCopread
);

  wire add, addi, addiu, addu, \and , and_3_out, and_7_out, and_8_out, andi, COM, com_branch, isAdd, isAnd,
       isOr, isSub, isXor, jump_t, lw, \nor , not_1_out, \or , or_4_out, or_5_out, ori, r_type2_1_sllv,
       r_type2_1_srav, r_type2_1_srlv, shamt_is_0, sll, slt, slti, sltu, sra, srl, sub, subu;
  wire [3:0] multiplexer_1_out, multiplexer_2_out, multiplexer_3_out, multiplexer_4_out, multiplexer_5_out,
       multiplexer_6_out, multiplexer_7_out, multiplexer_8_out, multiplexer_9_out;

  or or_1 (MemRead, lw, isHalf);
  nor nor_1 (shamt_is_0, in_1[6], in_1[7], in_1[8], in_1[9], in_1[10]);
  and and_1 (isHalf, in_1[31], ~in_1[30], ~in_1[29], ~in_1[28], ~in_1[27], in_1[26]);  // AND_Gate
  and and_2 (com_branch, ~in_1[31], ~in_1[30], ~in_1[29], ~in_1[28], ~in_1[27], in_1[26]);  // AND_Gate
  and and_3 (and_3_out, ~in_1[16], ~in_1[17], ~in_1[18], ~in_1[19], ~in_1[20]);  // AND_Gate
  and and_4 (isCopread, ~in_1[21], ~in_1[22], ~in_1[23], ~in_1[24], ~in_1[25]);  // AND_Gate
  nor nor_2 (R_type, in_1[26], in_1[27], in_1[28], in_1[29], in_1[30], in_1[31]);
  and and_5 (bltz, com_branch, and_3_out);
  and and_6 (isCop, ~in_1[31], in_1[30], ~in_1[29], ~in_1[28], ~in_1[27], ~in_1[26]);  // AND_Gate
  I_type i_type_1 (
    .op5(in_1[31]), .op4(in_1[30]), .op3(in_1[29]), .op2(in_1[28]), .op1(in_1[27]), .op0(in_1[26]),
    .addi(addi), .addiu(addiu), .andi(andi), .ori(ori), .xori(isXor), .lw(lw), .sw(MemWrite), .beq(beq),
    .bne(bne), .slti(slti));  // open: lui, sltiu
  J_type j_type_1 (
    .op5(in_1[31]), .op4(in_1[30]), .op3(in_1[29]), .op2(in_1[28]), .op1(in_1[27]), .op0(in_1[26]),
    .j(jump_t), .jal(jal));
  R_type2 r_type2_1 (
    .func5(in_1[5]), .func4(in_1[4]), .sra(sra), .func3(in_1[3]), .func2(in_1[2]), .func1(in_1[1]),
    .sllv(r_type2_1_sllv), .func0(in_1[0]), .opiszero(R_type), .srlv(r_type2_1_srlv), .srav(r_type2_1_srav),
    .jr(jr), .syscall(syscall));
  R_type r_type_1 (
    .func5(in_1[5]), .func4(in_1[4]), .add(add), .func3(in_1[3]), .func2(in_1[2]), .func1(in_1[1]),
    .addu(addu), .func0(in_1[0]), .opiszero(R_type), .sub(sub), .subu(subu), .\and (\and ), .\or (\or ),
    .\nor (\nor ), .slt(slt), .sltu(sltu), .sll(sll), .srl(srl));  // open: xor
  or or_2 (J_type, jump_t, jal);
  Multiplexer #(.width(4), .enable("false")) multiplexer_1 (
    .in0(4'b0000), .in1(4'b0001), .out(multiplexer_1_out), .sel(sra));
  or or_3 (isAnd, \and , andi);
  or or_4 (or_4_out, addi, jal, addiu, andi);
  or or_5 (or_5_out, ori, MemRead, isXor, slti);
  and and_7 (and_7_out, isCop, isCopread);
  and and_8 (and_8_out, R_type, ~jr, ~syscall);  // AND_Gate
  Multiplexer #(.width(4), .enable("false")) multiplexer_2 (
    .in0(multiplexer_1_out), .in1(4'b0010), .out(multiplexer_2_out), .sel(srl));
  or or_6 (RegWrite, or_4_out, or_5_out, and_7_out, and_8_out);
  Multiplexer #(.width(4), .enable("false")) multiplexer_3 (
    .in0(multiplexer_2_out), .in1(4'b0101), .out(multiplexer_3_out), .sel(isAdd));
  Multiplexer #(.width(4), .enable("false")) multiplexer_4 (
    .in0(multiplexer_3_out), .in1(4'b0110), .out(multiplexer_4_out), .sel(isSub));
  or or_7 (COM, slt, bltz, slti);
  Multiplexer #(.width(4), .enable("false")) multiplexer_5 (
    .in0(multiplexer_4_out), .in1(4'b0111), .out(multiplexer_5_out), .sel(isAnd));
  Multiplexer #(.width(4), .enable("false")) multiplexer_6 (
    .in0(multiplexer_5_out), .in1(4'b1000), .out(multiplexer_6_out), .sel(isOr));
  or or_8 (isAdd, lw, addu, addiu, addi, add, MemWrite);
  or or_9 (shift, sll, srl, sra);
  Multiplexer #(.width(4), .enable("false")) multiplexer_7 (
    .in0(multiplexer_6_out), .in1(4'b1001), .out(multiplexer_7_out), .sel(isXor));
  Multiplexer #(.width(4), .enable("false")) multiplexer_8 (
    .in0(multiplexer_7_out), .in1(4'b1010), .out(multiplexer_8_out), .sel(\nor ));
  Multiplexer #(.width(4), .enable("false")) multiplexer_9 (
    .in0(multiplexer_8_out), .in1(4'b1011), .out(multiplexer_9_out), .sel(COM));
  or or_10 (isOr, ori, \or );
  Multiplexer #(.width(4), .enable("false")) multiplexer_10 (
    .in0(multiplexer_9_out), .in1(4'b1100), .out(ALUOp), .sel(sltu));
  or or_11 (isSub, sub, subu);
  not not_1 (not_1_out, R_type);
  or or_12 (\unsigned , addiu, addu, subu, sltu);
  and and_9 (I_type, not_1_out, ~jal, ~jump_t);  // AND_Gate
  and and_10 (AluSrc, I_type, ~beq, ~bne);  // AND_Gate

  assign jump = J_type;
  assign MemtoReg = MemRead;
  assign RegDst = R_type;

  // Other names for the same wires on the sheet: func[5:0] = in_1[5:0]; shamt[4:0] = in_1[10:6];
  //   rd[4:0] = in_1[15:11]; rt[4:0] = in_1[20:16]; rs[4:0] = in_1[25:21]; op[5:0] = in_1[31:26]; isLoad = MemRead;
  //   lh = isHalf; op_is_0 = R_type; sw = MemWrite; xori = isXor
endmodule

module Control_Unit (
  input  [31:0] in_1,
  output addi,
  output sra,
  output addiu,
  output andi,
  output ori,
  output lw,
  output sw,
  output beq,
  output bne,
  output slti,
  output jr,
  output syscall,
  output add,
  output addu,
  output sub,
  output j,
  output \and ,
  output \or ,
  output \nor ,
  output slt,
  output jal,
  output sltu,
  output sll,
  output srl
);

  wire i_type_1_lui, i_type_1_sltiu, i_type_1_xori, op_is_0, r_type2_1_sllv, r_type2_1_srav, r_type2_1_srlv,
       shamt_is_0;

  nor nor_1 (shamt_is_0, in_1[6], in_1[7], in_1[8], in_1[9], in_1[10]);
  nor nor_2 (op_is_0, in_1[26], in_1[27], in_1[28], in_1[29], in_1[30], in_1[31]);
  I_type i_type_1 (
    .op5(in_1[31]), .op4(in_1[30]), .op3(in_1[29]), .op2(in_1[28]), .op1(in_1[27]), .op0(in_1[26]),
    .addi(addi), .addiu(addiu), .andi(andi), .ori(ori), .xori(i_type_1_xori), .lui(i_type_1_lui), .lw(lw),
    .sw(sw), .beq(beq), .bne(bne), .slti(slti), .sltiu(i_type_1_sltiu));
  J_type j_type_1 (
    .op5(in_1[31]), .op4(in_1[30]), .op3(in_1[29]), .op2(in_1[28]), .op1(in_1[27]), .op0(in_1[26]), .j(j),
    .jal(jal));
  R_type2 r_type2_1 (
    .func5(in_1[5]), .func4(in_1[4]), .sra(sra), .func3(in_1[3]), .func2(in_1[2]), .func1(in_1[1]),
    .sllv(r_type2_1_sllv), .func0(in_1[0]), .opiszero(op_is_0), .srlv(r_type2_1_srlv), .srav(r_type2_1_srav),
    .jr(jr), .syscall(syscall));
  R_type r_type_1 (
    .func5(in_1[5]), .func4(in_1[4]), .add(add), .func3(in_1[3]), .func2(in_1[2]), .func1(in_1[1]),
    .addu(addu), .func0(in_1[0]), .opiszero(op_is_0), .sub(sub), .\and (\and ), .\or (\or ), .\nor (\nor ),
    .slt(slt), .sltu(sltu), .sll(sll), .srl(srl));  // open: subu, xor

  // Other names for the same wires on the sheet: func[5:0] = in_1[5:0]; shamt[4:0] = in_1[10:6];
  //   rd[4:0] = in_1[15:11]; rt[4:0] = in_1[20:16]; rs[4:0] = in_1[25:21]; op[5:0] = in_1[31:26]
endmodule

module I_type (
  input  op5,
  input  op4,
  input  op3,
  input  op2,
  input  op1,
  input  op0,
  output addi,
  output addiu,
  output andi,
  output ori,
  output xori,
  output lui,
  output lw,
  output sw,
  output beq,
  output bne,
  output slti,
  output sltiu
);

  wire not_1_out, not_2_out, not_3_out, not_4_out, not_5_out, not_6_out, not_7_out, not_8_out, not_9_out,
       not_10_out, not_11_out, not_12_out, not_13_out, not_14_out, not_15_out, not_16_out, not_17_out,
       not_18_out, not_19_out, not_20_out, not_21_out, not_22_out, not_23_out, not_24_out, not_25_out,
       not_26_out, not_27_out, not_28_out, not_29_out, not_30_out, not_31_out, not_32_out, not_33_out,
       not_34_out, not_35_out, not_36_out, not_37_out, not_38_out, not_39_out, not_40_out, not_41_out,
       not_42_out;

  not not_1 (not_1_out, op5);
  not not_2 (not_2_out, op4);
  not not_3 (not_3_out, op2);
  not not_4 (not_4_out, op1);
  not not_5 (not_5_out, op0);
  not not_6 (not_6_out, op5);
  not not_7 (not_7_out, op4);
  not not_8 (not_8_out, op2);
  not not_9 (not_9_out, op1);
  not not_10 (not_10_out, op5);
  not not_11 (not_11_out, op4);
  not not_12 (not_12_out, op1);
  not not_13 (not_13_out, op0);
  not not_14 (not_14_out, op5);
  not not_15 (not_15_out, op4);
  not not_16 (not_16_out, op1);
  not not_17 (not_17_out, op5);
  not not_18 (not_18_out, op4);
  not not_19 (not_19_out, op0);
  not not_20 (not_20_out, op5);
  not not_21 (not_21_out, op4);
  not not_22 (not_22_out, op4);
  not not_23 (not_23_out, op3);
  not not_24 (not_24_out, op2);
  not not_25 (not_25_out, op4);
  not not_26 (not_26_out, op2);
  not not_27 (not_27_out, op5);
  not not_28 (not_28_out, op4);
  not not_29 (not_29_out, op3);
  not not_30 (not_30_out, op1);
  not not_31 (not_31_out, op0);
  not not_32 (not_32_out, op5);
  not not_33 (not_33_out, op4);
  not not_34 (not_34_out, op3);
  not not_35 (not_35_out, op1);
  not not_36 (not_36_out, op5);
  not not_37 (not_37_out, op4);
  not not_38 (not_38_out, op2);
  not not_39 (not_39_out, op0);
  not not_40 (not_40_out, op5);
  not not_41 (not_41_out, op4);
  not not_42 (not_42_out, op2);
  and and_1 (addi, not_1_out, not_2_out, op3, not_3_out, not_4_out, not_5_out);
  and and_2 (addiu, not_6_out, not_7_out, op3, not_8_out, not_9_out, op0);
  and and_3 (andi, not_10_out, not_11_out, op3, op2, not_12_out, not_13_out);
  and and_4 (ori, not_14_out, not_15_out, op3, op2, not_16_out, op0);
  and and_5 (xori, not_17_out, not_18_out, op3, op2, op1, not_19_out);
  and and_6 (lui, not_20_out, not_21_out, op3, op2, op1, op0);
  and and_7 (lw, op5, not_22_out, not_23_out, not_24_out, op1, op0);
  and and_8 (sw, op5, not_25_out, op3, not_26_out, op1, op0);
  and and_9 (beq, not_27_out, not_28_out, not_29_out, op2, not_30_out, not_31_out);
  and and_10 (bne, not_32_out, not_33_out, not_34_out, op2, not_35_out, op0);
  and and_11 (slti, not_36_out, not_37_out, op3, not_38_out, op1, not_39_out);
  and and_12 (sltiu, not_40_out, not_41_out, op3, not_42_out, op1, op0);
endmodule

module R_type (
  input  func5,
  input  func4,
  input  func3,
  input  func2,
  input  func1,
  input  func0,
  input  opiszero,
  output add,
  output addu,
  output sub,
  output subu,
  output \and ,
  output \or ,
  output \xor ,
  output \nor ,
  output slt,
  output sltu,
  output sll,
  output srl
);

  wire not_1_out, not_2_out, not_3_out, not_4_out, not_5_out, not_6_out, not_7_out, not_8_out, not_9_out,
       not_10_out, not_11_out, not_12_out, not_13_out, not_14_out, not_15_out, not_16_out, not_17_out,
       not_18_out, not_19_out, not_20_out, not_21_out, not_22_out, not_23_out, not_24_out, not_25_out,
       not_26_out, not_27_out, not_28_out, not_29_out, not_30_out, not_31_out, not_32_out, not_33_out,
       not_34_out, not_35_out, not_36_out, not_37_out, not_38_out, not_39_out, not_40_out, not_41_out,
       not_42_out, not_43_out, not_44_out;

  not not_1 (not_1_out, func4);
  not not_2 (not_2_out, func3);
  not not_3 (not_3_out, func2);
  not not_4 (not_4_out, func1);
  not not_5 (not_5_out, func0);
  not not_6 (not_6_out, func4);
  not not_7 (not_7_out, func3);
  not not_8 (not_8_out, func2);
  not not_9 (not_9_out, func1);
  not not_10 (not_10_out, func4);
  not not_11 (not_11_out, func3);
  not not_12 (not_12_out, func2);
  not not_13 (not_13_out, func0);
  not not_14 (not_14_out, func4);
  not not_15 (not_15_out, func3);
  not not_16 (not_16_out, func2);
  not not_17 (not_17_out, func4);
  not not_18 (not_18_out, func3);
  not not_19 (not_19_out, func1);
  not not_20 (not_20_out, func0);
  not not_21 (not_21_out, func4);
  not not_22 (not_22_out, func3);
  not not_23 (not_23_out, func1);
  not not_24 (not_24_out, func4);
  not not_25 (not_25_out, func3);
  not not_26 (not_26_out, func0);
  not not_27 (not_27_out, func4);
  not not_28 (not_28_out, func3);
  not not_29 (not_29_out, func4);
  not not_30 (not_30_out, func2);
  not not_31 (not_31_out, func0);
  not not_32 (not_32_out, func4);
  not not_33 (not_33_out, func2);
  not not_34 (not_34_out, func5);
  not not_35 (not_35_out, func4);
  not not_36 (not_36_out, func3);
  not not_37 (not_37_out, func2);
  not not_38 (not_38_out, func1);
  not not_39 (not_39_out, func0);
  not not_40 (not_40_out, func5);
  not not_41 (not_41_out, func4);
  not not_42 (not_42_out, func3);
  not not_43 (not_43_out, func2);
  not not_44 (not_44_out, func0);
  and and_1 (add, func5, not_1_out, not_2_out, not_3_out, not_4_out, not_5_out, opiszero);
  and and_2 (addu, func5, not_6_out, not_7_out, not_8_out, not_9_out, func0, opiszero);
  and and_3 (sub, func5, not_10_out, not_11_out, not_12_out, func1, not_13_out, opiszero);
  and and_4 (subu, func5, not_14_out, not_15_out, not_16_out, func1, func0, opiszero);
  and and_5 (\and , func5, not_17_out, not_18_out, func2, not_19_out, not_20_out, opiszero);
  and and_6 (\or , func5, not_21_out, not_22_out, func2, not_23_out, func0, opiszero);
  and and_7 (\xor , func5, not_24_out, not_25_out, func2, func1, not_26_out, opiszero);
  and and_8 (\nor , func5, not_27_out, not_28_out, func2, func1, func0, opiszero);
  and and_9 (slt, func5, not_29_out, func3, not_30_out, func1, not_31_out, opiszero);
  and and_10 (sltu, func5, not_32_out, func3, not_33_out, func1, func0, opiszero);
  and and_11 (sll, not_34_out, not_35_out, not_36_out, not_37_out, not_38_out, not_39_out, opiszero);
  and and_12 (srl, not_40_out, not_41_out, not_42_out, not_43_out, func1, not_44_out, opiszero);
endmodule

module R_type2 (
  input  func5,
  input  func4,
  input  func3,
  input  func2,
  input  func1,
  input  func0,
  input  opiszero,
  output sra,
  output sllv,
  output srlv,
  output srav,
  output jr,
  output syscall
);

  wire not_1_out, not_2_out, not_3_out, not_4_out, not_5_out, not_6_out, not_7_out, not_8_out, not_9_out,
       not_10_out, not_11_out, not_12_out, not_13_out, not_14_out, not_15_out, not_16_out, not_17_out,
       not_18_out, not_19_out, not_20_out, not_21_out, not_22_out, not_23_out, not_24_out, not_25_out;

  not not_1 (not_1_out, func5);
  not not_2 (not_2_out, func4);
  not not_3 (not_3_out, func3);
  not not_4 (not_4_out, func2);
  not not_5 (not_5_out, func5);
  not not_6 (not_6_out, func4);
  not not_7 (not_7_out, func3);
  not not_8 (not_8_out, func1);
  not not_9 (not_9_out, func0);
  not not_10 (not_10_out, func5);
  not not_11 (not_11_out, func4);
  not not_12 (not_12_out, func3);
  not not_13 (not_13_out, func0);
  not not_14 (not_14_out, func5);
  not not_15 (not_15_out, func4);
  not not_16 (not_16_out, func3);
  not not_17 (not_17_out, func5);
  not not_18 (not_18_out, func4);
  not not_19 (not_19_out, func2);
  not not_20 (not_20_out, func1);
  not not_21 (not_21_out, func0);
  not not_22 (not_22_out, func5);
  not not_23 (not_23_out, func4);
  not not_24 (not_24_out, func1);
  not not_25 (not_25_out, func0);
  and and_1 (sra, not_1_out, not_2_out, not_3_out, not_4_out, func1, func0, opiszero);
  and and_2 (sllv, not_5_out, not_6_out, not_7_out, func2, not_8_out, not_9_out, opiszero);
  and and_3 (srlv, not_10_out, not_11_out, not_12_out, func2, func1, not_13_out, opiszero);
  and and_4 (srav, not_14_out, not_15_out, not_16_out, func2, func1, func0, opiszero);
  and and_5 (jr, not_17_out, not_18_out, func3, not_19_out, not_20_out, not_21_out, opiszero);
  and and_6 (syscall, not_22_out, not_23_out, func3, func2, not_24_out, not_25_out, opiszero);
endmodule

module J_type (
  input  op5,
  input  op4,
  input  op3,
  input  op2,
  input  op1,
  input  op0,
  output j,
  output jal
);

  wire not_1_out, not_2_out, not_3_out, not_4_out, not_5_out, not_6_out, not_7_out, not_8_out, not_9_out;

  not not_1 (not_1_out, op5);
  not not_2 (not_2_out, op4);
  not not_3 (not_3_out, op3);
  not not_4 (not_4_out, op2);
  not not_5 (not_5_out, op0);
  not not_6 (not_6_out, op5);
  not not_7 (not_7_out, op4);
  not not_8 (not_8_out, op3);
  not not_9 (not_9_out, op2);
  and and_1 (j, not_1_out, not_2_out, not_3_out, not_4_out, op1, not_5_out);
  and and_2 (jal, not_6_out, not_7_out, not_8_out, not_9_out, op1, op0);
endmodule

module newUnit (
  input  [31:0] in_1,
  output MemWrite,
  output J_type,
  output I_type,
  output R_type,
  output MemRead,
  output RegDst,
  output AluSrc,
  output jump,
  output MemtoReg,
  output RegWrite,
  output shift,
  output syscall,
  output \unsigned ,
  output jr,
  output jal
);

  wire add, addi, addiu, addu, \and , and_2_out, andi, beq, bne, \nor , not_1_out, \or , or_1_out, or_2_out,
       ori, r_type2_1_sllv, r_type2_1_srav, r_type2_1_srlv, shamt_is_0, sll, slt, slti, sltu, sra, srl, sub;

  nor nor_1 (shamt_is_0, in_1[6], in_1[7], in_1[8], in_1[9], in_1[10]);
  nor nor_2 (R_type, in_1[26], in_1[27], in_1[28], in_1[29], in_1[30], in_1[31]);
  I_type i_type_1 (
    .op5(in_1[31]), .op4(in_1[30]), .op3(in_1[29]), .op2(in_1[28]), .op1(in_1[27]), .op0(in_1[26]),
    .addi(addi), .addiu(addiu), .andi(andi), .ori(ori), .lw(MemRead), .sw(MemWrite), .beq(beq), .bne(bne),
    .slti(slti));  // open: xori, lui, sltiu
  J_type j_type_1 (
    .op5(in_1[31]), .op4(in_1[30]), .op3(in_1[29]), .op2(in_1[28]), .op1(in_1[27]), .op0(in_1[26]), .j(jump),
    .jal(jal));
  R_type2 r_type2_1 (
    .func5(in_1[5]), .func4(in_1[4]), .sra(sra), .func3(in_1[3]), .func2(in_1[2]), .func1(in_1[1]),
    .sllv(r_type2_1_sllv), .func0(in_1[0]), .opiszero(R_type), .srlv(r_type2_1_srlv), .srav(r_type2_1_srav),
    .jr(jr), .syscall(syscall));
  R_type r_type_1 (
    .func5(in_1[5]), .func4(in_1[4]), .add(add), .func3(in_1[3]), .func2(in_1[2]), .func1(in_1[1]),
    .addu(addu), .func0(in_1[0]), .opiszero(R_type), .sub(sub), .\and (\and ), .\or (\or ), .\nor (\nor ),
    .slt(slt), .sltu(sltu), .sll(sll), .srl(srl));  // open: subu, xor
  and and_1 (J_type, jump, jal);
  or or_1 (or_1_out, addi, addiu, andi);
  or or_2 (or_2_out, ori, MemRead, slti);
  and and_2 (and_2_out, R_type, ~jr);  // AND_Gate
  or or_3 (RegWrite, or_1_out, or_2_out, and_2_out);
  or or_4 (shift, sll, srl, sra);
  not not_1 (not_1_out, R_type);
  or or_5 (\unsigned , addiu, addu, sltu);
  and and_3 (AluSrc, not_1_out, ~jal, ~jump);  // AND_Gate

  assign I_type = AluSrc;
  assign MemtoReg = MemRead;
  assign RegDst = R_type;

  // Other names for the same wires on the sheet: func[5:0] = in_1[5:0]; shamt[4:0] = in_1[10:6];
  //   rd[4:0] = in_1[15:11]; rt[4:0] = in_1[20:16]; rs[4:0] = in_1[25:21]; op[5:0] = in_1[31:26]; lw = MemRead;
  //   op_is_0 = R_type; sw = MemWrite
endmodule

module Latch (
  input  clk,
  input  syscall,
  input  equal,
  output halt
);

  wire and_1_out, d_ff_1_q;

  and and_1 (and_1_out, syscall, equal);
  D_Flip_Flop d_ff_1 (.clk(and_1_out), .D(1'b1), .Q(d_ff_1_q));  // open: Qn, preset, en, reset
  D_Flip_Flop d_ff_2 (.clk(clk), .D(d_ff_1_q), .Q(halt));  // open: Qn, preset, en, reset
endmodule

module status_machine (
  input  in_1,
  input  in_2,
  input  in_3,
  input  in_4
);

  Register #(.width(2)) register_1 ();  // open: D, en, Q, clk, clr
endmodule

module _3Roms_for_trap_prog (
  input  [9:0] addr,
  input  [1:0] intNo,
  output [31:0] IE
);

  wire [31:0] rom_1_data, rom_2_data, rom_3_data;

  ROM #(.addrWidth(10), .dataWidth(32)) rom_1 (.addr(addr), .data(rom_1_data));  // open: sel
  ROM #(.addrWidth(10), .dataWidth(32)) rom_2 (.addr(addr), .data(rom_2_data));  // open: sel
  ROM #(.addrWidth(10), .dataWidth(32)) rom_3 (.addr(addr), .data(rom_3_data));  // open: sel
  Multiplexer #(.select(2), .width(32), .enable("false")) multiplexer_1 (
    .in0(rom_1_data), .in1(rom_2_data), .in2(rom_3_data), .out(IE), .sel(intNo));  // open: in3

  // Notes on the sheet:
  //   contents of rom_1 (hex, n*v repeats v):
  //   401a0800 401b1000 afba0000 23bd0004 afbb0000 23bd0004 201a0008 409a1000 201a0001 409a1000 afa40000
  //   23bd0004 afa50000 23bd0004 afa60000 23bd0004 afa70000 23bd0004 afb00000 23bd0004 afb10000 23bd0004
  //   afb20000 23bd0004 afb30000 23bd0004 afb40000 23bd0004 afb50000 23bd0004 afb60000 23bd0004 afb70000
  //   23bd0004 3a0f020 20160001 20140006 20150001 168020 108100 2149825 132020 20020022 c 1600fffa 295a022
  //   1680fff7 23bdfffc 8fb70000 23bdfffc 8fb60000 23bdfffc 8fb50000 23bdfffc 8fb40000 23bdfffc 8fb30000
  //   23bdfffc 8fb20000 23bdfffc 8fb10000 23bdfffc 8fb00000 23bdfffc 8fa70000 23bdfffc 8fa60000 23bdfffc
  //   8fa50000 23bdfffc 8fa40000 23bdfffc 8fbb0000 23bdfffc 8fba0000 40041000 409a0800 375b0008 409b1000
  //   20020022 c 42000018
  //   contents of rom_2 (hex, n*v repeats v):
  //   401a0800 401b1000 afba0000 23bd0004 afbb0000 23bd0004 201a0008 409a1000 201a0003 409a1000 afa40000
  //   23bd0004 afa50000 23bd0004 afa60000 23bd0004 afa70000 23bd0004 afb00000 23bd0004 afb10000 23bd0004
  //   afb20000 23bd0004 afb30000 23bd0004 afb40000 23bd0004 afb50000 23bd0004 afb60000 23bd0004 afb70000
  //   23bd0004 3a0f020 20160002 20140006 20150001 168020 108100 2149825 132020 20020022 c 1600fffa 295a022
  //   1680fff7 23bdfffc 8fb70000 23bdfffc 8fb60000 23bdfffc 8fb50000 23bdfffc 8fb40000 23bdfffc 8fb30000
  //   23bdfffc 8fb20000 23bdfffc 8fb10000 23bdfffc 8fb00000 23bdfffc 8fa70000 23bdfffc 8fa60000 23bdfffc
  //   8fa50000 23bdfffc 8fa40000 23bdfffc 8fbb0000 23bdfffc 8fba0000 40041000 409a0800 375b0008 409b1000
  //   20020022 c 42000018
  //   contents of rom_3 (hex, n*v repeats v):
  //   401a0800 401b1000 afba0000 23bd0004 afbb0000 23bd0004 201a0008 409a1000 201a0003 409a1000 afa40000
  //   23bd0004 afa50000 23bd0004 afa60000 23bd0004 afa70000 23bd0004 afb00000 23bd0004 afb10000 23bd0004
  //   afb20000 23bd0004 afb30000 23bd0004 afb40000 23bd0004 afb50000 23bd0004 afb60000 23bd0004 afb70000
  //   23bd0004 3a0f020 20160003 20140006 20150001 168020 108100 2149825 132020 20020022 c 1600fffa 295a022
  //   1680fff7 23bdfffc 8fb70000 23bdfffc 8fb60000 23bdfffc 8fb50000 23bdfffc 8fb40000 23bdfffc 8fb30000
  //   23bdfffc 8fb20000 23bdfffc 8fb10000 23bdfffc 8fb00000 23bdfffc 8fa70000 23bdfffc 8fa60000 23bdfffc
  //   8fa50000 23bdfffc 8fa40000 23bdfffc 8fbb0000 23bdfffc 8fba0000 40041000 409a0800 375b0008 409b1000
  //   20020022 c 42000018
endmodule

module circuit (
);

  wire clock_1_out, control_unit_1_alusrc, control_unit_1_beq, control_unit_1_bltz, control_unit_1_bne,
       control_unit_1_i_type, control_unit_1_iscop, control_unit_1_iscopread, control_unit_1_ishalf,
       control_unit_1_j_type, control_unit_1_jal, control_unit_1_jr, control_unit_1_jump,
       control_unit_1_memread, control_unit_1_memtoreg, control_unit_1_memwrite, control_unit_1_r_type,
       control_unit_1_regdst, control_unit_1_regwrite, control_unit_1_shift, control_unit_1_syscall,
       control_unit_1_unsigned;
  wire [3:0] control_unit_1_aluop;
  wire [9:0] PC_q_2;
  wire [31:0] adder_1_out, PC_q, rom_1_data;

  Adder #(.width(32)) adder_1 (.a({PC_q[31:12], PC_q_2, PC_q[1:0]}), .b(32'h4), .out(adder_1_out));  // open: cin, cout
  Register #(.width(32)) PC (
    .D(adder_1_out), .Q({PC_q[31:12], PC_q_2, PC_q[1:0]}), .clk(clock_1_out));  // open: en, clr
  Clock clock_1 (.out(clock_1_out));
  ROM #(.addrWidth(10), .dataWidth(32)) rom_1 (.addr(PC_q_2), .data(rom_1_data));  // open: sel
  // Probe on control_unit_1_j_type
  // Probe on control_unit_1_i_type
  // Probe on control_unit_1_regwrite
  // Probe on control_unit_1_syscall
  // Probe on control_unit_1_regdst
  // Probe on control_unit_1_r_type
  // Probe on control_unit_1_unsigned
  // Probe on control_unit_1_shift
  // Probe on control_unit_1_memread
  // Probe on control_unit_1_memwrite
  // Probe on control_unit_1_jal
  // Probe on control_unit_1_jr
  // Probe on control_unit_1_memtoreg
  // Probe on control_unit_1_aluop
  // Probe on control_unit_1_alusrc
  Control_unit control_unit_1 (
    .in_1(rom_1_data), .J_type(control_unit_1_j_type), .MemWrite(control_unit_1_memwrite),
    .MemRead(control_unit_1_memread), .MemtoReg(control_unit_1_memtoreg), .AluSrc(control_unit_1_alusrc),
    .RegWrite(control_unit_1_regwrite), .syscall(control_unit_1_syscall), .shift(control_unit_1_shift),
    .\unsigned (control_unit_1_unsigned), .jr(control_unit_1_jr), .jal(control_unit_1_jal),
    .jump(control_unit_1_jump), .I_type(control_unit_1_i_type), .R_type(control_unit_1_r_type),
    .RegDst(control_unit_1_regdst), .beq(control_unit_1_beq), .bne(control_unit_1_bne),
    .ALUOp(control_unit_1_aluop), .isHalf(control_unit_1_ishalf), .bltz(control_unit_1_bltz),
    .isCop(control_unit_1_iscop), .isCopread(control_unit_1_iscopread));
  // Probe on control_unit_1_jump
  // Probe on control_unit_1_beq
  // Probe on control_unit_1_bne
  // Probe on control_unit_1_iscop
  // Probe on control_unit_1_ishalf
  // Probe on control_unit_1_bltz
  // Probe on control_unit_1_iscopread

  // Notes on the sheet:
  //   contents of rom_1 (hex, n*v repeats v):
  //   20110001 8000c05 20110001 20120002 20130003 8000c09 20110001 20120002 20130003 8000c0d 20110001
  //   20120002 20130003 8000c11 20110001 20120002 20130003 c000cb8 20100001 20110001 118fc0 112020
  //   20020022 c 118882 12200001 8000c15 112020 20020022 c 20110001 118880 112020 20020022 c 12200001
  //   8000c1f 20110001 118fc0 112020 20020022 c 1188c3 112020 20020022 c 118903 112020 20020022 c 118903
  //   112020 20020022 c 118903 112020 20020022 c 118903 112020 20020022 c 118903 112020 20020022 c 118903
  //   112020 20020022 c 118903 112020 20020022 c 20100001 109fc0 139fc3 8021 2012000c 24160003 26100001
  //   3210000f 20080008 20090001 139900 2709825 132020 20020022 c 1094022 1500fff9 22100001 2018000f
  //   2188024 108700 20080008 20090001 139902 2709825 132021 20020022 c 1094022 1500fff9 108702 2c9b022
  //   12c00001 8000c50 4020 1084027 84400 3508ffff 82021 20020022 c 2010ffff 20110000 ae300000 22100001
  //   22310004 ae300000 22100001 22310004 ae300000 22100001 22310004 ae300000 22100001 22310004 ae300000
  //   22100001 22310004 ae300000 22100001 22310004 ae300000 22100001 22310004 ae300000 22100001 22310004
  //   ae300000 22100001 22310004 ae300000 22100001 22310004 ae300000 22100001 22310004 ae300000 22100001
  //   22310004 ae300000 22100001 22310004 ae300000 22100001 22310004 ae300000 22100001 22310004 ae300000
  //   22100001 22310004 22100001 8020 2011003c 8e130000 8e340000 274402a 11000002 ae330000 ae140000
  //   2231fffc 1611fff8 102020 20020022 c 22100004 2011003c 1611fff2 2002000a c 20100000 22100001 102020
  //   20020022 c 22100002 102020 20020022 c 22100003 102020 20020022 c 22100004 102020 20020022 c 22100005
  //   102020 20020022 c 22100006 102020 20020022 c 22100007 102020 20020022 c 22100008 102020 20020022
  //   20020022 c 3e00008
endmodule
